// Logisim project 实验2-校交1801-U201816030-车春池.circ as structural Verilog
module \四位二进制可逆计数器  (
  input  D,
  input  C,
  input  B,
  input  A,
  input  CPU,
  input  CPD,
  input  CLR,
  input  LD,
  output QD,
  output QC,
  output QB,
  output QA
);

  wire and_1_out, and_2_out, and_3_out, and_4_out, and_5_out, and_6_out, d_ff_1_qn, d_ff_2_qn, d_ff_3_qn,
       d_ff_4_qn, multiplexer_1_out, multiplexer_2_out, multiplexer_3_out, multiplexer_4_out,
       multiplexer_5_out, multiplexer_6_out, multiplexer_7_out, multiplexer_8_out, not_1_out, not_2_out,
       not_3_out, not_4_out, not_5_out, or_1_out, or_2_out, or_3_out, or_4_out, or_5_out, or_6_out, or_7_out,
       or_8_out;

  not not_1 (not_1_out, LD);
  or or_1 (or_1_out, CPU, CPD);
  and and_1 (and_1_out, CPD, d_ff_4_qn, d_ff_3_qn, d_ff_2_qn);
  and and_2 (and_2_out, CPU, QA, QB, QC);
  and and_3 (and_3_out, CPD, d_ff_4_qn, d_ff_3_qn);
  and and_4 (and_4_out, CPU, QA, QB);
  and and_5 (and_5_out, CPD, d_ff_4_qn);
  and and_6 (and_6_out, CPU, QA);
  or or_2 (or_2_out, and_1_out, and_2_out);
  or or_3 (or_3_out, and_3_out, and_4_out);
  or or_4 (or_4_out, and_5_out, and_6_out);
  Multiplexer multiplexer_1 (.in0(1'b0), .in1(B), .out(multiplexer_1_out), .sel(not_1_out));  // open: en
  D_Flip_Flop #(.trigger("falling")) d_ff_1 (
    .clk(or_2_out), .D(d_ff_1_qn), .Q(QD), .Qn(d_ff_1_qn), .preset(multiplexer_2_out), .en(1'b1),
    .reset(or_5_out));
  Multiplexer multiplexer_2 (.in0(1'b0), .in1(D), .out(multiplexer_2_out), .sel(not_1_out));  // open: en
  D_Flip_Flop #(.trigger("falling")) d_ff_2 (
    .clk(or_3_out), .D(d_ff_2_qn), .Q(QC), .Qn(d_ff_2_qn), .preset(multiplexer_3_out), .en(1'b1),
    .reset(or_6_out));
  Multiplexer multiplexer_3 (.in0(1'b0), .in1(C), .out(multiplexer_3_out), .sel(not_1_out));  // open: en
  D_Flip_Flop #(.trigger("falling")) d_ff_3 (
    .clk(or_4_out), .D(d_ff_3_qn), .Q(QB), .Qn(d_ff_3_qn), .preset(multiplexer_1_out), .en(1'b1),
    .reset(or_7_out));
  D_Flip_Flop #(.trigger("falling")) d_ff_4 (
    .clk(or_1_out), .D(d_ff_4_qn), .Q(QA), .Qn(d_ff_4_qn), .preset(multiplexer_4_out), .en(1'b1),
    .reset(or_8_out));
  Multiplexer multiplexer_4 (.in0(1'b0), .in1(A), .out(multiplexer_4_out), .sel(not_1_out));  // open: en
  Multiplexer multiplexer_5 (.in0(1'b0), .in1(not_2_out), .out(multiplexer_5_out), .sel(not_1_out));  // open: en
  not not_2 (not_2_out, D);
  Multiplexer multiplexer_6 (.in0(1'b0), .in1(not_3_out), .out(multiplexer_6_out), .sel(not_1_out));  // open: en
  not not_3 (not_3_out, B);
  Multiplexer multiplexer_7 (.in0(1'b0), .in1(not_4_out), .out(multiplexer_7_out), .sel(not_1_out));  // open: en
  not not_4 (not_4_out, A);
  or or_5 (or_5_out, CLR, multiplexer_5_out);
  or or_6 (or_6_out, CLR, multiplexer_8_out);
  Multiplexer multiplexer_8 (.in0(1'b0), .in1(not_5_out), .out(multiplexer_8_out), .sel(not_1_out));  // open: en
  not not_5 (not_5_out, C);
  or or_7 (or_7_out, CLR, multiplexer_6_out);
  or or_8 (or_8_out, CLR, multiplexer_7_out);
endmodule

module \四位二进制可逆计数器测试电路  (
  input  D,
  input  C,
  input  B,
  input  A,
  input  CPD,
  input  CPU,
  input  CLR,
  input  LD,
  output QD,
  output QC,
  output QB,
  output QA
);

  \四位二进制可逆计数器  \u_四位二进制可逆计数器_1  (
    .CPD(CPD), .D(D), .QD(QD), .C(C), .QC(QC), .B(B), .QB(QB), .A(A), .QA(QA), .CPU(CPU), .CLR(CLR), .LD(LD));
endmodule

module \二进制转8421码电路  (
  input  A0,
  input  A1,
  input  A2,
  input  A3,
  output S1,
  output S2,
  output S4,
  output S8,
  output S10,
  output S20,
  output S40,
  output S80
);

  wire and_1_out, or_1_out;

  or or_1 (or_1_out, A1, A2);
  and and_1 (and_1_out, or_1_out, A3);
  \先行进位并行加法器  \u_先行进位并行加法器_1  (
    .A0(A0), .A1(A1), .A2(A2), .A3(A3), .B0(1'b0), .B1(and_1_out), .B2(and_1_out), .B3(1'b0), .C0(1'b0),
    .S0(S1), .S1(S2), .S2(S4), .S3(S8), .C4(S10));

  assign S20 = 1'b0;
  assign S40 = 1'b0;
  assign S80 = 1'b0;
endmodule

module \二进制转8421码测试电路  (
  input  A0,
  input  A1,
  input  A2,
  input  A3,
  output S1,
  output S2,
  output S4,
  output S8,
  output S10,
  output S20,
  output S40,
  output S80
);

  \二进制转8421码电路  \u_二进制转8421码电路_1  (
    .A0(A0), .A1(A1), .A2(A2), .A3(A3), .S1(S1), .S2(S2), .S4(S4), .S8(S8), .S10(S10), .S20(S20), .S40(S40),
    .S80(S80));
endmodule

module \显示电路  (
  input  A0,
  input  A1,
  input  A2,
  input  A3,
  output al,
  output bl,
  output cl,
  output dl,
  output el,
  output fl,
  output gl,
  output ah,
  output bh,
  output ch,
  output dh,
  output eh,
  output fh,
  output gh
);

  wire \二进制转8421码电路_1_s1 , \二进制转8421码电路_1_s2 , \二进制转8421码电路_1_s4 , \二进制转8421码电路_1_s8 , \二进制转8421码电路_1_s10 ,
       \二进制转8421码电路_1_s20 , \二进制转8421码电路_1_s40 , \二进制转8421码电路_1_s80 ;

  \二进制转8421码电路  \u_二进制转8421码电路_1  (
    .A0(A0), .A1(A1), .A2(A2), .A3(A3), .S1(\二进制转8421码电路_1_s1 ), .S2(\二进制转8421码电路_1_s2 ),
    .S4(\二进制转8421码电路_1_s4 ), .S8(\二进制转8421码电路_1_s8 ), .S10(\二进制转8421码电路_1_s10 ), .S20(\二进制转8421码电路_1_s20 ),
    .S40(\二进制转8421码电路_1_s40 ), .S80(\二进制转8421码电路_1_s80 ));
  \七段译码器  \u_七段译码器_1  (
    .A3(\二进制转8421码电路_1_s8 ), .A2(\二进制转8421码电路_1_s4 ), .A1(\二进制转8421码电路_1_s2 ), .A0(\二进制转8421码电路_1_s1 ),
    .a(al), .b(bl), .c(cl), .d(dl), .e(el), .f(fl), .g(gl));
  \七段译码器  \u_七段译码器_2  (
    .A3(\二进制转8421码电路_1_s80 ), .A2(\二进制转8421码电路_1_s40 ), .A1(\二进制转8421码电路_1_s20 ), .A0(\二进制转8421码电路_1_s10 ),
    .a(ah), .b(bh), .c(ch), .d(dh), .e(eh), .f(fh), .g(gh));
endmodule

module \显示电路测试电路  (
  input  A0,
  input  A1,
  input  A2,
  input  A3
);

  wire \显示电路_1_ah , \显示电路_1_al , \显示电路_1_bh , \显示电路_1_bl , \显示电路_1_ch , \显示电路_1_cl , \显示电路_1_dh ,
       \显示电路_1_dl , \显示电路_1_eh , \显示电路_1_el , \显示电路_1_fh , \显示电路_1_fl , \显示电路_1_gh , \显示电路_1_gl ;

  \显示电路  \u_显示电路_1  (
    .A0(A0), .A1(A1), .A2(A2), .A3(A3), .al(\显示电路_1_al ), .bl(\显示电路_1_bl ), .cl(\显示电路_1_cl ),
    .dl(\显示电路_1_dl ), .el(\显示电路_1_el ), .fl(\显示电路_1_fl ), .gl(\显示电路_1_gl ), .ah(\显示电路_1_ah ),
    .bh(\显示电路_1_bh ), .ch(\显示电路_1_ch ), .dh(\显示电路_1_dh ), .eh(\显示电路_1_eh ), .fh(\显示电路_1_fh ), .gh(\显示电路_1_gh ));
  _7_Segment_Display u_7_segment_display_1 (
    .g(\显示电路_1_gh ), .f(\显示电路_1_fh ), .a(\显示电路_1_ah ), .b(\显示电路_1_bh ), .e(\显示电路_1_eh ), .d(\显示电路_1_dh ),
    .c(\显示电路_1_ch ));  // open: dp
  _7_Segment_Display u_7_segment_display_2 (
    .g(\显示电路_1_gl ), .f(\显示电路_1_fl ), .a(\显示电路_1_al ), .b(\显示电路_1_bl ), .e(\显示电路_1_el ), .d(\显示电路_1_dl ),
    .c(\显示电路_1_cl ));  // open: dp
endmodule

module \报警电路  (
  input  D,
  input  C,
  input  B,
  input  A,
  input  D_2,
  input  U,
  input  CLR,
  input  LD,
  output QD,
  output QC,
  output QB,
  output QA
);

  wire and_1_out, and_2_out, not_1_out, \报警信号_out , \无人信号_out , \满员信号_out ;

  and and_1 (and_1_out, \无人信号_out , D_2);
  and and_2 (and_2_out, not_1_out, U);
  \四位二进制可逆计数器  \u_四位二进制可逆计数器_1  (
    .CPD(and_1_out), .D(D), .QD(QD), .C(C), .QC(QC), .B(B), .QB(QB), .A(A), .QA(QA), .CPU(and_2_out),
    .CLR(CLR), .LD(LD));
  or \u_无人信号  (\无人信号_out , QA, QB, QC, QD);
  and \u_满员信号  (\满员信号_out , QA, QB, QC, QD);
  not not_1 (not_1_out, \满员信号_out );
  and \u_报警信号  (\报警信号_out , \满员信号_out , U);
  LED Alarm (.in(\报警信号_out ));
endmodule

module \小型实验室门禁系统  (
  input  D,
  input  U,
  input  CLR,
  output al,
  output bl,
  output cl,
  output dl,
  output el,
  output fl,
  output gl,
  output ah,
  output bh,
  output ch,
  output dh,
  output eh,
  output fh,
  output gh,
  output Z
);

  wire and_1_out, and_2_out, not_1_out, \二进制转8421码电路_1_s1 , \二进制转8421码电路_1_s2 , \二进制转8421码电路_1_s4 ,
       \二进制转8421码电路_1_s8 , \二进制转8421码电路_1_s10 , \二进制转8421码电路_1_s20 , \二进制转8421码电路_1_s40 ,
       \二进制转8421码电路_1_s80 , \四位二进制可逆计数器_1_qa , \四位二进制可逆计数器_1_qb , \四位二进制可逆计数器_1_qc , \四位二进制可逆计数器_1_qd ,
       \无人信号_out , \满员信号_out ;

  and and_1 (and_1_out, \无人信号_out , D);
  and and_2 (and_2_out, not_1_out, U);
  \四位二进制可逆计数器  \u_四位二进制可逆计数器_1  (
    .CPD(and_1_out), .D(1'b0), .QD(\四位二进制可逆计数器_1_qd ), .C(1'b0), .QC(\四位二进制可逆计数器_1_qc ), .B(1'b0),
    .QB(\四位二进制可逆计数器_1_qb ), .A(1'b0), .QA(\四位二进制可逆计数器_1_qa ), .CPU(and_2_out), .CLR(CLR), .LD(1'b1));
  or \u_无人信号  (\无人信号_out , \四位二进制可逆计数器_1_qa , \四位二进制可逆计数器_1_qb , \四位二进制可逆计数器_1_qc , \四位二进制可逆计数器_1_qd );
  not not_1 (not_1_out, \满员信号_out );
  and \u_满员信号  (\满员信号_out , \四位二进制可逆计数器_1_qa , \四位二进制可逆计数器_1_qb , \四位二进制可逆计数器_1_qc , \四位二进制可逆计数器_1_qd );
  and \u_报警信号  (Z, \满员信号_out , U);
  \二进制转8421码电路  \u_二进制转8421码电路_1  (
    .A0(\四位二进制可逆计数器_1_qa ), .A1(\四位二进制可逆计数器_1_qb ), .A2(\四位二进制可逆计数器_1_qc ), .A3(\四位二进制可逆计数器_1_qd ),
    .S1(\二进制转8421码电路_1_s1 ), .S2(\二进制转8421码电路_1_s2 ), .S4(\二进制转8421码电路_1_s4 ), .S8(\二进制转8421码电路_1_s8 ),
    .S10(\二进制转8421码电路_1_s10 ), .S20(\二进制转8421码电路_1_s20 ), .S40(\二进制转8421码电路_1_s40 ), .S80(\二进制转8421码电路_1_s80 ));
  \七段译码器  \u_七段译码器_1  (
    .A3(\二进制转8421码电路_1_s8 ), .A2(\二进制转8421码电路_1_s4 ), .A1(\二进制转8421码电路_1_s2 ), .A0(\二进制转8421码电路_1_s1 ),
    .a(al), .b(bl), .c(cl), .d(dl), .e(el), .f(fl), .g(gl));
  \七段译码器  \u_七段译码器_2  (
    .A3(\二进制转8421码电路_1_s80 ), .A2(\二进制转8421码电路_1_s40 ), .A1(\二进制转8421码电路_1_s20 ), .A0(\二进制转8421码电路_1_s10 ),
    .a(ah), .b(bh), .c(ch), .d(dh), .e(eh), .f(fh), .g(gh));
endmodule

module \小型门禁系统测试电路  (
  input  in_1,
  input  in_2,
  input  in_3
);

  wire \小型实验室门禁系统_1_ah , \小型实验室门禁系统_1_al , \小型实验室门禁系统_1_bh , \小型实验室门禁系统_1_bl , \小型实验室门禁系统_1_ch ,
       \小型实验室门禁系统_1_cl , \小型实验室门禁系统_1_dh , \小型实验室门禁系统_1_dl , \小型实验室门禁系统_1_eh , \小型实验室门禁系统_1_el ,
       \小型实验室门禁系统_1_fh , \小型实验室门禁系统_1_fl , \小型实验室门禁系统_1_gh , \小型实验室门禁系统_1_gl , \小型实验室门禁系统_1_z ;

  _7_Segment_Display u_7_segment_display_1 (
    .g(\小型实验室门禁系统_1_gh ), .f(\小型实验室门禁系统_1_fh ), .a(\小型实验室门禁系统_1_ah ), .b(\小型实验室门禁系统_1_bh ),
    .e(\小型实验室门禁系统_1_eh ), .d(\小型实验室门禁系统_1_dh ), .c(\小型实验室门禁系统_1_ch ));  // open: dp
  _7_Segment_Display u_7_segment_display_2 (
    .g(\小型实验室门禁系统_1_gl ), .f(\小型实验室门禁系统_1_fl ), .a(\小型实验室门禁系统_1_al ), .b(\小型实验室门禁系统_1_bl ),
    .e(\小型实验室门禁系统_1_el ), .d(\小型实验室门禁系统_1_dl ), .c(\小型实验室门禁系统_1_cl ));  // open: dp
  \小型实验室门禁系统  \u_小型实验室门禁系统_1  (
    .D(in_3), .U(in_1), .CLR(in_2), .al(\小型实验室门禁系统_1_al ), .bl(\小型实验室门禁系统_1_bl ), .cl(\小型实验室门禁系统_1_cl ),
    .dl(\小型实验室门禁系统_1_dl ), .el(\小型实验室门禁系统_1_el ), .fl(\小型实验室门禁系统_1_fl ), .gl(\小型实验室门禁系统_1_gl ),
    .ah(\小型实验室门禁系统_1_ah ), .bh(\小型实验室门禁系统_1_bh ), .ch(\小型实验室门禁系统_1_ch ), .dh(\小型实验室门禁系统_1_dh ),
    .eh(\小型实验室门禁系统_1_eh ), .fh(\小型实验室门禁系统_1_fh ), .gh(\小型实验室门禁系统_1_gh ), .Z(\小型实验室门禁系统_1_z ));
  LED led_1 (.in(\小型实验室门禁系统_1_z ));
endmodule

module Mux2_1 (
  input  D0,
  input  S,
  input  D1,
  output Y
);

  wire and_1_out, and_2_out, not_1_out;

  not not_1 (not_1_out, S);
  and and_1 (and_1_out, D0, not_1_out);
  and and_2 (and_2_out, S, D1);
  or or_1 (Y, and_1_out, and_2_out);
endmodule

module \七段译码器  (
  input  A3,
  input  A2,
  input  A1,
  input  A0,
  output a,
  output b,
  output c,
  output d,
  output e,
  output f,
  output g
);

  wire and_1_out, and_2_out, and_3_out, and_4_out, and_5_out, and_6_out, and_7_out, and_8_out, and_9_out,
       and_10_out, and_11_out, and_12_out, and_13_out, and_14_out, and_15_out, and_16_out, and_17_out,
       and_18_out, and_19_out, and_20_out, and_21_out, and_22_out, and_23_out, and_24_out, and_25_out,
       and_26_out, not_1_out, not_2_out, not_3_out, not_4_out, not_5_out, not_6_out, not_7_out, not_8_out,
       not_9_out, not_10_out, not_11_out, not_12_out, not_13_out, not_14_out, not_15_out, not_16_out,
       not_17_out, not_18_out, not_19_out, not_20_out, not_21_out, not_22_out, not_23_out, not_24_out,
       not_25_out, not_26_out, not_27_out, not_28_out, not_29_out, not_30_out, not_31_out, not_32_out,
       not_33_out, not_34_out, not_35_out, not_36_out, not_37_out;

  not not_1 (not_1_out, A3);
  not not_2 (not_2_out, A2);
  and and_1 (and_1_out, not_1_out, not_2_out, not_3_out);
  not not_3 (not_3_out, A0);
  not not_4 (not_4_out, A3);
  and and_2 (and_2_out, not_4_out, not_5_out, A1);
  not not_5 (not_5_out, A2);
  not not_6 (not_6_out, A3);
  and and_3 (and_3_out, not_6_out, A2, A0);
  and and_4 (and_4_out, A3, not_7_out, not_8_out);
  not not_7 (not_7_out, A2);
  not not_8 (not_8_out, A1);
  not not_9 (not_9_out, A1);
  and and_5 (and_5_out, A3, not_9_out, A0);
  not not_10 (not_10_out, A3);
  and and_6 (and_6_out, not_10_out, not_11_out);
  not not_11 (not_11_out, A2);
  not not_12 (not_12_out, A2);
  and and_7 (and_7_out, not_12_out, not_13_out);
  not not_13 (not_13_out, A1);
  not not_14 (not_14_out, A1);
  and and_8 (and_8_out, not_14_out, not_15_out);
  not not_15 (not_15_out, A0);
  not not_16 (not_16_out, A3);
  and and_9 (and_9_out, not_16_out, A1, A0);
  not not_17 (not_17_out, A2);
  and and_10 (and_10_out, not_17_out, not_18_out);
  not not_18 (not_18_out, A1);
  not not_19 (not_19_out, A2);
  and and_11 (and_11_out, not_19_out, A0);
  not not_20 (not_20_out, A3);
  and and_12 (and_12_out, not_20_out, A2);
  not not_21 (not_21_out, A2);
  and and_13 (and_13_out, not_21_out, not_22_out);
  not not_22 (not_22_out, A0);
  not not_23 (not_23_out, A2);
  and and_14 (and_14_out, not_23_out, A1);
  and and_15 (and_15_out, A1, not_24_out);
  not not_24 (not_24_out, A0);
  and and_16 (and_16_out, A2, not_25_out, A0);
  not not_25 (not_25_out, A1);
  not not_26 (not_26_out, A2);
  and and_17 (and_17_out, not_26_out, not_27_out);
  not not_27 (not_27_out, A0);
  and and_18 (and_18_out, A1, not_28_out);
  not not_28 (not_28_out, A0);
  not not_29 (not_29_out, A1);
  and and_19 (and_19_out, not_29_out, not_30_out);
  not not_30 (not_30_out, A0);
  and and_20 (and_20_out, A2, not_31_out);
  not not_31 (not_31_out, A1);
  and and_21 (and_21_out, A2, not_32_out);
  not not_32 (not_32_out, A0);
  and and_22 (and_22_out, A3, not_33_out);
  not not_33 (not_33_out, A1);
  not not_34 (not_34_out, A1);
  and and_23 (and_23_out, not_34_out, A2);
  and and_24 (and_24_out, A1, not_35_out);
  not not_35 (not_35_out, A2);
  and and_25 (and_25_out, A1, not_36_out);
  not not_36 (not_36_out, A0);
  and and_26 (and_26_out, A3, not_37_out);
  not not_37 (not_37_out, A1);
  or or_1 (a, and_1_out, and_2_out, and_3_out, and_4_out, and_5_out);
  or or_2 (b, and_6_out, and_7_out, and_8_out, and_9_out);
  or or_3 (c, and_10_out, and_11_out, and_12_out);
  or or_4 (d, and_13_out, and_14_out, and_15_out, and_16_out);
  or or_5 (e, and_17_out, and_18_out);
  or or_6 (f, and_19_out, and_20_out, and_21_out, and_22_out);
  or or_7 (g, and_23_out, and_24_out, and_25_out, and_26_out);
endmodule
