// Logisim project 实验3-校交1801-U201816030-车春池.circ as structural Verilog: 10 circuits, main circuit 四位乘法器
module \四位乘法器  (
  input  [3:0] a,
  input  [3:0] b,
  output [7:0] out_3
);

  wire [7:0] adder_1_out, adder_2_out, adder_3_out, adder_4_out, bit_extender_1_out, multiplexer_1_out,
       multiplexer_2_out, multiplexer_3_out, shifter_1_out, shifter_2_out, shifter_3_out;

  assign bit_extender_1_out = {{4{1'b0}}, b};  // Bit_Extender bit_extender_1
  Adder adder_1 (.a({8{1'b0}}), .b(bit_extender_1_out), .out(adder_1_out));  // open: cin, cout
  Shifter shifter_1 (.in(bit_extender_1_out), .\dist (3'b001), .out(shifter_1_out));
  Multiplexer #(.width(8), .enable("false")) multiplexer_1 (
    .in0({8{1'b0}}), .in1(adder_1_out), .out(multiplexer_1_out), .sel(a[0]));
  Adder adder_2 (.a(multiplexer_1_out), .b(shifter_1_out), .out(adder_2_out));  // open: cin, cout
  Shifter shifter_2 (.in(shifter_1_out), .\dist (3'b001), .out(shifter_2_out));
  Multiplexer #(.width(8), .enable("false")) multiplexer_2 (
    .in0(multiplexer_1_out), .in1(adder_2_out), .out(multiplexer_2_out), .sel(a[1]));
  Adder adder_3 (.a(multiplexer_2_out), .b(shifter_2_out), .out(adder_3_out));  // open: cin, cout
  Shifter shifter_3 (.in(shifter_2_out), .\dist (3'b001), .out(shifter_3_out));
  Multiplexer #(.width(8), .enable("false")) multiplexer_3 (
    .in0(multiplexer_2_out), .in1(adder_3_out), .out(multiplexer_3_out), .sel(a[2]));
  Adder adder_4 (.a(multiplexer_3_out), .b(shifter_3_out), .out(adder_4_out));  // open: cin, cout
  Multiplexer #(.width(8), .enable("false")) multiplexer_4 (
    .in0(multiplexer_3_out), .in1(adder_4_out), .out(out_3), .sel(a[3]));
endmodule

module \四位乘法器测试电路  (
  input  [3:0] in_1,
  input  [3:0] in_2,
  output [7:0] out_3
);

  \四位乘法器  \u_四位乘法器_1  (.a(in_1), .b(in_2), .out_3(out_3));
endmodule

module \_32X4乘法器  (
  input  [3:0] a,
  input  [31:0] b,
  output [31:0] out_low,
  output [31:0] out_high
);

  wire [31:0] adder_64_1_out_high, adder_64_1_out_low, adder_64_2_out_high, adder_64_2_out_low,
       adder_64_3_out_high, adder_64_3_out_low, adder_64_4_out_high, adder_64_4_out_low,
       extender32_64_1_out_high, extender32_64_1_out_low, left_64_1_out_high, left_64_1_out_low,
       left_64_2_out_high, left_64_2_out_low, left_64_3_out_high, left_64_3_out_low, mux2_1_64_1_out_high,
       mux2_1_64_1_out_low, mux2_1_64_2_out_high, mux2_1_64_2_out_low, mux2_1_64_3_out_high,
       mux2_1_64_3_out_low, not_1_out, not_2_out;

  assign not_1_out = ~{32{1'b1}};  // NOT_Gate not_1, 32 bits wide
  assign not_2_out = ~{32{1'b1}};  // NOT_Gate not_2, 32 bits wide
  Extender32_64 extender32_64_1 (.in(b), .out_low(extender32_64_1_out_low), .out_high(extender32_64_1_out_high));
  Adder_64 adder_64_1 (
    .a_low(not_1_out), .a_high(not_2_out), .b_low(extender32_64_1_out_low),
    .b_high(extender32_64_1_out_high), .out_low(adder_64_1_out_low), .out_high(adder_64_1_out_high));  // open: overflow
  Mux2_1_64 mux2_1_64_1 (
    .sel(a[0]), .a_low(not_1_out), .a_high(not_2_out), .b_low(adder_64_1_out_low),
    .b_high(adder_64_1_out_high), .out_low(mux2_1_64_1_out_low), .out_high(mux2_1_64_1_out_high));
  Left_64 left_64_1 (
    .in_low(extender32_64_1_out_low), .in_high(extender32_64_1_out_high), .out_low(left_64_1_out_low),
    .out_high(left_64_1_out_high));
  Adder_64 adder_64_2 (
    .a_low(mux2_1_64_1_out_low), .a_high(mux2_1_64_1_out_high), .b_low(left_64_1_out_low),
    .b_high(left_64_1_out_high), .out_low(adder_64_2_out_low), .out_high(adder_64_2_out_high));  // open: overflow
  Mux2_1_64 mux2_1_64_2 (
    .sel(a[1]), .a_low(mux2_1_64_1_out_low), .a_high(mux2_1_64_1_out_high), .b_low(adder_64_2_out_low),
    .b_high(adder_64_2_out_high), .out_low(mux2_1_64_2_out_low), .out_high(mux2_1_64_2_out_high));
  Left_64 left_64_2 (
    .in_low(left_64_1_out_low), .in_high(left_64_1_out_high), .out_low(left_64_2_out_low),
    .out_high(left_64_2_out_high));
  Adder_64 adder_64_3 (
    .a_low(mux2_1_64_2_out_low), .a_high(mux2_1_64_2_out_high), .b_low(left_64_2_out_low),
    .b_high(left_64_2_out_high), .out_low(adder_64_3_out_low), .out_high(adder_64_3_out_high));  // open: overflow
  Mux2_1_64 mux2_1_64_3 (
    .sel(a[2]), .a_low(mux2_1_64_2_out_low), .a_high(mux2_1_64_2_out_high), .b_low(adder_64_3_out_low),
    .b_high(adder_64_3_out_high), .out_low(mux2_1_64_3_out_low), .out_high(mux2_1_64_3_out_high));
  Left_64 left_64_3 (
    .in_low(left_64_2_out_low), .in_high(left_64_2_out_high), .out_low(left_64_3_out_low),
    .out_high(left_64_3_out_high));
  Adder_64 adder_64_4 (
    .a_low(mux2_1_64_3_out_low), .a_high(mux2_1_64_3_out_high), .b_low(left_64_3_out_low),
    .b_high(left_64_3_out_high), .out_low(adder_64_4_out_low), .out_high(adder_64_4_out_high));  // open: overflow
  Mux2_1_64 mux2_1_64_4 (
    .sel(a[3]), .a_low(mux2_1_64_3_out_low), .a_high(mux2_1_64_3_out_high), .b_low(adder_64_4_out_low),
    .b_high(adder_64_4_out_high), .out_low(out_low), .out_high(out_high));
  Left_64 left_64_4 (.in_low(left_64_3_out_low), .in_high(left_64_3_out_high));  // open: out_low, out_high
endmodule

module \_32X4乘法器测试电路  (
  input  [3:0] in_1,
  input  [31:0] in_2,
  output [31:0] out_3,
  output [31:0] out_4
);

  \_32X4乘法器  \u_32x4乘法器_1  (.a(in_1), .b(in_2), .out_low(out_3), .out_high(out_4));
endmodule

module \_32X32乘法器  (
  input  [31:0] a,
  input  [31:0] b,
  output [31:0] out_low,
  output [31:0] out_high
);

  wire [31:0] adder_64_1_out_high, adder_64_1_out_low, adder_64_2_out_high, adder_64_2_out_low,
       adder_64_3_out_high, adder_64_3_out_low, adder_64_4_out_high, adder_64_4_out_low, adder_64_5_out_high,
       adder_64_5_out_low, adder_64_6_out_high, adder_64_6_out_low, \n32x4乘法器_1_out_high ,
       \n32x4乘法器_1_out_low , \n32x4乘法器_2_out_low , \n32x4乘法器_3_out_low , \n32x4乘法器_4_out_low ,
       \n32x4乘法器_5_out_low , \n32x4乘法器_6_out_low , \n32x4乘法器_7_out_low , \n32x4乘法器_8_out_low , not_1_out;
  wire [31:4] \n32x4乘法器_8_out_high , not_2_out;
  wire [31:8] \n32x4乘法器_7_out_high , not_3_out;
  wire [31:12] \n32x4乘法器_6_out_high , not_4_out;
  wire [31:16] \n32x4乘法器_5_out_high , not_5_out;
  wire [31:20] \n32x4乘法器_4_out_high , not_6_out;
  wire [31:24] \n32x4乘法器_3_out_high , not_7_out;
  wire [31:28] \n32x4乘法器_2_out_high ;

  \_32X4乘法器  \u_32x4乘法器_1  (.a(a[3:0]), .b(b), .out_low(\n32x4乘法器_1_out_low ), .out_high(\n32x4乘法器_1_out_high ));
  assign not_1_out[3:0] = ~4'b1111;  // NOT_Gate not_1, 4 bits wide
  \_32X4乘法器  \u_32x4乘法器_2  (
    .a(a[7:4]), .b(b), .out_low({\n32x4乘法器_2_out_low [3:0], not_1_out[31:4]}),
    .out_high({\n32x4乘法器_2_out_high , \n32x4乘法器_2_out_low [31:4]}));
  assign not_2_out[7:4] = ~4'b1111;  // NOT_Gate not_2, 4 bits wide
  \_32X4乘法器  \u_32x4乘法器_3  (
    .a(a[11:8]), .b(b), .out_low({\n32x4乘法器_3_out_low [7:0], not_2_out[31:8]}),
    .out_high({\n32x4乘法器_3_out_high , \n32x4乘法器_3_out_low [31:8]}));
  assign not_3_out[11:8] = ~4'b1111;  // NOT_Gate not_3, 4 bits wide
  \_32X4乘法器  \u_32x4乘法器_4  (
    .a(a[15:12]), .b(b), .out_low({\n32x4乘法器_4_out_low [11:0], not_3_out[31:12]}),
    .out_high({\n32x4乘法器_4_out_high , \n32x4乘法器_4_out_low [31:12]}));
  assign not_4_out[15:12] = ~4'b1111;  // NOT_Gate not_4, 4 bits wide
  \_32X4乘法器  \u_32x4乘法器_5  (
    .a(a[19:16]), .b(b), .out_low({\n32x4乘法器_5_out_low [15:0], not_4_out[31:16]}),
    .out_high({\n32x4乘法器_5_out_high , \n32x4乘法器_5_out_low [31:16]}));
  assign not_5_out[19:16] = ~4'b1111;  // NOT_Gate not_5, 4 bits wide
  \_32X4乘法器  \u_32x4乘法器_6  (
    .a(a[23:20]), .b(b), .out_low({\n32x4乘法器_6_out_low [19:0], not_5_out[31:20]}),
    .out_high({\n32x4乘法器_6_out_high , \n32x4乘法器_6_out_low [31:20]}));
  assign not_6_out[23:20] = ~4'b1111;  // NOT_Gate not_6, 4 bits wide
  \_32X4乘法器  \u_32x4乘法器_7  (
    .a(a[27:24]), .b(b), .out_low({\n32x4乘法器_7_out_low [23:0], not_6_out[31:24]}),
    .out_high({\n32x4乘法器_7_out_high , \n32x4乘法器_7_out_low [31:24]}));
  assign not_7_out[27:24] = ~4'b1111;  // NOT_Gate not_7, 4 bits wide
  \_32X4乘法器  \u_32x4乘法器_8  (
    .a(a[31:28]), .b(b), .out_low({\n32x4乘法器_8_out_low [27:0], not_7_out[31:28]}),
    .out_high({\n32x4乘法器_8_out_high , \n32x4乘法器_8_out_low [31:28]}));
  Adder_64 adder_64_1 (
    .a_low(\n32x4乘法器_1_out_low ), .a_high(\n32x4乘法器_1_out_high ), .b_low(not_1_out),
    .b_high(\n32x4乘法器_2_out_low ), .out_low(adder_64_1_out_low), .out_high(adder_64_1_out_high));  // open: overflow
  Adder_64 adder_64_2 (
    .a_low({not_2_out, not_2_out[7:4]}), .a_high(\n32x4乘法器_3_out_low ),
    .b_low({not_3_out, not_3_out[11:8], not_3_out[11:8]}), .b_high(\n32x4乘法器_4_out_low ),
    .out_low(adder_64_2_out_low), .out_high(adder_64_2_out_high));  // open: overflow
  Adder_64 adder_64_3 (
    .a_low({not_4_out, not_4_out[15:12], not_4_out[15:12], not_4_out[15:12]}), .a_high(\n32x4乘法器_5_out_low ),
    .b_low({not_5_out, not_5_out[19:16], not_5_out[19:16], not_5_out[19:16], not_5_out[19:16]}),
    .b_high(\n32x4乘法器_6_out_low ), .out_low(adder_64_3_out_low), .out_high(adder_64_3_out_high));  // open: overflow
  Adder_64 adder_64_4 (
    .a_low({not_6_out, not_6_out[23:20], not_6_out[23:20], not_6_out[23:20], not_6_out[23:20], not_6_out[23:20]}),
    .a_high(\n32x4乘法器_7_out_low ),
    .b_low({not_7_out, not_7_out[27:24], not_7_out[27:24], not_7_out[27:24], not_7_out[27:24], not_7_out[27:24], not_7_out[27:24]}),
    .b_high(\n32x4乘法器_8_out_low ), .out_low(adder_64_4_out_low), .out_high(adder_64_4_out_high));  // open: overflow
  Adder_64 adder_64_5 (
    .a_low(adder_64_1_out_low), .a_high(adder_64_1_out_high), .b_low(adder_64_2_out_low),
    .b_high(adder_64_2_out_high), .out_low(adder_64_5_out_low), .out_high(adder_64_5_out_high));  // open: overflow
  Adder_64 adder_64_6 (
    .a_low(adder_64_3_out_low), .a_high(adder_64_3_out_high), .b_low(adder_64_4_out_low),
    .b_high(adder_64_4_out_high), .out_low(adder_64_6_out_low), .out_high(adder_64_6_out_high));  // open: overflow
  Adder_64 adder_64_7 (
    .a_low(adder_64_5_out_low), .a_high(adder_64_5_out_high), .b_low(adder_64_6_out_low),
    .b_high(adder_64_6_out_high), .out_low(out_low), .out_high(out_high));  // open: overflow
endmodule

module \_32X32乘法器测试电路  (
  input  [31:0] in_1,
  input  [31:0] in_2,
  output [31:0] out_3,
  output [31:0] out_4
);

  \_32X32乘法器  \u_32x32乘法器_1  (.a(in_1), .b(in_2), .out_low(out_3), .out_high(out_4));
endmodule

module Adder_64 (
  input  [31:0] a_low,
  input  [31:0] a_high,
  input  [31:0] b_low,
  input  [31:0] b_high,
  output [31:0] out_low,
  output [31:0] out_high,
  output overflow
);

  wire adder_1_cout;

  Adder #(.width(32)) adder_1 (.a(a_low), .b(b_low), .out(out_low), .cout(adder_1_cout));  // open: cin
  Adder #(.width(32)) adder_2 (.a(a_high), .b(b_high), .out(out_high), .cin(adder_1_cout), .cout(overflow));
endmodule

module Mux2_1_64 (
  input  sel,
  input  [31:0] a_low,
  input  [31:0] a_high,
  input  [31:0] b_low,
  input  [31:0] b_high,
  output [31:0] out_low,
  output [31:0] out_high
);

  Multiplexer #(.width(32)) multiplexer_1 (.in0(a_low), .in1(b_low), .out(out_low), .sel(sel));  // open: en
  Multiplexer #(.width(32)) multiplexer_2 (.in0(a_high), .in1(b_high), .out(out_high), .sel(sel));  // open: en
endmodule

module Left_64 (
  input  [31:0] in_low,
  input  [31:0] in_high,
  output [31:0] out_low,
  output [31:0] out_high
);

  not not_1 (out_low[0], 1'b1);

  assign out_high = {in_high[30:0], in_low[31]};
  assign out_low[31:1] = in_low[30:0];
endmodule

module Extender32_64 (
  input  [31:0] in,
  output [31:0] out_low,
  output [31:0] out_high
);

  assign out_high = ~{32{1'b1}};  // NOT_Gate not_1, 32 bits wide

  assign out_low = in;
endmodule
