// Logisim project 实验4-校交1801-U201816030-车春池.circ as structural Verilog: 6 circuits, main circuit 四位除法器测试电路
module \四位除法器测试电路  (
  input  [3:0] in_1,
  input  [3:0] in_2,
  output [3:0] out_3,
  output [3:0] out_4
);

  \四位除法器  \u_四位除法器_1  (.d(in_1), .n2(in_2), .rem(out_3), .quot(out_4));
endmodule

module \_32位除法器  (
  input  [31:0] n,
  input  [31:0] d,
  output [31:0] quot,
  output [31:0] rem
);

  wire [31:0] div1_1_nextquot, div1_1_nextrem, div1_3_nextquot, div1_3_nextrem, div1_4_nextquot,
       div1_4_nextrem, div1_5_nextquot, div1_5_nextrem, div1_6_nextquot, div1_6_nextrem, div1_7_nextquot,
       div1_7_nextrem, div1_8_nextquot, div1_8_nextrem, div1_9_nextquot, div1_9_nextrem, div1_10_nextquot,
       div1_10_nextrem, div1_11_nextquot, div1_11_nextrem, div1_12_nextquot, div1_12_nextrem,
       div1_13_nextquot, div1_13_nextrem, div1_14_nextquot, div1_14_nextrem, div1_15_nextquot,
       div1_15_nextrem, div1_16_nextquot, div1_16_nextrem, div1_17_nextquot, div1_17_nextrem,
       div1_18_nextquot, div1_18_nextrem, div1_19_nextquot, div1_19_nextrem, div1_20_nextquot,
       div1_20_nextrem, div1_21_nextquot, div1_21_nextrem, div1_22_nextquot, div1_22_nextrem,
       div1_23_nextquot, div1_23_nextrem, div1_24_nextquot, div1_24_nextrem, div1_25_nextquot,
       div1_25_nextrem, div1_26_nextquot, div1_26_nextrem, div1_27_nextquot, div1_27_nextrem,
       div1_28_nextquot, div1_28_nextrem, div1_29_nextquot, div1_29_nextrem, div1_30_nextquot,
       div1_30_nextrem, div1_31_nextquot, div1_31_nextrem, div1_32_nextquot, div1_32_nextrem;

  Div1 div1_1 (
    .d(d), .CurRem(div1_5_nextrem), .CurQuot(div1_5_nextquot), .NextRem(div1_1_nextrem),
    .NextQuot(div1_1_nextquot));
  Div1 div1_2 (.d(d), .CurRem(div1_6_nextrem), .CurQuot(div1_6_nextquot), .NextRem(rem), .NextQuot(quot));
  Div1 div1_3 (.d(d), .CurRem({32{1'b0}}), .CurQuot(n), .NextRem(div1_3_nextrem), .NextQuot(div1_3_nextquot));
  Div1 div1_4 (
    .d(d), .CurRem(div1_1_nextrem), .CurQuot(div1_1_nextquot), .NextRem(div1_4_nextrem),
    .NextQuot(div1_4_nextquot));
  Div1 div1_5 (
    .d(d), .CurRem(div1_9_nextrem), .CurQuot(div1_9_nextquot), .NextRem(div1_5_nextrem),
    .NextQuot(div1_5_nextquot));
  Div1 div1_6 (
    .d(d), .CurRem(div1_10_nextrem), .CurQuot(div1_10_nextquot), .NextRem(div1_6_nextrem),
    .NextQuot(div1_6_nextquot));
  Div1 div1_7 (
    .d(d), .CurRem(div1_3_nextrem), .CurQuot(div1_3_nextquot), .NextRem(div1_7_nextrem),
    .NextQuot(div1_7_nextquot));
  Div1 div1_8 (
    .d(d), .CurRem(div1_4_nextrem), .CurQuot(div1_4_nextquot), .NextRem(div1_8_nextrem),
    .NextQuot(div1_8_nextquot));
  Div1 div1_9 (
    .d(d), .CurRem(div1_12_nextrem), .CurQuot(div1_12_nextquot), .NextRem(div1_9_nextrem),
    .NextQuot(div1_9_nextquot));
  Div1 div1_10 (
    .d(d), .CurRem(div1_14_nextrem), .CurQuot(div1_14_nextquot), .NextRem(div1_10_nextrem),
    .NextQuot(div1_10_nextquot));
  Div1 div1_11 (
    .d(d), .CurRem(div1_7_nextrem), .CurQuot(div1_7_nextquot), .NextRem(div1_11_nextrem),
    .NextQuot(div1_11_nextquot));
  Div1 div1_12 (
    .d(d), .CurRem(div1_17_nextrem), .CurQuot(div1_17_nextquot), .NextRem(div1_12_nextrem),
    .NextQuot(div1_12_nextquot));
  Div1 div1_13 (
    .d(d), .CurRem(div1_8_nextrem), .CurQuot(div1_8_nextquot), .NextRem(div1_13_nextrem),
    .NextQuot(div1_13_nextquot));
  Div1 div1_14 (
    .d(d), .CurRem(div1_18_nextrem), .CurQuot(div1_18_nextquot), .NextRem(div1_14_nextrem),
    .NextQuot(div1_14_nextquot));
  Div1 div1_15 (
    .d(d), .CurRem(div1_11_nextrem), .CurQuot(div1_11_nextquot), .NextRem(div1_15_nextrem),
    .NextQuot(div1_15_nextquot));
  Div1 div1_16 (
    .d(d), .CurRem(div1_13_nextrem), .CurQuot(div1_13_nextquot), .NextRem(div1_16_nextrem),
    .NextQuot(div1_16_nextquot));
  Div1 div1_17 (
    .d(d), .CurRem(div1_21_nextrem), .CurQuot(div1_21_nextquot), .NextRem(div1_17_nextrem),
    .NextQuot(div1_17_nextquot));
  Div1 div1_18 (
    .d(d), .CurRem(div1_22_nextrem), .CurQuot(div1_22_nextquot), .NextRem(div1_18_nextrem),
    .NextQuot(div1_18_nextquot));
  Div1 div1_19 (
    .d(d), .CurRem(div1_15_nextrem), .CurQuot(div1_15_nextquot), .NextRem(div1_19_nextrem),
    .NextQuot(div1_19_nextquot));
  Div1 div1_20 (
    .d(d), .CurRem(div1_16_nextrem), .CurQuot(div1_16_nextquot), .NextRem(div1_20_nextrem),
    .NextQuot(div1_20_nextquot));
  Div1 div1_21 (
    .d(d), .CurRem(div1_25_nextrem), .CurQuot(div1_25_nextquot), .NextRem(div1_21_nextrem),
    .NextQuot(div1_21_nextquot));
  Div1 div1_22 (
    .d(d), .CurRem(div1_26_nextrem), .CurQuot(div1_26_nextquot), .NextRem(div1_22_nextrem),
    .NextQuot(div1_22_nextquot));
  Div1 div1_23 (
    .d(d), .CurRem(div1_19_nextrem), .CurQuot(div1_19_nextquot), .NextRem(div1_23_nextrem),
    .NextQuot(div1_23_nextquot));
  Div1 div1_24 (
    .d(d), .CurRem(div1_20_nextrem), .CurQuot(div1_20_nextquot), .NextRem(div1_24_nextrem),
    .NextQuot(div1_24_nextquot));
  Div1 div1_25 (
    .d(d), .CurRem(div1_28_nextrem), .CurQuot(div1_28_nextquot), .NextRem(div1_25_nextrem),
    .NextQuot(div1_25_nextquot));
  Div1 div1_26 (
    .d(d), .CurRem(div1_30_nextrem), .CurQuot(div1_30_nextquot), .NextRem(div1_26_nextrem),
    .NextQuot(div1_26_nextquot));
  Div1 div1_27 (
    .d(d), .CurRem(div1_23_nextrem), .CurQuot(div1_23_nextquot), .NextRem(div1_27_nextrem),
    .NextQuot(div1_27_nextquot));
  Div1 div1_28 (
    .d(d), .CurRem(div1_31_nextrem), .CurQuot(div1_31_nextquot), .NextRem(div1_28_nextrem),
    .NextQuot(div1_28_nextquot));
  Div1 div1_29 (
    .d(d), .CurRem(div1_24_nextrem), .CurQuot(div1_24_nextquot), .NextRem(div1_29_nextrem),
    .NextQuot(div1_29_nextquot));
  Div1 div1_30 (
    .d(d), .CurRem(div1_32_nextrem), .CurQuot(div1_32_nextquot), .NextRem(div1_30_nextrem),
    .NextQuot(div1_30_nextquot));
  Div1 div1_31 (
    .d(d), .CurRem(div1_27_nextrem), .CurQuot(div1_27_nextquot), .NextRem(div1_31_nextrem),
    .NextQuot(div1_31_nextquot));
  Div1 div1_32 (
    .d(d), .CurRem(div1_29_nextrem), .CurQuot(div1_29_nextquot), .NextRem(div1_32_nextrem),
    .NextQuot(div1_32_nextquot));
endmodule

module \_32位除法器测试电路  (
  input  [31:0] in_1,
  input  [31:0] in_2,
  output [31:0] out_3,
  output [31:0] out_4
);

  \_32位除法器  \u_32位除法器_1  (.n(in_1), .d(in_2), .quot(out_3), .rem(out_4));
endmodule

module Set_1 (
  input  [3:0] in,
  output [3:0] out
);


  assign out = {in[3:1], 1'b1};
endmodule

module Div1 (
  input  [31:0] CurQuot,
  input  [31:0] CurRem,
  input  [31:0] d,
  output [31:0] NextQuot,
  output [31:0] NextRem
);

  wire comparator_1_gt;
  wire [31:0] or_1_out, or_2_out, shifter_1_out, shifter_2_out, shifter_3_out, subtractor_1_out;

  Shifter #(.width(32)) shifter_1 (.in(CurRem), .\dist (5'b00001), .out(shifter_1_out));
  assign or_1_out = shifter_1_out | shifter_2_out;  // OR_Gate or_1, 32 bits wide
  Shifter #(.width(32), .shift("lr")) shifter_2 (.in(CurQuot), .\dist ({5{1'b1}}), .out(shifter_2_out));
  Shifter #(.width(32)) shifter_3 (.in(CurQuot), .\dist (5'b00001), .out(shifter_3_out));
  Comparator #(.width(32), .mode("unsigned")) comparator_1 (.a(d), .b(or_1_out), .gt(comparator_1_gt));  // open: eq, lt
  Subtractor #(.width(32)) subtractor_1 (.a(or_1_out), .b(d), .out(subtractor_1_out));  // open: bin, bout
  assign or_2_out = 32'h1 | shifter_3_out;  // OR_Gate or_2, 32 bits wide
  Multiplexer #(.width(32)) multiplexer_1 (
    .in0(subtractor_1_out), .in1(or_1_out), .out(NextRem), .sel(comparator_1_gt));  // open: en
  Multiplexer #(.width(32)) multiplexer_2 (
    .in0(or_2_out), .in1(shifter_3_out), .out(NextQuot), .sel(comparator_1_gt));  // open: en
endmodule

module \四位除法器  (
  input  [3:0] d,
  input  [3:0] n2,
  output [3:0] rem,
  output [3:0] quot
);

  wire comparator_1_gt, comparator_2_gt, comparator_3_gt, comparator_4_gt;
  wire [3:0] multiplexer_1_out, multiplexer_2_out, multiplexer_5_out, multiplexer_6_out, multiplexer_7_out,
       multiplexer_8_out, or_1_out, or_2_out, or_3_out, or_4_out, or_5_out, or_6_out, or_7_out, or_8_out,
       shifter_1_out, shifter_2_out, shifter_3_out, shifter_4_out, shifter_5_out, shifter_6_out,
       shifter_7_out, shifter_8_out, shifter_9_out, shifter_10_out, shifter_11_out, shifter_12_out,
       subtractor_1_out, subtractor_2_out, subtractor_3_out, subtractor_4_out;

  Shifter #(.width(4)) shifter_1 (.in(4'b0000), .\dist (2'b01), .out(shifter_1_out));
  Shifter #(.width(4), .shift("lr")) shifter_2 (.in(n2), .\dist (2'b11), .out(shifter_2_out));
  Shifter #(.width(4)) shifter_3 (.in(n2), .\dist (2'b01), .out(shifter_3_out));
  assign or_1_out = shifter_1_out | shifter_2_out;  // OR_Gate or_1, 4 bits wide
  Comparator #(.width(4), .mode("unsigned")) comparator_1 (.a(d), .b(or_1_out), .gt(comparator_1_gt));  // open: eq, lt
  Subtractor #(.width(4)) subtractor_1 (.a(or_1_out), .b(d), .out(subtractor_1_out));  // open: bin, bout
  assign or_2_out = 4'b0001 | shifter_3_out;  // OR_Gate or_2, 4 bits wide
  Multiplexer #(.width(4)) multiplexer_1 (
    .in0(subtractor_1_out), .in1(or_1_out), .out(multiplexer_1_out), .sel(comparator_1_gt));  // open: en
  Multiplexer #(.width(4)) multiplexer_2 (
    .in0(or_2_out), .in1(shifter_3_out), .out(multiplexer_2_out), .sel(comparator_1_gt));  // open: en
  Shifter #(.width(4)) shifter_4 (.in(multiplexer_7_out), .\dist (2'b01), .out(shifter_4_out));
  Shifter #(.width(4), .shift("lr")) shifter_5 (.in(multiplexer_8_out), .\dist (2'b11), .out(shifter_5_out));
  Shifter #(.width(4)) shifter_6 (.in(multiplexer_8_out), .\dist (2'b01), .out(shifter_6_out));
  Shifter #(.width(4)) shifter_7 (.in(multiplexer_1_out), .\dist (2'b01), .out(shifter_7_out));
  Shifter #(.width(4), .shift("lr")) shifter_8 (.in(multiplexer_2_out), .\dist (2'b11), .out(shifter_8_out));
  Shifter #(.width(4)) shifter_9 (.in(multiplexer_2_out), .\dist (2'b01), .out(shifter_9_out));
  assign or_3_out = shifter_4_out | shifter_5_out;  // OR_Gate or_3, 4 bits wide
  Comparator #(.width(4), .mode("unsigned")) comparator_2 (.a(d), .b(or_3_out), .gt(comparator_2_gt));  // open: eq, lt
  Subtractor #(.width(4)) subtractor_2 (.a(or_3_out), .b(d), .out(subtractor_2_out));  // open: bin, bout
  assign or_4_out = 4'b0001 | shifter_6_out;  // OR_Gate or_4, 4 bits wide
  assign or_5_out = shifter_7_out | shifter_8_out;  // OR_Gate or_5, 4 bits wide
  Multiplexer #(.width(4)) multiplexer_3 (
    .in0(subtractor_2_out), .in1(or_3_out), .out(rem), .sel(comparator_2_gt));  // open: en
  Multiplexer #(.width(4)) multiplexer_4 (
    .in0(or_4_out), .in1(shifter_6_out), .out(quot), .sel(comparator_2_gt));  // open: en
  Comparator #(.width(4), .mode("unsigned")) comparator_3 (.a(d), .b(or_5_out), .gt(comparator_3_gt));  // open: eq, lt
  Subtractor #(.width(4)) subtractor_3 (.a(or_5_out), .b(d), .out(subtractor_3_out));  // open: bin, bout
  assign or_6_out = 4'b0001 | shifter_9_out;  // OR_Gate or_6, 4 bits wide
  Multiplexer #(.width(4)) multiplexer_5 (
    .in0(subtractor_3_out), .in1(or_5_out), .out(multiplexer_5_out), .sel(comparator_3_gt));  // open: en
  Multiplexer #(.width(4)) multiplexer_6 (
    .in0(or_6_out), .in1(shifter_9_out), .out(multiplexer_6_out), .sel(comparator_3_gt));  // open: en
  Shifter #(.width(4)) shifter_10 (.in(multiplexer_5_out), .\dist (2'b01), .out(shifter_10_out));
  Shifter #(.width(4), .shift("lr")) shifter_11 (.in(multiplexer_6_out), .\dist (2'b11), .out(shifter_11_out));
  Shifter #(.width(4)) shifter_12 (.in(multiplexer_6_out), .\dist (2'b01), .out(shifter_12_out));
  assign or_7_out = shifter_10_out | shifter_11_out;  // OR_Gate or_7, 4 bits wide
  Comparator #(.width(4), .mode("unsigned")) comparator_4 (.a(d), .b(or_7_out), .gt(comparator_4_gt));  // open: eq, lt
  Subtractor #(.width(4)) subtractor_4 (.a(or_7_out), .b(d), .out(subtractor_4_out));  // open: bin, bout
  assign or_8_out = 4'b0001 | shifter_12_out;  // OR_Gate or_8, 4 bits wide
  Multiplexer #(.width(4)) multiplexer_7 (
    .in0(subtractor_4_out), .in1(or_7_out), .out(multiplexer_7_out), .sel(comparator_4_gt));  // open: en
  Multiplexer #(.width(4)) multiplexer_8 (
    .in0(or_8_out), .in1(shifter_12_out), .out(multiplexer_8_out), .sel(comparator_4_gt));  // open: en
endmodule
