// Logisim project 实验1-校交1801-U201816030-车春池.circ as structural Verilog: 6 circuits, main circuit 一位二进制半加器
module \一位二进制半加器  (
  input  A,
  input  B,
  output C,
  output S
);

  and and_1 (C, B, A);
  xor xor_1 (S, B, A);
endmodule

module \一位二进制全加器  (
  input  A,
  input  B,
  input  Ci,
  output S,
  output C
);

  wire and_1_out, and_2_out, xor_1_out;

  and and_1 (and_1_out, A, B);
  xor xor_1 (xor_1_out, A, B);
  xor xor_2 (S, xor_1_out, Ci);
  and and_2 (and_2_out, xor_1_out, Ci);
  or or_1 (C, and_2_out, and_1_out);
endmodule

module \串行进位并行加法器  (
  input  C0,
  input  A0,
  input  B0,
  input  A1,
  input  B1,
  input  A2,
  input  B2,
  input  A3,
  input  B3,
  output S0,
  output S1,
  output S2,
  output S3,
  output C4
);

  wire \一位二进制全加器_1_c , \一位二进制全加器_2_c , \一位二进制全加器_3_c ;

  \一位二进制全加器  \u_一位二进制全加器_1  (.A(A0), .B(B0), .Ci(C0), .S(S0), .C(\一位二进制全加器_1_c ));
  \一位二进制全加器  \u_一位二进制全加器_2  (.A(A1), .B(B1), .Ci(\一位二进制全加器_1_c ), .S(S1), .C(\一位二进制全加器_2_c ));
  \一位二进制全加器  \u_一位二进制全加器_3  (.A(A2), .B(B2), .Ci(\一位二进制全加器_2_c ), .S(S2), .C(\一位二进制全加器_3_c ));
  \一位二进制全加器  \u_一位二进制全加器_4  (.A(A3), .B(B3), .Ci(\一位二进制全加器_3_c ), .S(S3), .C(C4));
endmodule

module \先行进位并行加法器  (
  input  A0,
  input  A1,
  input  A2,
  input  A3,
  input  B0,
  input  B1,
  input  B2,
  input  B3,
  input  C0,
  output S0,
  output S1,
  output S2,
  output S3,
  output C4
);

  wire and_1_out, and_2_out, and_3_out, and_4_out, and_5_out, and_6_out, and_7_out, and_8_out, and_9_out,
       and_10_out, and_11_out, and_12_out, and_13_out, and_14_out, or_1_out, or_2_out, or_3_out, xor_1_out,
       xor_2_out, xor_3_out, xor_4_out, xor_5_out, xor_6_out, xor_7_out, xor_8_out, xor_9_out, xor_10_out,
       xor_11_out, xor_12_out, xor_13_out, xor_14_out, xor_15_out, xor_16_out, xor_17_out, xor_18_out,
       xor_19_out, xor_20_out;

  xor odd_parity_1 (S0, A0, B0, C0);
  xor xor_1 (xor_1_out, A0, B0);
  xor xor_2 (xor_2_out, A1, B1);
  xor xor_3 (xor_3_out, A0, B0);
  xor xor_4 (xor_4_out, A1, B1);
  xor xor_5 (xor_5_out, A2, B2);
  xor xor_6 (xor_6_out, A1, B1);
  xor xor_7 (xor_7_out, A0, B0);
  xor xor_8 (xor_8_out, A2, B2);
  xor xor_9 (xor_9_out, A1, B1);
  xor xor_10 (xor_10_out, A2, B2);
  xor xor_11 (xor_11_out, A3, B3);
  xor xor_12 (xor_12_out, A2, B2);
  xor xor_13 (xor_13_out, A1, B1);
  xor xor_14 (xor_14_out, A0, B0);
  xor xor_15 (xor_15_out, A3, B3);
  xor xor_16 (xor_16_out, A2, B2);
  xor xor_17 (xor_17_out, A1, B1);
  xor xor_18 (xor_18_out, A3, B3);
  xor xor_19 (xor_19_out, A2, B2);
  xor xor_20 (xor_20_out, A3, B3);
  and and_1 (and_1_out, xor_1_out, C0);
  and and_2 (and_2_out, A0, B0);
  and and_3 (and_3_out, xor_2_out, xor_3_out, C0);
  and and_4 (and_4_out, A0, B0, xor_4_out);
  and and_5 (and_5_out, A1, B1);
  and and_6 (and_6_out, xor_5_out, xor_6_out, xor_7_out, C0);
  and and_7 (and_7_out, xor_8_out, xor_9_out, A0, B0);
  and and_8 (and_8_out, A1, B1, xor_10_out);
  and and_9 (and_9_out, A2, B2);
  and and_10 (and_10_out, xor_11_out, xor_12_out, xor_13_out, xor_14_out, C0);
  and and_11 (and_11_out, xor_15_out, xor_16_out, xor_17_out, A0, B0);
  and and_12 (and_12_out, xor_18_out, xor_19_out, A1, B1);
  and and_13 (and_13_out, A2, B2, xor_20_out);
  and and_14 (and_14_out, A3, B3);
  or or_1 (or_1_out, and_1_out, and_2_out);
  or or_2 (or_2_out, and_3_out, and_4_out, and_5_out);
  or or_3 (or_3_out, and_6_out, and_7_out, and_8_out, and_9_out);
  or or_4 (C4, and_10_out, and_11_out, and_12_out, and_13_out, and_14_out);
  xor odd_parity_2 (S1, A1, B1, or_1_out);
  xor odd_parity_3 (S2, A2, B2, or_2_out);
  xor odd_parity_4 (S3, A3, B3, or_3_out);
endmodule

module \先行进位并行加法器测试电路  (
  input  A0,
  input  A1,
  input  A2,
  input  A3,
  input  B0,
  input  B1,
  input  B2,
  input  B3,
  input  C0,
  output S0,
  output S1,
  output S2,
  output S3,
  output C4
);

  \先行进位并行加法器  \u_先行进位并行加法器_1  (
    .A0(A0), .A1(A1), .A2(A2), .A3(A3), .B0(B0), .B1(B1), .B2(B2), .B3(B3), .C0(C0), .S0(S0), .S1(S1),
    .S2(S2), .S3(S3), .C4(C4));
endmodule

module test (
  input  A0,
  input  A1,
  input  A2,
  input  A3,
  input  B0,
  input  B1,
  input  B2,
  input  B3,
  input  C0,
  output S0,
  output S1,
  output S2,
  output S3,
  output C4
);

  wire and_1_out, and_2_out, and_3_out, and_4_out, and_5_out, and_6_out, and_7_out, and_8_out, and_9_out,
       and_10_out, and_11_out, and_12_out, and_13_out, and_14_out, or_1_out, or_2_out, or_3_out, xor_1_out,
       xor_2_out, xor_3_out, xor_4_out, xor_5_out, xor_6_out, xor_7_out, xor_8_out, xor_9_out, xor_10_out,
       xor_11_out, xor_12_out, xor_13_out, xor_14_out, xor_15_out, xor_16_out, xor_17_out, xor_18_out,
       xor_19_out, xor_20_out;

  xor odd_parity_1 (S0, A0, B0, C0);
  xor xor_1 (xor_1_out, A0, B0);
  xor xor_2 (xor_2_out, A1, B1);
  xor xor_3 (xor_3_out, A0, B0);
  xor xor_4 (xor_4_out, A1, B1);
  xor xor_5 (xor_5_out, A2, B2);
  xor xor_6 (xor_6_out, A1, B1);
  xor xor_7 (xor_7_out, A0, B0);
  xor xor_8 (xor_8_out, A2, B2);
  xor xor_9 (xor_9_out, A1, B1);
  xor xor_10 (xor_10_out, A2, B2);
  xor xor_11 (xor_11_out, A3, B3);
  xor xor_12 (xor_12_out, A2, B2);
  xor xor_13 (xor_13_out, A1, B1);
  xor xor_14 (xor_14_out, A0, B0);
  xor xor_15 (xor_15_out, A3, B3);
  xor xor_16 (xor_16_out, A2, B2);
  xor xor_17 (xor_17_out, A1, B1);
  xor xor_18 (xor_18_out, A3, B3);
  xor xor_19 (xor_19_out, A2, B2);
  xor xor_20 (xor_20_out, A3, B3);
  and and_1 (and_1_out, xor_1_out, C0);
  and and_2 (and_2_out, A0, B0);
  and and_3 (and_3_out, xor_2_out, xor_3_out, C0);
  and and_4 (and_4_out, A0, B0, xor_4_out);
  and and_5 (and_5_out, A1, B1);
  and and_6 (and_6_out, xor_5_out, xor_6_out, xor_7_out, C0);
  and and_7 (and_7_out, xor_8_out, xor_9_out, A0, B0);
  and and_8 (and_8_out, A1, B1, xor_10_out);
  and and_9 (and_9_out, A2, B2);
  and and_10 (and_10_out, xor_11_out, xor_12_out, xor_13_out, xor_14_out, C0);
  and and_11 (and_11_out, xor_15_out, xor_16_out, xor_17_out, A0, B0);
  and and_12 (and_12_out, xor_18_out, xor_19_out, A1, B1);
  and and_13 (and_13_out, A2, B2, xor_20_out);
  and and_14 (and_14_out, A3, B3);
  or or_1 (or_1_out, and_1_out, and_2_out);
  or or_2 (or_2_out, and_3_out, and_4_out, and_5_out);
  or or_3 (or_3_out, and_6_out, and_7_out, and_8_out, and_9_out);
  or or_4 (C4, and_10_out, and_11_out, and_12_out, and_13_out, and_14_out);
  xor odd_parity_2 (S1, A1, B1, or_1_out);
  xor odd_parity_3 (S2, A2, B2, or_2_out);
  xor odd_parity_4 (S3, A3, B3, or_3_out);
endmodule
