// Logisim project 实验1-校交1801-U201890018-郝凯欣.circ as structural Verilog: 5 circuits, main circuit 一位半加器
// C4
module \一位半加器  (
  input  A,
  input  B,
  output S,
  output C
);

  xor xor_1 (S, A, B);
  and and_1 (C, A, B);
endmodule

module \一位全加器  (
  input  A,
  input  B,
  input  Ci,
  output S,
  output Co
);

  wire and_1_out, and_2_out, and_3_out, and_4_out, and_5_out, odd_parity_1_out;

  xor odd_parity_1 (odd_parity_1_out, A, B, Ci);
  and and_1 (and_1_out, A, B, Ci);
  and and_2 (and_2_out, A, B);
  and and_3 (and_3_out, B, Ci);
  and and_4 (and_4_out, A, Ci);
  and and_5 (and_5_out, A, B, Ci);
  or or_1 (S, odd_parity_1_out, and_1_out);
  or or_2 (Co, and_2_out, and_3_out, and_4_out, and_5_out);
endmodule

// C0
module \串行四位并行加法器  (
  input  A0,
  input  A1,
  input  A2,
  input  A3,
  input  B0,
  input  B1,
  input  B2,
  input  B3,
  input  C0,
  output S0,
  output S1,
  output S2,
  output S3,
  output C4
);

  wire \一位全加器_1_co , \一位全加器_2_co , \一位全加器_3_co ;

  \一位全加器  \u_一位全加器_1  (.A(A0), .B(B0), .Ci(C0), .S(S0), .Co(\一位全加器_1_co ));
  \一位全加器  \u_一位全加器_2  (.A(A1), .B(B1), .Ci(\一位全加器_1_co ), .S(S1), .Co(\一位全加器_2_co ));
  \一位全加器  \u_一位全加器_3  (.A(A2), .B(B2), .Ci(\一位全加器_2_co ), .S(S2), .Co(\一位全加器_3_co ));
  \一位全加器  \u_一位全加器_4  (.A(A3), .B(B3), .Ci(\一位全加器_3_co ), .S(S3), .Co(C4));
endmodule

module \先行四位并行加法器  (
  input  A0,
  input  A1,
  input  A2,
  input  A3,
  input  B0,
  input  B1,
  input  B2,
  input  B3,
  input  C0,
  output S0,
  output S1,
  output S2,
  output S3,
  output C4
);

  wire and_1_out, and_2_out, and_3_out, and_4_out, and_5_out, and_6_out, and_7_out, and_8_out, and_9_out,
       and_10_out, and_11_out, and_12_out, and_13_out, and_14_out, or_1_out, or_2_out, or_3_out, xor_1_out,
       xor_2_out, xor_3_out, xor_4_out, xor_5_out, xor_6_out, xor_7_out, xor_8_out, xor_9_out, xor_10_out,
       xor_11_out, xor_12_out, xor_13_out, xor_14_out, xor_15_out, xor_16_out, xor_17_out, xor_18_out,
       xor_19_out, xor_20_out;

  xor odd_parity_1 (S0, A0, B0, C0);
  xor xor_1 (xor_1_out, B0, A0);
  xor xor_2 (xor_2_out, B1, A1);
  xor xor_3 (xor_3_out, B0, A0);
  xor xor_4 (xor_4_out, B1, A1);
  xor xor_5 (xor_5_out, B2, A2);
  xor xor_6 (xor_6_out, B1, A1);
  xor xor_7 (xor_7_out, B0, A0);
  xor xor_8 (xor_8_out, B2, A2);
  xor xor_9 (xor_9_out, B1, A1);
  xor xor_10 (xor_10_out, B2, A2);
  xor xor_11 (xor_11_out, B3, A3);
  xor xor_12 (xor_12_out, B2, A2);
  xor xor_13 (xor_13_out, B1, A1);
  xor xor_14 (xor_14_out, B0, A0);
  xor xor_15 (xor_15_out, B3, A3);
  xor xor_16 (xor_16_out, B2, A2);
  xor xor_17 (xor_17_out, B1, A1);
  xor xor_18 (xor_18_out, B3, A3);
  xor xor_19 (xor_19_out, B2, A2);
  xor xor_20 (xor_20_out, B3, A3);
  and and_1 (and_1_out, A0, B0);
  and and_2 (and_2_out, xor_1_out, C0);
  and and_3 (and_3_out, A1, B1);
  and and_4 (and_4_out, xor_2_out, xor_3_out, C0);
  and and_5 (and_5_out, xor_4_out, A0, B0);
  and and_6 (and_6_out, A2, B2);
  and and_7 (and_7_out, xor_5_out, xor_6_out, xor_7_out, C0);
  and and_8 (and_8_out, xor_8_out, xor_9_out, A0, B0);
  and and_9 (and_9_out, xor_10_out, A1, B1);
  and and_10 (and_10_out, A3, B3);
  and and_11 (and_11_out, xor_11_out, xor_12_out, xor_13_out, xor_14_out, C0);
  and and_12 (and_12_out, xor_15_out, xor_16_out, xor_17_out, A0, B0);
  and and_13 (and_13_out, xor_18_out, xor_19_out, A1, B1);
  and and_14 (and_14_out, xor_20_out, A2, B2);
  or or_1 (or_1_out, and_1_out, and_2_out);
  or or_2 (or_2_out, and_3_out, and_4_out, and_5_out);
  or or_3 (or_3_out, and_6_out, and_7_out, and_8_out, and_9_out);
  xor odd_parity_2 (S1, or_1_out, B1, A1);
  xor odd_parity_3 (S2, B2, A2, or_2_out);
  xor odd_parity_4 (S3, B3, A3, or_3_out);
  or or_4 (C4, and_10_out, and_11_out, and_12_out, and_13_out, and_14_out);
endmodule

module test (
  input  in_1,
  input  in_2,
  input  in_3,
  input  in_4,
  input  in_5,
  input  in_6,
  input  in_7,
  input  in_8,
  input  in_9,
  input  in_10,
  input  in_11,
  input  in_12,
  input  in_13,
  input  in_14,
  input  in_15,
  input  in_16,
  input  in_17,
  input  in_18,
  input  in_19,
  input  in_20,
  input  in_21,
  input  in_22,
  input  in_23,
  output out_24,
  output out_25,
  output out_26,
  output out_27,
  output out_28,
  output out_29,
  output out_30,
  output out_31,
  output out_32,
  output out_33,
  output out_34,
  output out_35,
  output out_36,
  output out_37
);

  \一位半加器  \u_一位半加器_1  (.A(in_19), .B(in_23), .S(out_34), .C(out_36));
  \先行四位并行加法器  \u_先行四位并行加法器_1  (
    .A0(in_14), .A1(in_13), .A2(in_12), .A3(in_11), .B0(in_18), .B1(in_17), .B2(in_16), .B3(in_15),
    .C0(in_10), .S0(out_31), .S1(out_30), .S2(out_29), .S3(out_28), .C4(out_33));
  \一位全加器  \u_一位全加器_1  (.A(in_20), .B(in_21), .Ci(in_22), .S(out_35), .Co(out_37));
  \串行四位并行加法器  \u_串行四位并行加法器_1  (
    .A0(in_1), .A1(in_2), .A2(in_3), .A3(in_4), .B0(in_5), .B1(in_6), .B2(in_7), .B3(in_8), .C4(out_32),
    .S0(out_24), .S1(out_25), .S2(out_26), .S3(out_27), .C0(in_9));
endmodule
