// Logisim project 实验2-校交1801-U201890018-郝凯欣.circ as structural Verilog: 5 circuits, main circuit lab1
module lab1 (
  input  in_1,
  input  in_2,
  input  CPu,
  input  CPd,
  input  in_5,
  input  CLR,
  input  in_7,
  input  in_8,
  output Qd,
  output Qc,
  output Qb,
  output Qa
);

  wire and_1_out, and_2_out, and_3_out, and_4_out, and_5_out, and_6_out, d_ff_1_qn, d_ff_2_qn, d_ff_3_qn,
       d_ff_4_qn, multiplexer_1_out, multiplexer_2_out, multiplexer_3_out, multiplexer_4_out,
       multiplexer_5_out, multiplexer_6_out, multiplexer_7_out, multiplexer_8_out, not_1_out, not_2_out,
       not_3_out, not_4_out, or_1_out, or_2_out, or_3_out, or_4_out, or_5_out, or_6_out, or_7_out, or_8_out;

  or or_1 (or_1_out, CPu, CPd);
  and and_1 (and_1_out, CPd, d_ff_4_qn, d_ff_3_qn, d_ff_2_qn);
  and and_2 (and_2_out, CPu, Qa, Qb, Qc);
  and and_3 (and_3_out, CPd, d_ff_4_qn, d_ff_3_qn);
  and and_4 (and_4_out, CPu, Qa, Qb);
  and and_5 (and_5_out, CPd, d_ff_4_qn);
  and and_6 (and_6_out, CPu, Qa);
  or or_2 (or_2_out, and_1_out, and_2_out);
  or or_3 (or_3_out, and_3_out, and_4_out);
  or or_4 (or_4_out, and_5_out, and_6_out);
  Multiplexer multiplexer_1 (.in0(1'b0), .in1(in_5), .out(multiplexer_1_out), .sel(in_7));  // open: en
  D_Flip_Flop #(.trigger("falling")) d_ff_1 (
    .clk(or_2_out), .D(d_ff_1_qn), .Q(Qd), .Qn(d_ff_1_qn), .preset(multiplexer_2_out), .en(1'b1),
    .reset(or_7_out));
  Multiplexer multiplexer_2 (.in0(1'b0), .in1(in_1), .out(multiplexer_2_out), .sel(in_7));  // open: en
  D_Flip_Flop #(.trigger("falling")) d_ff_2 (
    .clk(or_3_out), .D(d_ff_2_qn), .Q(Qc), .Qn(d_ff_2_qn), .preset(multiplexer_3_out), .en(1'b1),
    .reset(or_8_out));
  Multiplexer multiplexer_3 (.in0(1'b0), .in1(in_2), .out(multiplexer_3_out), .sel(in_7));  // open: en
  D_Flip_Flop #(.trigger("falling")) d_ff_3 (
    .clk(or_4_out), .D(d_ff_3_qn), .Q(Qb), .Qn(d_ff_3_qn), .preset(multiplexer_1_out), .en(1'b1),
    .reset(or_5_out));
  or or_5 (or_5_out, CLR, multiplexer_6_out);
  D_Flip_Flop #(.trigger("falling")) d_ff_4 (
    .clk(or_1_out), .D(d_ff_4_qn), .Q(Qa), .Qn(d_ff_4_qn), .preset(multiplexer_4_out), .en(1'b1),
    .reset(or_6_out));
  or or_6 (or_6_out, CLR, multiplexer_7_out);
  Multiplexer multiplexer_4 (.in0(1'b0), .in1(in_8), .out(multiplexer_4_out), .sel(in_7));  // open: en
  or or_7 (or_7_out, CLR, multiplexer_5_out);
  Multiplexer multiplexer_5 (.in0(1'b0), .in1(not_1_out), .out(multiplexer_5_out), .sel(in_7));  // open: en
  not not_1 (not_1_out, in_1);
  or or_8 (or_8_out, CLR, multiplexer_8_out);
  Multiplexer multiplexer_6 (.in0(1'b0), .in1(not_4_out), .out(multiplexer_6_out), .sel(in_7));  // open: en
  Multiplexer multiplexer_7 (.in0(1'b0), .in1(not_2_out), .out(multiplexer_7_out), .sel(in_7));  // open: en
  not not_2 (not_2_out, in_8);
  Multiplexer multiplexer_8 (.in0(1'b0), .in1(not_3_out), .out(multiplexer_8_out), .sel(in_7));  // open: en
  not not_3 (not_3_out, in_2);
  not not_4 (not_4_out, in_5);
endmodule

module \测试  (
  input  in_1,
  input  in_2,
  input  in_3,
  input  in_4,
  input  in_5,
  input  in_6,
  input  in_7,
  input  in_8,
  input  in_9,
  input  in_10,
  input  in_11,
  input  in_12,
  input  in_13,
  input  in_14,
  input  in_15,
  input  in_16,
  output out_17,
  output out_18,
  output out_19,
  output out_20,
  output out_21,
  output out_22,
  output out_23,
  output out_24,
  output out_25,
  output out_26,
  output out_27,
  output out_28
);

  wire button_1_out, button_2_out, button_3_out, lab2_2_s1, lab2_2_s2, lab2_2_s4, lab2_2_s8, lab2_2_s10,
       lab2_2_s20, lab2_2_s40, lab2_2_s80, lab3_1_a, lab3_1_b, lab3_1_c, lab3_1_d, lab3_1_e, lab3_1_f,
       lab3_1_g, lab3_2_a, lab3_2_b, lab3_2_c, lab3_2_d, lab3_2_e, lab3_2_f, lab3_2_g, lab4_1_out_4,
       lab4_1_out_5, lab4_1_out_6, lab4_1_out_7, lab4_1_out_8, lab4_1_out_9, lab4_1_out_10, lab4_1_out_11,
       lab4_1_out_12, lab4_1_out_13, lab4_1_out_14, lab4_1_out_15, lab4_1_out_16, lab4_1_out_17,
       lab4_1_out_18;

  Button button_1 (.out(button_1_out));
  Button button_2 (.out(button_2_out));
  Button button_3 (.out(button_3_out));
  _7_Segment_Display u_7_segment_display_1 (
    .g(lab4_1_out_10), .f(lab4_1_out_9), .a(lab4_1_out_4), .b(lab4_1_out_5), .e(lab4_1_out_8),
    .d(lab4_1_out_7), .c(lab4_1_out_6));  // open: dp
  lab1 lab1_1 (
    .Qd(out_25), .Qc(out_26), .Qb(out_27), .Qa(out_28), .CPd(in_11), .CPu(in_10), .in_7(in_15), .in_8(in_14),
    .in_5(in_16), .in_1(in_12), .in_2(in_13));  // open: CLR
  lab4 lab4_1 (
    .out_17(lab4_1_out_17), .out_4(lab4_1_out_4), .out_5(lab4_1_out_5), .out_6(lab4_1_out_6),
    .out_7(lab4_1_out_7), .out_8(lab4_1_out_8), .out_9(lab4_1_out_9), .out_11(lab4_1_out_11),
    .out_12(lab4_1_out_12), .out_13(lab4_1_out_13), .out_14(lab4_1_out_14), .out_15(lab4_1_out_15),
    .out_16(lab4_1_out_16), .out_18(lab4_1_out_18), .in_1(button_1_out), .in_2(button_2_out),
    .in_3(button_3_out), .out_10(lab4_1_out_10));
  lab2 lab2_1 (
    .S8(out_18), .S4(out_19), .S2(out_20), .S1(out_21), .S20(out_17), .S40(out_22), .S80(out_23),
    .S10(out_24), .in_1(in_1), .in_2(in_2), .in_3(in_3), .in_4(in_4));
  _7_Segment_Display u_7_segment_display_2 (
    .g(lab4_1_out_17), .f(lab4_1_out_16), .a(lab4_1_out_11), .b(lab4_1_out_12), .e(lab4_1_out_15),
    .d(lab4_1_out_14), .c(lab4_1_out_13));  // open: dp
  LED led_1 (.in(lab4_1_out_18));
  lab2 lab2_2 (
    .S8(lab2_2_s8), .S4(lab2_2_s4), .S2(lab2_2_s2), .S1(lab2_2_s1), .S20(lab2_2_s20), .S40(lab2_2_s40),
    .S80(lab2_2_s80), .S10(lab2_2_s10), .in_1(in_5), .in_2(in_6), .in_3(in_7), .in_4(in_8));
  LAB3 lab3_1 (
    .A0(lab2_2_s10), .A1(lab2_2_s80), .A2(lab2_2_s40), .A3(lab2_2_s20), .a(lab3_1_a), .b(lab3_1_b),
    .c(lab3_1_c), .d(lab3_1_d), .e(lab3_1_e), .f(lab3_1_f), .g(lab3_1_g));
  LAB3 lab3_2 (
    .A0(lab2_2_s1), .A1(lab2_2_s2), .A2(lab2_2_s4), .A3(lab2_2_s8), .a(lab3_2_a), .b(lab3_2_b), .c(lab3_2_c),
    .d(lab3_2_d), .e(lab3_2_e), .f(lab3_2_f), .g(lab3_2_g));
  _7_Segment_Display u_7_segment_display_3 (
    .g(lab3_1_g), .f(lab3_1_f), .a(lab3_1_a), .b(lab3_1_b), .e(lab3_1_e), .d(lab3_1_d), .c(lab3_1_c));  // open: dp
  _7_Segment_Display u_7_segment_display_4 (
    .g(lab3_2_g), .f(lab3_2_f), .a(lab3_2_a), .b(lab3_2_b), .e(lab3_2_e), .d(lab3_2_d), .c(lab3_2_c));  // open: dp
endmodule

module lab2 (
  input  in_1,
  input  in_2,
  input  in_3,
  input  in_4,
  output S10,
  output S4,
  output S2,
  output S8,
  output S1,
  output S20,
  output S40,
  output S80
);

  wire and_1_out, and_2_out, or_1_out;

  \先行四位并行加法器  \u_先行四位并行加法器_1  (
    .A0(in_4), .A1(in_3), .A2(in_2), .A3(in_1), .B0(1'b0), .B1(or_1_out), .B2(or_1_out), .B3(1'b0),
    .C0(1'b0), .S0(S1), .S1(S2), .S2(S4), .S3(S8), .C4(S10));
  and and_1 (and_1_out, in_3, in_1);
  and and_2 (and_2_out, in_2, in_1);
  or or_1 (or_1_out, and_1_out, and_2_out);

  assign S20 = 1'b0;
  assign S40 = 1'b0;
  assign S80 = 1'b0;
endmodule

module LAB3 (
  input  A0,
  input  A1,
  input  A2,
  input  A3,
  output a,
  output b,
  output c,
  output d,
  output e,
  output f,
  output g
);

  wire and_1_out, and_2_out, and_3_out, and_4_out, and_5_out, and_6_out, and_7_out, and_8_out, and_9_out,
       and_10_out, and_11_out, and_12_out, and_13_out, and_14_out, and_15_out, and_16_out, and_17_out,
       and_18_out, and_19_out, and_20_out, and_21_out, and_22_out, and_23_out, and_24_out, and_25_out,
       and_26_out, not_1_out, not_2_out, not_3_out, not_4_out, not_5_out, not_6_out, not_7_out, not_8_out,
       not_9_out, not_10_out, not_11_out, not_12_out, not_13_out, not_14_out, not_15_out, not_16_out,
       not_17_out, not_18_out, not_19_out, not_20_out, not_21_out, not_22_out, not_23_out, not_24_out,
       not_25_out, not_26_out, not_27_out, not_28_out, not_29_out, not_30_out, not_31_out, not_32_out,
       not_33_out, not_34_out, not_35_out, not_36_out, not_37_out;

  not not_1 (not_1_out, A3);
  not not_2 (not_2_out, A2);
  and and_1 (and_1_out, not_1_out, not_2_out, not_3_out);
  not not_3 (not_3_out, A0);
  not not_4 (not_4_out, A3);
  not not_5 (not_5_out, A2);
  and and_2 (and_2_out, not_4_out, not_5_out, A1);
  not not_6 (not_6_out, A3);
  and and_3 (and_3_out, not_6_out, A2, A0);
  not not_7 (not_7_out, A2);
  and and_4 (and_4_out, A3, not_7_out, not_8_out);
  not not_8 (not_8_out, A1);
  not not_9 (not_9_out, A1);
  and and_5 (and_5_out, A3, not_9_out, A0);
  not not_10 (not_10_out, A3);
  and and_6 (and_6_out, not_10_out, not_11_out);
  not not_11 (not_11_out, A2);
  not not_12 (not_12_out, A2);
  and and_7 (and_7_out, not_12_out, not_13_out);
  not not_13 (not_13_out, A1);
  not not_14 (not_14_out, A1);
  and and_8 (and_8_out, not_14_out, not_15_out);
  not not_15 (not_15_out, A0);
  not not_16 (not_16_out, A3);
  and and_9 (and_9_out, not_16_out, A1, A0);
  not not_17 (not_17_out, A2);
  and and_10 (and_10_out, not_17_out, not_18_out);
  not not_18 (not_18_out, A1);
  not not_19 (not_19_out, A2);
  and and_11 (and_11_out, not_19_out, A0);
  not not_20 (not_20_out, A3);
  and and_12 (and_12_out, not_20_out, A2);
  not not_21 (not_21_out, A2);
  and and_13 (and_13_out, not_21_out, not_22_out);
  not not_22 (not_22_out, A0);
  not not_23 (not_23_out, A2);
  and and_14 (and_14_out, not_23_out, A1);
  and and_15 (and_15_out, A1, not_24_out);
  not not_24 (not_24_out, A0);
  not not_25 (not_25_out, A1);
  and and_16 (and_16_out, A2, not_25_out, A0);
  not not_26 (not_26_out, A2);
  and and_17 (and_17_out, not_26_out, not_27_out);
  not not_27 (not_27_out, A0);
  and and_18 (and_18_out, A1, not_28_out);
  not not_28 (not_28_out, A0);
  not not_29 (not_29_out, A1);
  and and_19 (and_19_out, not_29_out, not_30_out);
  not not_30 (not_30_out, A0);
  and and_20 (and_20_out, A2, not_31_out);
  not not_31 (not_31_out, A1);
  and and_21 (and_21_out, A2, not_32_out);
  not not_32 (not_32_out, A0);
  and and_22 (and_22_out, A3, not_33_out);
  not not_33 (not_33_out, A1);
  not not_34 (not_34_out, A2);
  and and_23 (and_23_out, not_34_out, A1);
  and and_24 (and_24_out, A2, not_35_out);
  not not_35 (not_35_out, A1);
  and and_25 (and_25_out, A2, not_36_out);
  not not_36 (not_36_out, A0);
  and and_26 (and_26_out, A3, not_37_out);
  not not_37 (not_37_out, A2);
  or or_1 (c, and_10_out, and_11_out, and_12_out);
  or or_2 (e, and_17_out, and_18_out);
  or or_3 (a, and_1_out, and_2_out, and_3_out, and_4_out, and_5_out);
  or or_4 (d, and_13_out, and_14_out, and_15_out, and_16_out);
  or or_5 (f, and_19_out, and_20_out, and_21_out, and_22_out);
  or or_6 (g, and_23_out, and_24_out, and_25_out, and_26_out);
  or or_7 (b, and_6_out, and_7_out, and_8_out, and_9_out);
endmodule

module lab4 (
  input  in_1,
  input  in_2,
  input  in_3,
  output out_4,
  output out_5,
  output out_6,
  output out_7,
  output out_8,
  output out_9,
  output out_10,
  output out_11,
  output out_12,
  output out_13,
  output out_14,
  output out_15,
  output out_16,
  output out_17,
  output out_18
);

  wire and_2_out, and_3_out, lab1_1_qa, lab1_1_qb, lab1_1_qc, lab1_1_qd, lab2_1_s1, lab2_1_s2, lab2_1_s4,
       lab2_1_s8, lab2_1_s10, lab2_1_s20, lab2_1_s40, lab2_1_s80, nand_1_out, not_1_out, or_1_out;

  and and_1 (out_18, in_1, not_1_out);
  not not_1 (not_1_out, nand_1_out);
  nand nand_1 (nand_1_out, lab1_1_qa, lab1_1_qb, lab1_1_qc, lab1_1_qd);
  and and_2 (and_2_out, nand_1_out, in_1);
  and and_3 (and_3_out, in_2, or_1_out);
  lab1 lab1_1 (
    .CLR(in_3), .Qd(lab1_1_qd), .Qc(lab1_1_qc), .Qb(lab1_1_qb), .Qa(lab1_1_qa), .CPd(and_3_out),
    .CPu(and_2_out));  // open: in_7, in_8, in_5, in_1, in_2
  LAB3 lab3_1 (
    .A0(lab2_1_s10), .A1(lab2_1_s80), .A2(lab2_1_s40), .A3(lab2_1_s20), .a(out_4), .b(out_5), .c(out_6),
    .d(out_7), .e(out_8), .f(out_9), .g(out_10));
  LAB3 lab3_2 (
    .A0(lab2_1_s1), .A1(lab2_1_s2), .A2(lab2_1_s4), .A3(lab2_1_s8), .a(out_11), .b(out_12), .c(out_13),
    .d(out_14), .e(out_15), .f(out_16), .g(out_17));
  lab2 lab2_1 (
    .S8(lab2_1_s8), .S4(lab2_1_s4), .S2(lab2_1_s2), .S1(lab2_1_s1), .S20(lab2_1_s20), .S40(lab2_1_s40),
    .S80(lab2_1_s80), .S10(lab2_1_s10), .in_1(lab1_1_qd), .in_2(lab1_1_qc), .in_3(lab1_1_qb), .in_4(lab1_1_qa));
  or or_1 (or_1_out, lab1_1_qa, lab1_1_qb, lab1_1_qc, lab1_1_qd);
endmodule
