// Logisim project 实验5-校交1801-U201816022-尹泽源.circ as structural Verilog: 14 circuits, main circuit 四位二进制可逆计数器
module \四位二进制可逆计数器  (
  input  D,
  input  C,
  input  B,
  input  CPU,
  input  A,
  input  CPD,
  input  \LD非 ,
  input  CLR,
  output QD,
  output QC,
  output QB,
  output QA
);

  wire _1_qn, _2_qn, _3_qn, _4_qn, and_1_out, and_2_out, and_3_out, and_4_out, and_5_out, and_6_out,
       and_7_out, and_8_out, and_9_out, and_10_out, and_11_out, and_12_out, and_13_out, and_14_out,
       not_1_out, or_1_out, or_2_out, or_3_out, or_4_out, or_5_out, or_6_out, or_7_out, or_8_out;

  not not_1 (not_1_out, \LD非 );
  or or_1 (or_1_out, CPD, CPU);
  and and_1 (and_1_out, CPD, ~QA, ~QB);  // AND_Gate
  and and_2 (and_2_out, CPU, QA, QB);
  and and_3 (and_3_out, CPD, ~QA);  // AND_Gate
  and and_4 (and_4_out, CPU, QA);
  and and_5 (and_5_out, CPD, ~QC, ~QB, ~QA);  // AND_Gate
  and and_6 (and_6_out, CPU, QC, QB, QA);
  or or_2 (or_2_out, and_1_out, and_2_out);
  or or_3 (or_3_out, and_3_out, and_4_out);
  or or_4 (or_4_out, and_5_out, and_6_out);
  and and_7 (and_7_out, D, not_1_out);
  and and_8 (and_8_out, ~D, not_1_out);  // AND_Gate
  and and_9 (and_9_out, C, not_1_out);
  and and_10 (and_10_out, ~C, not_1_out);  // AND_Gate
  and and_11 (and_11_out, B, not_1_out);
  and and_12 (and_12_out, ~B, not_1_out);  // AND_Gate
  and and_13 (and_13_out, A, not_1_out);
  and and_14 (and_14_out, ~A, not_1_out);  // AND_Gate
  D_Flip_Flop #(.trigger("falling"), .Pre_Clr_Positions("ABOVE_BELOW"), .NegatePresetClear("false"), .enable("false"), .NewFFLayout("true")) _4 (
    .clk(or_4_out), .D(_4_qn), .Q(QD), .Qn(_4_qn), .preset(and_7_out), .reset(or_5_out));
  or or_5 (or_5_out, and_8_out, CLR);
  D_Flip_Flop #(.trigger("falling"), .Pre_Clr_Positions("ABOVE_BELOW"), .NegatePresetClear("false"), .enable("false"), .NewFFLayout("true")) _3 (
    .clk(or_2_out), .D(_3_qn), .Q(QC), .Qn(_3_qn), .preset(and_9_out), .reset(or_6_out));
  or or_6 (or_6_out, and_10_out, CLR);
  D_Flip_Flop #(.trigger("falling"), .Pre_Clr_Positions("ABOVE_BELOW"), .NegatePresetClear("false"), .enable("false"), .NewFFLayout("true")) _2 (
    .clk(or_3_out), .D(_2_qn), .Q(QB), .Qn(_2_qn), .preset(and_11_out), .reset(or_7_out));
  or or_7 (or_7_out, and_12_out, CLR);
  D_Flip_Flop #(.trigger("falling"), .Pre_Clr_Positions("ABOVE_BELOW"), .NegatePresetClear("false"), .enable("false"), .NewFFLayout("true")) _1 (
    .clk(or_1_out), .D(_1_qn), .Q(QA), .Qn(_1_qn), .preset(and_13_out), .reset(or_8_out));
  or or_8 (or_8_out, and_14_out, CLR);
endmodule

module \六十进制计数器  (
  input  CPU,
  input  Clr,
  input  CPD,
  input  Adj,
  output Q1D,
  output Q1C,
  output Q1B,
  output Q1A,
  output Q0D,
  output Q0C,
  output Q0B,
  output Q0A,
  output nQcc
);

  wire and_1_out, and_2_out, and_3_out, and_4_out, and_5_out, and_6_out, or_1_out, or_2_out, \全0_2_out ,
       \全0_out , \全1_out ;
  wire [7:0] \四位二进制可逆计数器_2_qa ;
  wire [7:4] divider_1_out, divider_1_rem;

  not not_1 (nQcc, and_1_out);
  and and_1 (and_1_out, \四位二进制可逆计数器_2_qa [2], \四位二进制可逆计数器_2_qa [3], \四位二进制可逆计数器_2_qa [4], \四位二进制可逆计数器_2_qa [5]);
  or or_1 (or_1_out, and_1_out, Clr);
  and and_2 (and_2_out, CPD, Adj);
  and and_3 (and_3_out, CPU, \全1_out );
  and and_4 (and_4_out, ~\全0_out , and_2_out, \全0_2_out );  // AND_Gate
  and \u_全0  (\全0_out , ~\四位二进制可逆计数器_2_qa [4], ~\四位二进制可逆计数器_2_qa [5], ~\四位二进制可逆计数器_2_qa [6], ~\四位二进制可逆计数器_2_qa [7]);  // AND_Gate
  and and_5 (and_5_out, \全0_2_out , ~\全0_out );  // AND_Gate
  \四位二进制可逆计数器  \u_四位二进制可逆计数器_1  (
    .D(1'b0), .C(1'b0), .B(1'b0), .CPU(and_3_out), .A(1'b0), .CPD(and_4_out), .\LD非 (1'b1), .CLR(or_1_out),
    .QD(\四位二进制可逆计数器_2_qa [7]), .QC(\四位二进制可逆计数器_2_qa [6]), .QB(\四位二进制可逆计数器_2_qa [5]), .QA(\四位二进制可逆计数器_2_qa [4]));
  and \u_全1  (\全1_out , \四位二进制可逆计数器_2_qa [0], \四位二进制可逆计数器_2_qa [1], \四位二进制可逆计数器_2_qa [2], \四位二进制可逆计数器_2_qa [3]);
  and \u_全0_2  (\全0_2_out , ~\四位二进制可逆计数器_2_qa [0], ~\四位二进制可逆计数器_2_qa [1], ~\四位二进制可逆计数器_2_qa [2], ~\四位二进制可逆计数器_2_qa [3]);  // AND_Gate
  or or_2 (or_2_out, ~\全0_2_out , and_5_out);  // OR_Gate
  Divider #(.width(8)) divider_1 (
    .a(\四位二进制可逆计数器_2_qa ), .b(8'ha), .out({divider_1_out, Q1D, Q1C, Q1B, Q1A}), .upper({8{1'b0}}),
    .rem({divider_1_rem, Q0D, Q0C, Q0B, Q0A}));
  and and_6 (and_6_out, or_2_out, and_2_out);
  \四位二进制可逆计数器  \u_四位二进制可逆计数器_2  (
    .D(1'b0), .C(1'b0), .B(1'b0), .CPU(CPU), .A(1'b0), .CPD(and_6_out), .\LD非 (1'b1), .CLR(or_1_out),
    .QD(\四位二进制可逆计数器_2_qa [3]), .QC(\四位二进制可逆计数器_2_qa [2]), .QB(\四位二进制可逆计数器_2_qa [1]), .QA(\四位二进制可逆计数器_2_qa [0]));
endmodule

module \六十进制计数器测试电路  (
  input  Adj,
  input  Clr,
  output \Q值 
);

  wire CPd_out, CPu_out, d_ff_1_qn, \六十进制计数器_1_nqcc ;
  wire [3:0] \六十进制计数器_1_q0a , \六十进制计数器_1_q1a ;

  Button CPu (.out(CPu_out));
  Button CPd (.out(CPd_out));
  Hex_Digit_Display hex_digit_display_1 (.value(\六十进制计数器_1_q1a ));  // open: dp
  Hex_Digit_Display hex_digit_display_2 (.value(\六十进制计数器_1_q0a ));  // open: dp
  \六十进制计数器  \u_六十进制计数器_1  (
    .CPU(CPu_out), .Clr(Clr), .CPD(CPd_out), .Adj(Adj), .Q1D(\六十进制计数器_1_q1a [3]), .Q1C(\六十进制计数器_1_q1a [2]),
    .Q1B(\六十进制计数器_1_q1a [1]), .Q1A(\六十进制计数器_1_q1a [0]), .Q0D(\六十进制计数器_1_q0a [3]), .Q0C(\六十进制计数器_1_q0a [2]),
    .Q0B(\六十进制计数器_1_q0a [1]), .Q0A(\六十进制计数器_1_q0a [0]), .nQcc(\六十进制计数器_1_nqcc ));
  D_Flip_Flop #(.trigger("rising"), .Pre_Clr_Positions("ABOVE_BELOW"), .NegatePresetClear("false"), .enable("false"), .NewFFLayout("true")) d_ff_1 (
    .clk(\六十进制计数器_1_nqcc ), .D(d_ff_1_qn), .Q(\Q值 ), .Qn(d_ff_1_qn));  // open: preset, reset

  // Notes on the sheet:
  //   所以采用D触发器来显示进位信号的变化
  //   进位信号每产生一次（由1变为0，再恢复到1），D触发器Q值变化一次
  //   因为最后一问要使用到此电路，所以设计时将进位信号输出操作和清零操作同时进行
  //   进位信号输出操作和清零操作同时进行，会导致进位信号无法直观地观察到
endmodule

module \十二进制计数器或二十四进制的计数器电路  (
  input  CPU,
  input  Adj,
  input  CPD,
  input  Clr,
  input  Set,
  output out_6,
  output out_7,
  output out_8,
  output out_9,
  output out_10,
  output out_11,
  output out_12,
  output out_13,
  output nQcc
);

  wire multiplexer_1_out, or_1_out, \满12_out , \满24_out ;

  \六十进制计数器  \u_六十进制计数器_1  (
    .CPU(CPU), .Clr(or_1_out), .CPD(CPD), .Adj(Adj), .Q1D(out_6), .Q1C(out_7), .Q1B(out_8), .Q1A(out_9),
    .Q0D(out_10), .Q0C(out_11), .Q0B(out_12), .Q0A(out_13));  // open: nQcc
  or or_1 (or_1_out, multiplexer_1_out, Clr);
  and \u_满12  (\满12_out , out_12, out_9);
  and \u_满24  (\满24_out , out_11, out_8);
  Multiplexer #(.select(1), .width(1), .disabled("Z"), .enable("false")) multiplexer_1 (
    .in0(\满12_out ), .in1(\满24_out ), .out(multiplexer_1_out), .sel(Set));
  not not_1 (nQcc, multiplexer_1_out);
endmodule

module \十二进制计数器或二十四进制的计数器测试电路  (
  input  Adj,
  input  Set,
  input  Clr,
  output \Q值 
);

  wire CPd_out, CPu_out, d_ff_1_qn, \十二进制计数器或二十四进制的计数器电路_1_nqcc ;
  wire [3:0] \十二进制计数器或二十四进制的计数器电路_1_out_9 , \十二进制计数器或二十四进制的计数器电路_1_out_13 ;

  Button CPu (.out(CPu_out));
  Button CPd (.out(CPd_out));
  Hex_Digit_Display hex_digit_display_1 (.value(\十二进制计数器或二十四进制的计数器电路_1_out_9 ));  // open: dp
  Hex_Digit_Display hex_digit_display_2 (.value(\十二进制计数器或二十四进制的计数器电路_1_out_13 ));  // open: dp
  \十二进制计数器或二十四进制的计数器电路  \u_十二进制计数器或二十四进制的计数器电路_1  (
    .nQcc(\十二进制计数器或二十四进制的计数器电路_1_nqcc ), .CPU(CPu_out), .Adj(Adj), .CPD(CPd_out),
    .out_6(\十二进制计数器或二十四进制的计数器电路_1_out_9 [3]), .out_7(\十二进制计数器或二十四进制的计数器电路_1_out_9 [2]),
    .out_8(\十二进制计数器或二十四进制的计数器电路_1_out_9 [1]), .out_9(\十二进制计数器或二十四进制的计数器电路_1_out_9 [0]),
    .out_10(\十二进制计数器或二十四进制的计数器电路_1_out_13 [3]), .out_11(\十二进制计数器或二十四进制的计数器电路_1_out_13 [2]),
    .out_12(\十二进制计数器或二十四进制的计数器电路_1_out_13 [1]), .out_13(\十二进制计数器或二十四进制的计数器电路_1_out_13 [0]), .Clr(Clr),
    .Set(Set));
  D_Flip_Flop #(.trigger("rising"), .Pre_Clr_Positions("ABOVE_BELOW"), .NegatePresetClear("false"), .enable("false"), .NewFFLayout("true")) d_ff_1 (
    .clk(\十二进制计数器或二十四进制的计数器电路_1_nqcc ), .D(d_ff_1_qn), .Q(\Q值 ), .Qn(d_ff_1_qn));  // open: preset, reset

  // Notes on the sheet:
  //   所以采用D触发器来显示进位信号的变化
  //   因为最后一问要使用到此电路，所以设计时将进位信号输出操作和清零操作同时进行
  //   进位信号输出操作和清零操作同时进行，会导致进位信号无法直观地观察到
  //   进位信号每产生一次（由1变为0，再恢复到1），D触发器Q值变化一次
endmodule

module \上下午文字显示的电路  (
  input  TT,
  input  AM_FM,
  output [4:0] out_3,
  output [4:0] out_4,
  output [4:0] out_5,
  output [4:0] out_6
);

  wire [4:0] multiplexer_2_out, multiplexer_5_out, multiplexer_7_out;

  Multiplexer #(.select(1), .width(5), .disabled("Z"), .enable("false")) multiplexer_1 (
    .in0({5{1'b0}}), .in1(multiplexer_2_out), .out(out_3), .sel(TT));
  Multiplexer #(.select(1), .width(5), .disabled("Z"), .enable("false")) multiplexer_2 (
    .in0(5'b00001), .in1(5'b10000), .out(multiplexer_2_out), .sel(AM_FM));
  Multiplexer #(.select(1), .width(5), .disabled("Z"), .enable("false")) multiplexer_3 (
    .in0({5{1'b0}}), .in1({5{1'b1}}), .out(out_4), .sel(TT));
  Multiplexer #(.select(1), .width(5), .disabled("Z"), .enable("false")) multiplexer_4 (
    .in0({5{1'b0}}), .in1(multiplexer_5_out), .out(out_5), .sel(TT));
  Multiplexer #(.select(1), .width(5), .disabled("Z"), .enable("false")) multiplexer_5 (
    .in0(5'b00101), .in1(5'b10100), .out(multiplexer_5_out), .sel(AM_FM));
  Multiplexer #(.select(1), .width(5), .disabled("Z"), .enable("false")) multiplexer_6 (
    .in0({5{1'b0}}), .in1(multiplexer_7_out), .out(out_6), .sel(TT));
  Multiplexer #(.select(1), .width(5), .disabled("Z"), .enable("false")) multiplexer_7 (
    .in0(5'b00001), .in1(5'b10000), .out(multiplexer_7_out), .sel(AM_FM));
endmodule

module \上下午文字显示测试电路  (
  input  in_1,
  input  in_2
);

  wire [4:0] \上下午文字显示的电路_1_out_3 , \上下午文字显示的电路_1_out_4 , \上下午文字显示的电路_1_out_5 , \上下午文字显示的电路_1_out_6 ;

  \上下午文字显示的电路  \u_上下午文字显示的电路_1  (
    .TT(in_2), .AM_FM(in_1), .out_3(\上下午文字显示的电路_1_out_3 ), .out_4(\上下午文字显示的电路_1_out_4 ),
    .out_5(\上下午文字显示的电路_1_out_5 ), .out_6(\上下午文字显示的电路_1_out_6 ));
  DotMatrix #(.inputtype("column"), .matrixcols(4), .matrixrows(5), .persist(0), .dotshape("square")) dotmatrix_1 (
    .col0(\上下午文字显示的电路_1_out_3 ), .col1(\上下午文字显示的电路_1_out_4 ), .col2(\上下午文字显示的电路_1_out_5 ),
    .col3(\上下午文字显示的电路_1_out_6 ));
endmodule

module \电子钟整点报时电路  (
  input  [3:0] \分1 ,
  input  [3:0] \分0 ,
  input  [3:0] \秒1 ,
  input  [3:0] \秒0 ,
  output out_5
);

  wire comparator_1_eq, comparator_2_eq, comparator_3_eq;

  Comparator #(.width(4), .mode("unsigned")) comparator_1 (
    .a(\分1 ), .b(4'b0101), .eq(comparator_1_eq));  // open: gt, lt
  Comparator #(.width(4), .mode("unsigned")) comparator_2 (
    .a(\分0 ), .b(4'b1001), .eq(comparator_2_eq));  // open: gt, lt
  Comparator #(.width(4), .mode("unsigned")) comparator_3 (
    .a(\秒1 ), .b(4'b0101), .eq(comparator_3_eq));  // open: gt, lt
  and and_1 (out_5, comparator_1_eq, comparator_2_eq, comparator_3_eq);
endmodule

module \电子钟整点报时电路测试电路  (
  input  [3:0] in_1,
  input  [3:0] in_2,
  input  [3:0] in_3,
  input  [3:0] in_4
);

  wire \电子钟整点报时电路_1_out_5 ;

  LED #(.active("true")) led_1 (.in(\电子钟整点报时电路_1_out_5 ));
  \电子钟整点报时电路  \u_电子钟整点报时电路_1  (.out_5(\电子钟整点报时电路_1_out_5 ), .\分1 (in_1), .\分0 (in_2), .\秒1 (in_3), .\秒0 (in_4));

  // Notes on the sheet:
  //   分:秒=59:50~59:59    LED灯亮起
endmodule

module \秒脉冲产生电路  (
  input  in_1,
  output out_2
);

  wire \六十进制计数器_1_q0a , \六十进制计数器_1_q0b , \六十进制计数器_1_q0c ;

  and and_1 (out_2, in_1, \六十进制计数器_1_q0b , \六十进制计数器_1_q0a );
  \六十进制计数器  \u_六十进制计数器_1  (
    .CPU(in_1), .Clr(\六十进制计数器_1_q0c ), .CPD(1'b0), .Adj(1'b0), .Q0C(\六十进制计数器_1_q0c ), .Q0B(\六十进制计数器_1_q0b ),
    .Q0A(\六十进制计数器_1_q0a ));  // open: Q1D, Q1C, Q1B, Q1A, Q0D, nQcc
endmodule

module \多功能数字钟  (
  input  Alarm,
  input  ctrl,
  input  Set_0_12_1_24,
  input  CP,
  input  Clr,
  input  CPu,
  input  CPd,
  input  Adj0,
  input  Adj1,
  output [3:0] \秒1 ,
  output [3:0] \秒0 ,
  output [3:0] \分1 ,
  output [3:0] \分0 ,
  output [3:0] \时0 ,
  output [3:0] \时1 ,
  output [4:0] out_16,
  output [4:0] out_17,
  output [4:0] out_18,
  output [4:0] out_19,
  output \闹钟 ,
  output \定点报时 
);

  wire _12_out, and_1_out, and_2_out, and_3_out, and_4_out, and_5_out, and_6_out, and_7_out, and_8_out,
       and_9_out, and_10_out, and_11_out, and_12_out, and_13_out, and_14_out, and_15_out, comparator_1_eq,
       comparator_1_gt, comparator_2_eq, not_1_out, or_1_out, or_2_out, \分不向小时进位_out , \分钟_nqcc , \秒_nqcc ,
       \秒脉冲产生电路_1_out_2 ;
  wire [3:0] multiplexer_5_out, multiplexer_6_out, \分钟_q0a , \分钟_q1a , \小时_out_9 , \小时_out_13 , \秒_q0a ,
       \秒_q1a , \闹钟_1_alarm分0 , \闹钟_1_alarm分1 , \闹钟_1_alarm时0 , \闹钟_1_alarm时1 ;
  wire [7:0] adder_1_out, bit_extender_1_out, bit_extender_2_out, multiplexer_7_out, multiplexer_8_out,
       multiplexer_9_out, multiplier_1_out, subtractor_1_out;
  wire [7:4] divider_1_out, divider_1_rem;

  \秒脉冲产生电路  \u_秒脉冲产生电路_1  (.out_2(\秒脉冲产生电路_1_out_2 ), .in_1(CP));
  and and_1 (and_1_out, CPu, ~Alarm, and_6_out);  // AND_Gate
  and and_2 (and_2_out, ~Alarm, Clr);  // AND_Gate
  and and_3 (and_3_out, Clr, Alarm);
  and and_4 (and_4_out, CPd, ~Alarm, and_6_out);  // AND_Gate
  Multiplexer #(.select(1), .width(4), .disabled("Z"), .enable("false")) multiplexer_1 (
    .in0(\秒_q1a ), .in1(4'b0000), .out(\秒1 ), .sel(Alarm));
  and and_5 (and_5_out, \秒脉冲产生电路_1_out_2 , ~and_6_out);  // AND_Gate
  and and_6 (and_6_out, Adj0, ~Alarm);  // AND_Gate
  Multiplexer #(.select(1), .width(4), .disabled("Z"), .enable("false")) multiplexer_2 (
    .in0(\秒_q0a ), .in1(4'b0000), .out(\秒0 ), .sel(Alarm));
  \六十进制计数器  \u_秒  (
    .CPU(and_5_out), .Clr(and_2_out), .CPD(1'b0), .Adj(1'b0), .Q1D(\秒_q1a [3]), .Q1C(\秒_q1a [2]),
    .Q1B(\秒_q1a [1]), .Q1A(\秒_q1a [0]), .Q0D(\秒_q0a [3]), .Q0C(\秒_q0a [2]), .Q0B(\秒_q0a [1]),
    .Q0A(\秒_q0a [0]), .nQcc(\秒_nqcc ));
  \电子钟整点报时电路  \u_电子钟整点报时电路_1  (.out_5(\定点报时 ), .\分1 (\分钟_q1a ), .\分0 (\分钟_q0a ), .\秒1 (\秒_q1a ), .\秒0 (\秒_q0a ));
  or or_1 (or_1_out, and_7_out, ~\秒_nqcc );  // OR_Gate
  and and_7 (and_7_out, and_1_out, and_9_out);
  and and_8 (and_8_out, and_9_out, and_4_out);
  and and_9 (and_9_out, and_6_out, ~Alarm, Adj1);  // AND_Gate
  Multiplexer #(.select(1), .width(4), .disabled("Z"), .enable("false")) multiplexer_3 (
    .in0(\分钟_q1a ), .in1(\闹钟_1_alarm分1 ), .out(\分1 ), .sel(Alarm));
  Multiplexer #(.select(1), .width(4), .disabled("Z"), .enable("false")) multiplexer_4 (
    .in0(\分钟_q0a ), .in1(\闹钟_1_alarm分0 ), .out(\分0 ), .sel(Alarm));
  \六十进制计数器  \u_分钟  (
    .CPU(or_1_out), .Clr(and_2_out), .CPD(and_8_out), .Adj(and_9_out), .Q1D(\分钟_q1a [3]), .Q1C(\分钟_q1a [2]),
    .Q1B(\分钟_q1a [1]), .Q1A(\分钟_q1a [0]), .Q0D(\分钟_q0a [3]), .Q0C(\分钟_q0a [2]), .Q0B(\分钟_q0a [1]),
    .Q0A(\分钟_q0a [0]), .nQcc(\分钟_nqcc ));
  and and_10 (and_10_out, CPu, Alarm);
  and and_11 (and_11_out, CPd, Alarm);
  and and_12 (and_12_out, Adj1, Alarm);
  \闹钟  \u_闹钟_1  (
    .\时1 (\小时_out_9 ), .\时0 (\小时_out_13 ), .\分1 (\分钟_q1a ), .\分0 (\分钟_q0a ), .\秒1 (\秒_q1a ), .\闹钟 (\闹钟 ),
    .Alarm(Alarm), .ctrl(ctrl), .Clr(and_3_out), .Adj1(and_12_out), .CPu(and_10_out), .CPd(and_11_out),
    .\Alarm分1 (\闹钟_1_alarm分1 ), .\Alarm分0 (\闹钟_1_alarm分0 ), .\Alarm时1 (\闹钟_1_alarm时1 ),
    .\Alarm时0 (\闹钟_1_alarm时0 ));
  and \u_分不向小时进位  (\分不向小时进位_out , ~\分钟_nqcc , ~and_9_out);  // AND_Gate
  and and_13 (and_13_out, and_1_out, and_14_out);
  and and_14 (and_14_out, and_6_out, ~Adj1);  // AND_Gate
  or or_2 (or_2_out, and_13_out, \分不向小时进位_out );
  and and_15 (and_15_out, and_14_out, and_4_out);
  \十二进制计数器或二十四进制的计数器电路  \u_小时  (
    .CPU(or_2_out), .Adj(and_14_out), .CPD(and_15_out), .out_6(\小时_out_9 [3]), .out_7(\小时_out_9 [2]),
    .out_8(\小时_out_9 [1]), .out_9(\小时_out_9 [0]), .out_10(\小时_out_13 [3]), .out_11(\小时_out_13 [2]),
    .out_12(\小时_out_13 [1]), .out_13(\小时_out_13 [0]), .Clr(and_2_out), .Set(1'b1));  // open: nQcc
  Multiplexer #(.select(1), .width(4), .disabled("Z"), .enable("false")) multiplexer_5 (
    .in0(\小时_out_9 ), .in1(\闹钟_1_alarm时1 ), .out(multiplexer_5_out), .sel(Alarm));
  Multiplexer #(.select(1), .width(4), .disabled("Z"), .enable("false")) multiplexer_6 (
    .in0(\小时_out_13 ), .in1(\闹钟_1_alarm时0 ), .out(multiplexer_6_out), .sel(Alarm));
  assign bit_extender_1_out = {{4{1'b0}}, multiplexer_5_out};  // Bit_Extender bit_extender_1
  Multiplier #(.width(8)) multiplier_1 (.a(8'ha), .b(bit_extender_1_out), .out(multiplier_1_out));  // open: cin, cout
  assign bit_extender_2_out = {{4{1'b0}}, multiplexer_6_out};  // Bit_Extender bit_extender_2
  Adder #(.width(8)) adder_1 (.a(multiplier_1_out), .b(bit_extender_2_out), .out(adder_1_out));  // open: cin, cout
  Comparator #(.width(8), .mode("unsigned")) comparator_1 (
    .a(adder_1_out), .b(8'hc), .gt(comparator_1_gt), .eq(comparator_1_eq));  // open: lt
  Subtractor #(.width(8)) subtractor_1 (.a(adder_1_out), .b(8'hc), .out(subtractor_1_out));  // open: bin, bout
  or _12 (_12_out, comparator_1_gt, comparator_1_eq);
  Multiplexer #(.select(1), .width(8), .disabled("Z"), .enable("false")) multiplexer_7 (
    .in0(adder_1_out), .in1(subtractor_1_out), .out(multiplexer_7_out), .sel(_12_out));
  Comparator #(.width(8), .mode("unsigned")) comparator_2 (
    .a(multiplexer_7_out), .b({8{1'b0}}), .eq(comparator_2_eq));  // open: gt, lt
  Multiplexer #(.select(1), .width(8), .disabled("Z"), .enable("false")) multiplexer_8 (
    .in0(adder_1_out), .in1(multiplexer_9_out), .out(multiplexer_8_out), .sel(not_1_out));
  Multiplexer #(.select(1), .width(8), .disabled("Z"), .enable("false")) multiplexer_9 (
    .in0(multiplexer_7_out), .in1(8'hc), .out(multiplexer_9_out), .sel(comparator_2_eq));
  Divider #(.width(8)) divider_1 (
    .a(multiplexer_8_out), .b(8'ha), .out({divider_1_out, \时1 }), .upper({8{1'b0}}),
    .rem({divider_1_rem, \时0 }));
  \上下午文字显示的电路  \u_上下午文字显示的电路_1  (
    .TT(not_1_out), .AM_FM(_12_out), .out_3(out_16), .out_4(out_17), .out_5(out_18), .out_6(out_19));
  not not_1 (not_1_out, Set_0_12_1_24);
endmodule

module \多功能数字钟测试电路  (
  input  in_1,
  input  in_2,
  input  in_3,
  input  in_4
);

  wire button_1_out, button_2_out, clock_1_out, \多功能数字钟_1_定点报时 , \多功能数字钟_1_闹钟 , \左_闹钟开关___右_闹钟值设置开关_p1 ,
       \左_闹钟开关___右_闹钟值设置开关_p2 ;
  wire [3:0] \多功能数字钟_1_分0 , \多功能数字钟_1_分1 , \多功能数字钟_1_时0 , \多功能数字钟_1_时1 , \多功能数字钟_1_秒0 , \多功能数字钟_1_秒1 ;
  wire [4:0] \多功能数字钟_1_out_16 , \多功能数字钟_1_out_17 , \多功能数字钟_1_out_18 , \多功能数字钟_1_out_19 ;

  DotMatrix #(.inputtype("column"), .matrixcols(4), .matrixrows(5), .persist(0), .dotshape("square")) dotmatrix_1 (
    .col0(\多功能数字钟_1_out_16 ), .col1(\多功能数字钟_1_out_17 ), .col2(\多功能数字钟_1_out_18 ), .col3(\多功能数字钟_1_out_19 ));
  Hex_Digit_Display hex_digit_display_1 (.value(\多功能数字钟_1_时1 ));  // open: dp
  \多功能数字钟  \u_多功能数字钟_1  (
    .out_16(\多功能数字钟_1_out_16 ), .out_17(\多功能数字钟_1_out_17 ), .out_18(\多功能数字钟_1_out_18 ),
    .out_19(\多功能数字钟_1_out_19 ), .\时1 (\多功能数字钟_1_时1 ), .\时0 (\多功能数字钟_1_时0 ), .\分1 (\多功能数字钟_1_分1 ),
    .\分0 (\多功能数字钟_1_分0 ), .\秒1 (\多功能数字钟_1_秒1 ), .CP(clock_1_out), .CPu(button_1_out), .CPd(button_2_out),
    .Set_0_12_1_24(in_3), .Clr(in_4), .\秒0 (\多功能数字钟_1_秒0 ), .Adj0(in_1), .Adj1(in_2),
    .\定点报时 (\多功能数字钟_1_定点报时 ), .\闹钟 (\多功能数字钟_1_闹钟 ), .ctrl(\左_闹钟开关___右_闹钟值设置开关_p1 ),
    .Alarm(\左_闹钟开关___右_闹钟值设置开关_p2 ));
  Clock #(.highDuration(1), .lowDuration(1)) clock_1 (.out(clock_1_out));
  Button button_1 (.out(button_1_out));
  Hex_Digit_Display hex_digit_display_2 (.value(\多功能数字钟_1_分1 ));  // open: dp
  Hex_Digit_Display hex_digit_display_3 (.value(\多功能数字钟_1_时0 ));  // open: dp
  Button button_2 (.out(button_2_out));
  Hex_Digit_Display hex_digit_display_4 (.value(\多功能数字钟_1_分0 ));  // open: dp
  Hex_Digit_Display hex_digit_display_5 (.value(\多功能数字钟_1_秒0 ));  // open: dp
  Hex_Digit_Display hex_digit_display_6 (.value(\多功能数字钟_1_秒1 ));  // open: dp
  // DipSwitch #(.NSwitches(2)) 左_闹钟开关___右_闹钟值设置开关: pin names not known; wires that end beside it: \左_闹钟开关___右_闹钟值设置开关_p1 , \左_闹钟开关___右_闹钟值设置开关_p2 
  LED #(.active("true")) led_1 (.in(\多功能数字钟_1_闹钟 ));
  LED #(.active("true")) led_2 (.in(\多功能数字钟_1_定点报时 ));

  // Notes on the sheet:
  //   闹钟开关打开（置1）：闹钟开启，正常报铃
  //   闹钟开关关闭（置0）：闹钟关闭，不会报铃
  //   闹钟值设置开关关闭（置0）：正常显示时间
  //   闹钟值设置开关打开（置1）：Adj1=0时，设置小时值；Adj1=1时，设置分钟值
endmodule

module \闹钟  (
  input  [3:0] \时1 ,
  input  [3:0] \时0 ,
  input  [3:0] \分1 ,
  input  ctrl,
  input  [3:0] \分0 ,
  input  [3:0] \秒1 ,
  input  Clr,
  input  CPu,
  input  CPd,
  input  Alarm,
  input  Adj1,
  output [3:0] \Alarm时1 ,
  output [3:0] \Alarm时0 ,
  output [3:0] \Alarm分1 ,
  output [3:0] \Alarm分0 ,
  output \闹钟 
);

  wire and_1_out, and_2_out, and_3_out, and_4_out, and_5_out, and_6_out, and_7_out, and_8_out, and_9_out,
       and_10_out, comparator_1_eq, comparator_2_eq, comparator_3_eq, comparator_4_eq, comparator_5_eq;

  and and_1 (and_1_out, CPu, Alarm);
  and and_2 (and_2_out, CPd, Alarm);
  and and_3 (and_3_out, and_5_out, and_2_out);
  and and_4 (and_4_out, and_1_out, and_5_out);
  and and_5 (and_5_out, Alarm, Adj1);
  \六十进制计数器  \u_分钟  (
    .CPU(and_4_out), .Clr(Clr), .CPD(and_3_out), .Adj(and_5_out), .Q1D(\Alarm分1 [3]), .Q1C(\Alarm分1 [2]),
    .Q1B(\Alarm分1 [1]), .Q1A(\Alarm分1 [0]), .Q0D(\Alarm分0 [3]), .Q0C(\Alarm分0 [2]), .Q0B(\Alarm分0 [1]),
    .Q0A(\Alarm分0 [0]));  // open: nQcc
  and and_6 (and_6_out, and_8_out, and_2_out);
  and and_7 (and_7_out, and_1_out, and_8_out);
  and and_8 (and_8_out, Alarm, ~Adj1);  // AND_Gate
  \十二进制计数器或二十四进制的计数器电路  \u_小时  (
    .CPU(and_7_out), .Adj(and_8_out), .CPD(and_6_out), .out_6(\Alarm时1 [3]), .out_7(\Alarm时1 [2]),
    .out_8(\Alarm时1 [1]), .out_9(\Alarm时1 [0]), .out_10(\Alarm时0 [3]), .out_11(\Alarm时0 [2]),
    .out_12(\Alarm时0 [1]), .out_13(\Alarm时0 [0]), .Clr(Clr), .Set(1'b1));  // open: nQcc
  Comparator #(.width(4), .mode("unsigned")) comparator_1 (
    .a(\时1 ), .b(\Alarm时1 ), .eq(comparator_1_eq));  // open: gt, lt
  Comparator #(.width(4), .mode("unsigned")) comparator_2 (
    .a(\时0 ), .b(\Alarm时0 ), .eq(comparator_2_eq));  // open: gt, lt
  Comparator #(.width(4), .mode("unsigned")) comparator_3 (
    .a(\分1 ), .b(\Alarm分1 ), .eq(comparator_3_eq));  // open: gt, lt
  Comparator #(.width(4), .mode("unsigned")) comparator_4 (
    .a(\分0 ), .b(\Alarm分0 ), .eq(comparator_4_eq));  // open: gt, lt
  Comparator #(.width(4), .mode("unsigned")) comparator_5 (
    .a(\秒1 ), .b(4'b0000), .eq(comparator_5_eq));  // open: gt, lt
  and and_9 (and_9_out, comparator_1_eq, comparator_2_eq, comparator_3_eq, comparator_4_eq);
  and and_10 (and_10_out, and_9_out, comparator_5_eq);
  and and_11 (\闹钟 , and_10_out, ctrl);
endmodule

module \闹钟测试  (
  input  in_1,
  input  in_2,
  input  in_3,
  input  in_4
);

  wire button_1_out, button_2_out, clock_1_out, \多功能数字钟_1_定点报时 , \多功能数字钟_1_闹钟 , \左_闹钟开关___右_闹钟值设置开关_p1 ,
       \左_闹钟开关___右_闹钟值设置开关_p2 ;
  wire [3:0] \多功能数字钟_1_分0 , \多功能数字钟_1_分1 , \多功能数字钟_1_时0 , \多功能数字钟_1_时1 , \多功能数字钟_1_秒0 , \多功能数字钟_1_秒1 ;
  wire [4:0] \多功能数字钟_1_out_16 , \多功能数字钟_1_out_17 , \多功能数字钟_1_out_18 , \多功能数字钟_1_out_19 ;

  DotMatrix #(.inputtype("column"), .matrixcols(4), .matrixrows(5), .persist(0), .dotshape("square")) dotmatrix_1 (
    .col0(\多功能数字钟_1_out_16 ), .col1(\多功能数字钟_1_out_17 ), .col2(\多功能数字钟_1_out_18 ), .col3(\多功能数字钟_1_out_19 ));
  Hex_Digit_Display hex_digit_display_1 (.value(\多功能数字钟_1_时1 ));  // open: dp
  \多功能数字钟  \u_多功能数字钟_1  (
    .out_16(\多功能数字钟_1_out_16 ), .out_17(\多功能数字钟_1_out_17 ), .out_18(\多功能数字钟_1_out_18 ),
    .out_19(\多功能数字钟_1_out_19 ), .\时1 (\多功能数字钟_1_时1 ), .\时0 (\多功能数字钟_1_时0 ), .\分1 (\多功能数字钟_1_分1 ),
    .\分0 (\多功能数字钟_1_分0 ), .\秒1 (\多功能数字钟_1_秒1 ), .CP(clock_1_out), .CPu(button_1_out), .CPd(button_2_out),
    .Set_0_12_1_24(in_3), .Clr(in_4), .\秒0 (\多功能数字钟_1_秒0 ), .Adj0(in_1), .Adj1(in_2),
    .\定点报时 (\多功能数字钟_1_定点报时 ), .\闹钟 (\多功能数字钟_1_闹钟 ), .ctrl(\左_闹钟开关___右_闹钟值设置开关_p1 ),
    .Alarm(\左_闹钟开关___右_闹钟值设置开关_p2 ));
  Clock #(.highDuration(1), .lowDuration(1)) clock_1 (.out(clock_1_out));
  Button button_1 (.out(button_1_out));
  Hex_Digit_Display hex_digit_display_2 (.value(\多功能数字钟_1_分1 ));  // open: dp
  Hex_Digit_Display hex_digit_display_3 (.value(\多功能数字钟_1_时0 ));  // open: dp
  Button button_2 (.out(button_2_out));
  Hex_Digit_Display hex_digit_display_4 (.value(\多功能数字钟_1_分0 ));  // open: dp
  Hex_Digit_Display hex_digit_display_5 (.value(\多功能数字钟_1_秒0 ));  // open: dp
  Hex_Digit_Display hex_digit_display_6 (.value(\多功能数字钟_1_秒1 ));  // open: dp
  // DipSwitch #(.NSwitches(2)) 左_闹钟开关___右_闹钟值设置开关: pin names not known; wires that end beside it: \左_闹钟开关___右_闹钟值设置开关_p1 , \左_闹钟开关___右_闹钟值设置开关_p2 
  LED #(.active("true")) led_1 (.in(\多功能数字钟_1_闹钟 ));
  LED #(.active("true")) led_2 (.in(\多功能数字钟_1_定点报时 ));

  // Notes on the sheet:
  //   闹钟测试电路和多功能数字钟测试电路相同
  //   闹钟开关打开（置1）：闹钟开启，正常报铃
  //   闹钟开关关闭（置0）：闹钟关闭，不会报铃
  //   闹钟值设置开关关闭（置0）：正常显示时间
  //   闹钟值设置开关打开（置1）：Adj1=0时，设置小时值；Adj1=1时，设置分钟值
endmodule
