// Logisim project 实验5-校交1801-U201816030-车春池.circ as structural Verilog
module \四位二进制可逆计数器  (
  input  D,
  input  C,
  input  B,
  input  A,
  input  CPU,
  input  CPD,
  input  CLR,
  input  LD,
  output QD,
  output QC,
  output QB,
  output QA
);

  wire and_1_out, and_2_out, and_3_out, and_4_out, and_5_out, and_6_out, d_ff_1_qn, d_ff_2_qn, d_ff_3_qn,
       d_ff_4_qn, multiplexer_1_out, multiplexer_2_out, multiplexer_3_out, multiplexer_4_out,
       multiplexer_5_out, multiplexer_6_out, multiplexer_7_out, multiplexer_8_out, not_1_out, not_2_out,
       not_3_out, not_4_out, not_5_out, or_1_out, or_2_out, or_3_out, or_4_out, or_5_out, or_6_out, or_7_out,
       or_8_out;

  not not_1 (not_1_out, LD);
  or or_1 (or_1_out, CPU, CPD);
  and and_1 (and_1_out, CPD, d_ff_4_qn, d_ff_3_qn, d_ff_2_qn);
  and and_2 (and_2_out, CPU, QA, QB, QC);
  and and_3 (and_3_out, CPD, d_ff_4_qn, d_ff_3_qn);
  and and_4 (and_4_out, CPU, QA, QB);
  and and_5 (and_5_out, CPD, d_ff_4_qn);
  and and_6 (and_6_out, CPU, QA);
  or or_2 (or_2_out, and_1_out, and_2_out);
  or or_3 (or_3_out, and_3_out, and_4_out);
  or or_4 (or_4_out, and_5_out, and_6_out);
  Multiplexer multiplexer_1 (.in0(1'b0), .in1(B), .out(multiplexer_1_out), .sel(not_1_out));  // open: en
  D_Flip_Flop #(.trigger("falling")) d_ff_1 (
    .clk(or_2_out), .D(d_ff_1_qn), .Q(QD), .Qn(d_ff_1_qn), .preset(multiplexer_2_out), .en(1'b1),
    .reset(or_5_out));
  Multiplexer multiplexer_2 (.in0(1'b0), .in1(D), .out(multiplexer_2_out), .sel(not_1_out));  // open: en
  D_Flip_Flop #(.trigger("falling")) d_ff_2 (
    .clk(or_3_out), .D(d_ff_2_qn), .Q(QC), .Qn(d_ff_2_qn), .preset(multiplexer_3_out), .en(1'b1),
    .reset(or_6_out));
  Multiplexer multiplexer_3 (.in0(1'b0), .in1(C), .out(multiplexer_3_out), .sel(not_1_out));  // open: en
  D_Flip_Flop #(.trigger("falling")) d_ff_3 (
    .clk(or_4_out), .D(d_ff_3_qn), .Q(QB), .Qn(d_ff_3_qn), .preset(multiplexer_1_out), .en(1'b1),
    .reset(or_7_out));
  D_Flip_Flop #(.trigger("falling")) d_ff_4 (
    .clk(or_1_out), .D(d_ff_4_qn), .Q(QA), .Qn(d_ff_4_qn), .preset(multiplexer_4_out), .en(1'b1),
    .reset(or_8_out));
  Multiplexer multiplexer_4 (.in0(1'b0), .in1(A), .out(multiplexer_4_out), .sel(not_1_out));  // open: en
  Multiplexer multiplexer_5 (.in0(1'b0), .in1(not_2_out), .out(multiplexer_5_out), .sel(not_1_out));  // open: en
  not not_2 (not_2_out, D);
  Multiplexer multiplexer_6 (.in0(1'b0), .in1(not_3_out), .out(multiplexer_6_out), .sel(not_1_out));  // open: en
  not not_3 (not_3_out, B);
  Multiplexer multiplexer_7 (.in0(1'b0), .in1(not_4_out), .out(multiplexer_7_out), .sel(not_1_out));  // open: en
  not not_4 (not_4_out, A);
  or or_5 (or_5_out, CLR, multiplexer_5_out);
  or or_6 (or_6_out, CLR, multiplexer_8_out);
  Multiplexer multiplexer_8 (.in0(1'b0), .in1(not_5_out), .out(multiplexer_8_out), .sel(not_1_out));  // open: en
  not not_5 (not_5_out, C);
  or or_7 (or_7_out, CLR, multiplexer_6_out);
  or or_8 (or_8_out, CLR, multiplexer_7_out);
endmodule

module \四位二进制可逆计数器测试电路  (
  input  D,
  input  C,
  input  B,
  input  A,
  input  CPD,
  input  CPU,
  input  CLR,
  input  LD,
  output QD,
  output QC,
  output QB,
  output QA
);

  \四位二进制可逆计数器  \u_四位二进制可逆计数器_1  (
    .CPD(CPD), .D(D), .QD(QD), .C(C), .QC(QC), .B(B), .QB(QB), .A(A), .QA(QA), .CPU(CPU), .CLR(CLR), .LD(LD));
endmodule

module \二进制转8421码电路  (
  input  A0,
  input  A1,
  input  A2,
  input  A3,
  output S1,
  output S2,
  output S4,
  output S8,
  output S10,
  output S20,
  output S40,
  output S80
);

  wire and_1_out, or_1_out;

  or or_1 (or_1_out, A1, A2);
  and and_1 (and_1_out, or_1_out, A3);
  \先行进位并行加法器  \u_先行进位并行加法器_1  (
    .A0(A0), .A1(A1), .A2(A2), .A3(A3), .B0(1'b0), .B1(and_1_out), .B2(and_1_out), .B3(1'b0), .C0(1'b0),
    .S0(S1), .S1(S2), .S2(S4), .S3(S8), .C4(S10));

  assign S20 = 1'b0;
  assign S40 = 1'b0;
  assign S80 = 1'b0;
endmodule

module \二进制转8421码测试电路  (
  input  A0,
  input  A1,
  input  A2,
  input  A3,
  output S1,
  output S2,
  output S4,
  output S8,
  output S10,
  output S20,
  output S40,
  output S80
);

  \二进制转8421码电路  \u_二进制转8421码电路_1  (
    .A0(A0), .A1(A1), .A2(A2), .A3(A3), .S1(S1), .S2(S2), .S4(S4), .S8(S8), .S10(S10), .S20(S20), .S40(S40),
    .S80(S80));
endmodule

module \显示电路  (
  input  A0,
  input  A1,
  input  A2,
  input  A3,
  output al,
  output bl,
  output cl,
  output dl,
  output el,
  output fl,
  output gl,
  output ah,
  output bh,
  output ch,
  output dh,
  output eh,
  output fh,
  output gh
);

  wire \二进制转8421码电路_1_s1 , \二进制转8421码电路_1_s2 , \二进制转8421码电路_1_s4 , \二进制转8421码电路_1_s8 , \二进制转8421码电路_1_s10 ,
       \二进制转8421码电路_1_s20 , \二进制转8421码电路_1_s40 , \二进制转8421码电路_1_s80 ;

  \二进制转8421码电路  \u_二进制转8421码电路_1  (
    .A0(A0), .A1(A1), .A2(A2), .A3(A3), .S1(\二进制转8421码电路_1_s1 ), .S2(\二进制转8421码电路_1_s2 ),
    .S4(\二进制转8421码电路_1_s4 ), .S8(\二进制转8421码电路_1_s8 ), .S10(\二进制转8421码电路_1_s10 ), .S20(\二进制转8421码电路_1_s20 ),
    .S40(\二进制转8421码电路_1_s40 ), .S80(\二进制转8421码电路_1_s80 ));
  \七段译码器  \u_七段译码器_1  (
    .A3(\二进制转8421码电路_1_s8 ), .A2(\二进制转8421码电路_1_s4 ), .A1(\二进制转8421码电路_1_s2 ), .A0(\二进制转8421码电路_1_s1 ),
    .a(al), .b(bl), .c(cl), .d(dl), .e(el), .f(fl), .g(gl));
  \七段译码器  \u_七段译码器_2  (
    .A3(\二进制转8421码电路_1_s80 ), .A2(\二进制转8421码电路_1_s40 ), .A1(\二进制转8421码电路_1_s20 ), .A0(\二进制转8421码电路_1_s10 ),
    .a(ah), .b(bh), .c(ch), .d(dh), .e(eh), .f(fh), .g(gh));
endmodule

module \显示电路测试电路  (
  input  A0,
  input  A1,
  input  A2,
  input  A3
);

  wire \显示电路_1_ah , \显示电路_1_al , \显示电路_1_bh , \显示电路_1_bl , \显示电路_1_ch , \显示电路_1_cl , \显示电路_1_dh ,
       \显示电路_1_dl , \显示电路_1_eh , \显示电路_1_el , \显示电路_1_fh , \显示电路_1_fl , \显示电路_1_gh , \显示电路_1_gl ;

  \显示电路  \u_显示电路_1  (
    .A0(A0), .A1(A1), .A2(A2), .A3(A3), .al(\显示电路_1_al ), .bl(\显示电路_1_bl ), .cl(\显示电路_1_cl ),
    .dl(\显示电路_1_dl ), .el(\显示电路_1_el ), .fl(\显示电路_1_fl ), .gl(\显示电路_1_gl ), .ah(\显示电路_1_ah ),
    .bh(\显示电路_1_bh ), .ch(\显示电路_1_ch ), .dh(\显示电路_1_dh ), .eh(\显示电路_1_eh ), .fh(\显示电路_1_fh ), .gh(\显示电路_1_gh ));
  _7_Segment_Display u_7_segment_display_1 (
    .g(\显示电路_1_gl ), .f(\显示电路_1_fl ), .a(\显示电路_1_al ), .b(\显示电路_1_bl ), .e(\显示电路_1_el ), .d(\显示电路_1_dl ),
    .c(\显示电路_1_cl ));  // open: dp
  _7_Segment_Display u_7_segment_display_2 (
    .g(\显示电路_1_gh ), .f(\显示电路_1_fh ), .a(\显示电路_1_ah ), .b(\显示电路_1_bh ), .e(\显示电路_1_eh ), .d(\显示电路_1_dh ),
    .c(\显示电路_1_ch ));  // open: dp
endmodule

module \报警电路  (
  input  D,
  input  C,
  input  B,
  input  A,
  input  D_2,
  input  U,
  input  CLR,
  input  LD,
  output QD,
  output QC,
  output QB,
  output QA
);

  wire and_1_out, and_2_out, not_1_out, \报警信号_out , \无人信号_out , \满员信号_out ;

  and and_1 (and_1_out, \无人信号_out , D_2);
  and and_2 (and_2_out, not_1_out, U);
  \四位二进制可逆计数器  \u_四位二进制可逆计数器_1  (
    .CPD(and_1_out), .D(D), .QD(QD), .C(C), .QC(QC), .B(B), .QB(QB), .A(A), .QA(QA), .CPU(and_2_out),
    .CLR(CLR), .LD(LD));
  or \u_无人信号  (\无人信号_out , QA, QB, QC, QD);
  not not_1 (not_1_out, \满员信号_out );
  and \u_满员信号  (\满员信号_out , QA, QB, QC, QD);
  LED Alarm (.in(\报警信号_out ));
  and \u_报警信号  (\报警信号_out , \满员信号_out , U);
endmodule

module \小型实验室门禁系统  (
  input  D,
  input  U,
  input  CLR,
  output al,
  output bl,
  output cl,
  output dl,
  output el,
  output fl,
  output gl,
  output ah,
  output bh,
  output ch,
  output dh,
  output eh,
  output fh,
  output gh,
  output Z
);

  wire and_1_out, and_2_out, not_1_out, \二进制转8421码电路_1_s1 , \二进制转8421码电路_1_s2 , \二进制转8421码电路_1_s4 ,
       \二进制转8421码电路_1_s8 , \二进制转8421码电路_1_s10 , \二进制转8421码电路_1_s20 , \二进制转8421码电路_1_s40 ,
       \二进制转8421码电路_1_s80 , \四位二进制可逆计数器_1_qa , \四位二进制可逆计数器_1_qb , \四位二进制可逆计数器_1_qc , \四位二进制可逆计数器_1_qd ,
       \无人信号_out , \满员信号_out ;

  and and_1 (and_1_out, \无人信号_out , D);
  and and_2 (and_2_out, not_1_out, U);
  \四位二进制可逆计数器  \u_四位二进制可逆计数器_1  (
    .CPD(and_1_out), .D(1'b0), .QD(\四位二进制可逆计数器_1_qd ), .C(1'b0), .QC(\四位二进制可逆计数器_1_qc ), .B(1'b0),
    .QB(\四位二进制可逆计数器_1_qb ), .A(1'b0), .QA(\四位二进制可逆计数器_1_qa ), .CPU(and_2_out), .CLR(CLR), .LD(1'b1));
  or \u_无人信号  (\无人信号_out , \四位二进制可逆计数器_1_qa , \四位二进制可逆计数器_1_qb , \四位二进制可逆计数器_1_qc , \四位二进制可逆计数器_1_qd );
  and \u_满员信号  (\满员信号_out , \四位二进制可逆计数器_1_qa , \四位二进制可逆计数器_1_qb , \四位二进制可逆计数器_1_qc , \四位二进制可逆计数器_1_qd );
  not not_1 (not_1_out, \满员信号_out );
  and \u_报警信号  (Z, \满员信号_out , U);
  \二进制转8421码电路  \u_二进制转8421码电路_1  (
    .A0(\四位二进制可逆计数器_1_qa ), .A1(\四位二进制可逆计数器_1_qb ), .A2(\四位二进制可逆计数器_1_qc ), .A3(\四位二进制可逆计数器_1_qd ),
    .S1(\二进制转8421码电路_1_s1 ), .S2(\二进制转8421码电路_1_s2 ), .S4(\二进制转8421码电路_1_s4 ), .S8(\二进制转8421码电路_1_s8 ),
    .S10(\二进制转8421码电路_1_s10 ), .S20(\二进制转8421码电路_1_s20 ), .S40(\二进制转8421码电路_1_s40 ), .S80(\二进制转8421码电路_1_s80 ));
  \七段译码器  \u_七段译码器_1  (
    .A3(\二进制转8421码电路_1_s8 ), .A2(\二进制转8421码电路_1_s4 ), .A1(\二进制转8421码电路_1_s2 ), .A0(\二进制转8421码电路_1_s1 ),
    .a(al), .b(bl), .c(cl), .d(dl), .e(el), .f(fl), .g(gl));
  \七段译码器  \u_七段译码器_2  (
    .A3(\二进制转8421码电路_1_s80 ), .A2(\二进制转8421码电路_1_s40 ), .A1(\二进制转8421码电路_1_s20 ), .A0(\二进制转8421码电路_1_s10 ),
    .a(ah), .b(bh), .c(ch), .d(dh), .e(eh), .f(fh), .g(gh));
endmodule

module \小型门禁系统测试电路  (
  input  in_1,
  input  in_2,
  input  in_3
);

  wire \小型实验室门禁系统_1_ah , \小型实验室门禁系统_1_al , \小型实验室门禁系统_1_bh , \小型实验室门禁系统_1_bl , \小型实验室门禁系统_1_ch ,
       \小型实验室门禁系统_1_cl , \小型实验室门禁系统_1_dh , \小型实验室门禁系统_1_dl , \小型实验室门禁系统_1_eh , \小型实验室门禁系统_1_el ,
       \小型实验室门禁系统_1_fh , \小型实验室门禁系统_1_fl , \小型实验室门禁系统_1_gh , \小型实验室门禁系统_1_gl , \小型实验室门禁系统_1_z ;

  _7_Segment_Display u_7_segment_display_1 (
    .g(\小型实验室门禁系统_1_gh ), .f(\小型实验室门禁系统_1_fh ), .a(\小型实验室门禁系统_1_ah ), .b(\小型实验室门禁系统_1_bh ),
    .e(\小型实验室门禁系统_1_eh ), .d(\小型实验室门禁系统_1_dh ), .c(\小型实验室门禁系统_1_ch ));  // open: dp
  _7_Segment_Display u_7_segment_display_2 (
    .g(\小型实验室门禁系统_1_gl ), .f(\小型实验室门禁系统_1_fl ), .a(\小型实验室门禁系统_1_al ), .b(\小型实验室门禁系统_1_bl ),
    .e(\小型实验室门禁系统_1_el ), .d(\小型实验室门禁系统_1_dl ), .c(\小型实验室门禁系统_1_cl ));  // open: dp
  \小型实验室门禁系统  \u_小型实验室门禁系统_1  (
    .D(in_3), .U(in_1), .CLR(in_2), .al(\小型实验室门禁系统_1_al ), .bl(\小型实验室门禁系统_1_bl ), .cl(\小型实验室门禁系统_1_cl ),
    .dl(\小型实验室门禁系统_1_dl ), .el(\小型实验室门禁系统_1_el ), .fl(\小型实验室门禁系统_1_fl ), .gl(\小型实验室门禁系统_1_gl ),
    .ah(\小型实验室门禁系统_1_ah ), .bh(\小型实验室门禁系统_1_bh ), .ch(\小型实验室门禁系统_1_ch ), .dh(\小型实验室门禁系统_1_dh ),
    .eh(\小型实验室门禁系统_1_eh ), .fh(\小型实验室门禁系统_1_fh ), .gh(\小型实验室门禁系统_1_gh ), .Z(\小型实验室门禁系统_1_z ));
  LED led_1 (.in(\小型实验室门禁系统_1_z ));
endmodule

module Mux2_1 (
  input  D0,
  input  S,
  input  D1,
  output Y
);

  wire and_1_out, and_2_out, not_1_out;

  not not_1 (not_1_out, S);
  and and_1 (and_1_out, D0, not_1_out);
  and and_2 (and_2_out, S, D1);
  or or_1 (Y, and_1_out, and_2_out);
endmodule

module \七段译码器  (
  input  A3,
  input  A2,
  input  A1,
  input  A0,
  output a,
  output b,
  output c,
  output d,
  output e,
  output f,
  output g
);

  wire and_1_out, and_2_out, and_3_out, and_4_out, and_5_out, and_6_out, and_7_out, and_8_out, and_9_out,
       and_10_out, and_11_out, and_12_out, and_13_out, and_14_out, and_15_out, and_16_out, and_17_out,
       and_18_out, and_19_out, and_20_out, and_21_out, and_22_out, and_23_out, and_24_out, and_25_out,
       and_26_out, not_1_out, not_2_out, not_3_out, not_4_out, not_5_out, not_6_out, not_7_out, not_8_out,
       not_9_out, not_10_out, not_11_out, not_12_out, not_13_out, not_14_out, not_15_out, not_16_out,
       not_17_out, not_18_out, not_19_out, not_20_out, not_21_out, not_22_out, not_23_out, not_24_out,
       not_25_out, not_26_out, not_27_out, not_28_out, not_29_out, not_30_out, not_31_out, not_32_out,
       not_33_out, not_34_out, not_35_out, not_36_out, not_37_out;

  not not_1 (not_1_out, A3);
  not not_2 (not_2_out, A2);
  and and_1 (and_1_out, not_1_out, not_2_out, not_3_out);
  not not_3 (not_3_out, A0);
  not not_4 (not_4_out, A3);
  and and_2 (and_2_out, not_4_out, not_5_out, A1);
  not not_5 (not_5_out, A2);
  not not_6 (not_6_out, A3);
  and and_3 (and_3_out, not_6_out, A2, A0);
  not not_7 (not_7_out, A2);
  and and_4 (and_4_out, A3, not_7_out, not_8_out);
  not not_8 (not_8_out, A1);
  and and_5 (and_5_out, A3, not_9_out, A0);
  not not_9 (not_9_out, A1);
  not not_10 (not_10_out, A3);
  and and_6 (and_6_out, not_10_out, not_11_out);
  not not_11 (not_11_out, A2);
  not not_12 (not_12_out, A2);
  and and_7 (and_7_out, not_12_out, not_13_out);
  not not_13 (not_13_out, A1);
  not not_14 (not_14_out, A1);
  and and_8 (and_8_out, not_14_out, not_15_out);
  not not_15 (not_15_out, A0);
  not not_16 (not_16_out, A3);
  and and_9 (and_9_out, not_16_out, A1, A0);
  not not_17 (not_17_out, A2);
  and and_10 (and_10_out, not_17_out, not_18_out);
  not not_18 (not_18_out, A1);
  not not_19 (not_19_out, A2);
  and and_11 (and_11_out, not_19_out, A0);
  not not_20 (not_20_out, A3);
  and and_12 (and_12_out, not_20_out, A2);
  not not_21 (not_21_out, A2);
  and and_13 (and_13_out, not_21_out, not_22_out);
  not not_22 (not_22_out, A0);
  not not_23 (not_23_out, A2);
  and and_14 (and_14_out, not_23_out, A1);
  and and_15 (and_15_out, A1, not_24_out);
  not not_24 (not_24_out, A0);
  not not_25 (not_25_out, A1);
  and and_16 (and_16_out, A2, not_25_out, A0);
  not not_26 (not_26_out, A2);
  and and_17 (and_17_out, not_26_out, not_27_out);
  not not_27 (not_27_out, A0);
  and and_18 (and_18_out, A1, not_28_out);
  not not_28 (not_28_out, A0);
  not not_29 (not_29_out, A1);
  and and_19 (and_19_out, not_29_out, not_30_out);
  not not_30 (not_30_out, A0);
  and and_20 (and_20_out, A2, not_31_out);
  not not_31 (not_31_out, A1);
  and and_21 (and_21_out, A2, not_32_out);
  not not_32 (not_32_out, A0);
  and and_22 (and_22_out, A3, not_33_out);
  not not_33 (not_33_out, A1);
  not not_34 (not_34_out, A1);
  and and_23 (and_23_out, not_34_out, A2);
  and and_24 (and_24_out, A1, not_35_out);
  not not_35 (not_35_out, A2);
  and and_25 (and_25_out, A1, not_36_out);
  not not_36 (not_36_out, A0);
  and and_26 (and_26_out, A3, not_37_out);
  not not_37 (not_37_out, A1);
  or or_1 (a, and_1_out, and_2_out, and_3_out, and_4_out, and_5_out);
  or or_2 (b, and_6_out, and_7_out, and_8_out, and_9_out);
  or or_3 (c, and_10_out, and_11_out, and_12_out);
  or or_4 (d, and_13_out, and_14_out, and_15_out, and_16_out);
  or or_5 (e, and_17_out, and_18_out);
  or or_6 (f, and_19_out, and_20_out, and_21_out, and_22_out);
  or or_7 (g, and_23_out, and_24_out, and_25_out, and_26_out);
endmodule

module \_60进制计数器  (
  input  CPU,
  input  CPD,
  input  ADJ,
  input  CLR,
  output out_5,
  output out_6,
  output out_7,
  output out_8,
  output out_9,
  output out_10,
  output out_11,
  output out_12,
  output Qcc
);

  wire and_1_out, and_2_out, and_3_out, and_4_out, and_5_out, and_6_out, and_7_out, and_8_out, and_9_out,
       and_10_out, not_1_out, not_2_out, not_3_out, not_4_out, not_5_out, not_6_out, not_7_out, not_8_out,
       not_9_out, not_10_out, not_11_out, not_12_out, or_1_out;
  wire [7:0] \四位二进制可逆计数器_2_qa ;
  wire [7:4] divider_1_out, divider_1_rem;

  and and_1 (and_1_out, CPD, ADJ);
  or or_1 (or_1_out, CLR, and_10_out);
  and and_2 (and_2_out, and_7_out, ~and_3_out);  // AND_Gate
  and and_3 (and_3_out, not_12_out, and_7_out);
  not not_1 (not_1_out, and_2_out);
  and and_4 (and_4_out, and_8_out, CPU);
  and and_5 (and_5_out, not_12_out, and_1_out, and_7_out);
  and and_6 (and_6_out, and_1_out, not_1_out);
  and and_7 (and_7_out, not_7_out, not_5_out, not_6_out, not_3_out);
  not not_2 (not_2_out, 1'b1);
  not not_3 (not_3_out, \四位二进制可逆计数器_2_qa [0]);
  not not_4 (not_4_out, 1'b1);
  \四位二进制可逆计数器  \u_四位二进制可逆计数器_1  (
    .CPD(and_5_out), .D(not_2_out), .QD(\四位二进制可逆计数器_2_qa [7]), .C(not_2_out), .QC(\四位二进制可逆计数器_2_qa [6]),
    .B(not_2_out), .QB(\四位二进制可逆计数器_2_qa [5]), .A(not_2_out), .QA(\四位二进制可逆计数器_2_qa [4]), .CPU(and_4_out),
    .CLR(or_1_out), .LD(1'b1));
  not not_5 (not_5_out, \四位二进制可逆计数器_2_qa [2]);
  not not_6 (not_6_out, \四位二进制可逆计数器_2_qa [1]);
  \四位二进制可逆计数器  \u_四位二进制可逆计数器_2  (
    .CPD(and_6_out), .D(not_4_out), .QD(\四位二进制可逆计数器_2_qa [3]), .C(not_4_out), .QC(\四位二进制可逆计数器_2_qa [2]),
    .B(not_4_out), .QB(\四位二进制可逆计数器_2_qa [1]), .A(not_4_out), .QA(\四位二进制可逆计数器_2_qa [0]), .CPU(CPU),
    .CLR(or_1_out), .LD(1'b1));
  not not_7 (not_7_out, \四位二进制可逆计数器_2_qa [3]);
  not not_8 (not_8_out, \四位二进制可逆计数器_2_qa [4]);
  not not_9 (not_9_out, \四位二进制可逆计数器_2_qa [7]);
  not not_10 (not_10_out, \四位二进制可逆计数器_2_qa [6]);
  not not_11 (not_11_out, \四位二进制可逆计数器_2_qa [5]);
  and and_8 (and_8_out, \四位二进制可逆计数器_2_qa [3], \四位二进制可逆计数器_2_qa [2], \四位二进制可逆计数器_2_qa [1], \四位二进制可逆计数器_2_qa [0]);
  and and_9 (and_9_out, not_8_out, not_9_out, not_10_out, not_11_out);
  not not_12 (not_12_out, and_9_out);
  and and_10 (and_10_out, \四位二进制可逆计数器_2_qa [4], \四位二进制可逆计数器_2_qa [5], \四位二进制可逆计数器_2_qa [2], \四位二进制可逆计数器_2_qa [3]);
  not not_13 (Qcc, and_10_out);
  Divider divider_1 (
    .a(\四位二进制可逆计数器_2_qa ), .b(8'ha), .out({divider_1_out, out_5, out_6, out_7, out_8}), .upper({8{1'b0}}),
    .rem({divider_1_rem, out_9, out_10, out_11, out_12}));
endmodule

module \_60进制计数器测试电路  (
  input  in_1,
  input  in_2,
  output out_3
);

  wire button_1_out, button_2_out;
  wire [3:0] \n60进制计数器_1_out_8 , \n60进制计数器_1_out_12 ;

  Button button_1 (.out(button_1_out));
  Button button_2 (.out(button_2_out));
  Hex_Digit_Display hex_digit_display_1 (.value(\n60进制计数器_1_out_8 ));  // open: dp
  \_60进制计数器  \u_60进制计数器_1  (
    .CPU(button_1_out), .CPD(button_2_out), .ADJ(in_1), .CLR(in_2), .out_5(\n60进制计数器_1_out_8 [3]),
    .out_6(\n60进制计数器_1_out_8 [2]), .out_7(\n60进制计数器_1_out_8 [1]), .out_8(\n60进制计数器_1_out_8 [0]),
    .out_9(\n60进制计数器_1_out_12 [3]), .out_10(\n60进制计数器_1_out_12 [2]), .out_11(\n60进制计数器_1_out_12 [1]),
    .out_12(\n60进制计数器_1_out_12 [0]), .Qcc(out_3));
  Hex_Digit_Display hex_digit_display_2 (.value(\n60进制计数器_1_out_12 ));  // open: dp
endmodule

module \十二进制计数器或二十四进制的计数器电路  (
  input  CPU,
  input  CPD,
  input  Adj,
  input  CLR,
  input  SET,
  output _1d,
  output _1c,
  output _1b,
  output _1a,
  output _0d,
  output _0c,
  output _0b,
  output _0a,
  output nQcc
);

  wire and_1_out, and_2_out, and_3_out, not_1_out, or_1_out, or_2_out;
  wire [7:0] \n60进制计数器_1_out_12 ;

  \_60进制计数器  \u_60进制计数器_1  (
    .CPU(CPU), .CPD(CPD), .ADJ(Adj), .CLR(or_2_out), .out_5(\n60进制计数器_1_out_12 [7]),
    .out_6(\n60进制计数器_1_out_12 [6]), .out_7(\n60进制计数器_1_out_12 [5]), .out_8(\n60进制计数器_1_out_12 [4]),
    .out_9(\n60进制计数器_1_out_12 [3]), .out_10(\n60进制计数器_1_out_12 [2]), .out_11(\n60进制计数器_1_out_12 [1]),
    .out_12(\n60进制计数器_1_out_12 [0]));  // open: Qcc
  and and_1 (and_1_out, ~SET, ~\n60进制计数器_1_out_12 [0], ~\n60进制计数器_1_out_12 [1], ~\n60进制计数器_1_out_12 [2], ~\n60进制计数器_1_out_12 [3], ~\n60进制计数器_1_out_12 [4], ~\n60进制计数器_1_out_12 [5], ~\n60进制计数器_1_out_12 [6], ~\n60进制计数器_1_out_12 [7]);  // AND_Gate
  Multiplexer #(.width(8)) multiplexer_1 (
    .in0(\n60进制计数器_1_out_12 ), .in1(8'h12), .out({_1d, _1c, _1b, _1a, _0d, _0c, _0b, _0a}), .sel(and_1_out));  // open: en
  and and_2 (and_2_out, ~\n60进制计数器_1_out_12 [0], ~\n60进制计数器_1_out_12 [1], ~\n60进制计数器_1_out_12 [4], ~\n60进制计数器_1_out_12 [3], \n60进制计数器_1_out_12 [5], \n60进制计数器_1_out_12 [2]);  // AND_Gate
  and and_3 (and_3_out, \n60进制计数器_1_out_12 [4], \n60进制计数器_1_out_12 [1]);
  not not_1 (not_1_out, or_1_out);
  or or_1 (or_1_out, \n60进制计数器_1_out_12 [0], ~and_3_out);  // OR_Gate
  Multiplexer multiplexer_2 (.in0(not_1_out), .in1(and_2_out), .out(nQcc), .sel(SET));  // open: en
  or or_2 (or_2_out, nQcc, CLR);
endmodule

module \十二进制计数器或二十四进制的计数器电路测试电路  (
  input  in_1,
  input  in_2,
  input  in_3,
  output out_4
);

  wire button_1_out, button_2_out;
  wire [3:0] \十二进制计数器或二十四进制的计数器电路_1__0a , \十二进制计数器或二十四进制的计数器电路_1__1a ;

  Button button_1 (.out(button_1_out));
  Button button_2 (.out(button_2_out));
  Hex_Digit_Display hex_digit_display_1 (.value(\十二进制计数器或二十四进制的计数器电路_1__1a ));  // open: dp
  \十二进制计数器或二十四进制的计数器电路  \u_十二进制计数器或二十四进制的计数器电路_1  (
    .CPU(button_1_out), .CPD(button_2_out), .Adj(in_1), .CLR(in_3), .SET(in_2),
    ._1d(\十二进制计数器或二十四进制的计数器电路_1__1a [3]), ._1c(\十二进制计数器或二十四进制的计数器电路_1__1a [2]),
    ._1b(\十二进制计数器或二十四进制的计数器电路_1__1a [1]), ._1a(\十二进制计数器或二十四进制的计数器电路_1__1a [0]),
    ._0d(\十二进制计数器或二十四进制的计数器电路_1__0a [3]), ._0c(\十二进制计数器或二十四进制的计数器电路_1__0a [2]),
    ._0b(\十二进制计数器或二十四进制的计数器电路_1__0a [1]), ._0a(\十二进制计数器或二十四进制的计数器电路_1__0a [0]), .nQcc(out_4));
  Hex_Digit_Display hex_digit_display_2 (.value(\十二进制计数器或二十四进制的计数器电路_1__0a ));  // open: dp
endmodule

module \上下午文字显示的电路  (
  input  AM_FM,
  input  TT,
  output [4:0] out_3,
  output [4:0] out_4,
  output [4:0] out_5,
  output [4:0] out_6
);

  wire [4:0] multiplexer_2_out, multiplexer_5_out, multiplexer_7_out;

  Multiplexer #(.width(5)) multiplexer_1 (.in0({5{1'b0}}), .in1(multiplexer_2_out), .out(out_3), .sel(TT));  // open: en
  Multiplexer #(.width(5)) multiplexer_2 (
    .in0(5'b00001), .in1(5'b10000), .out(multiplexer_2_out), .sel(AM_FM));  // open: en
  Multiplexer #(.width(5)) multiplexer_3 (.in0({5{1'b0}}), .in1({5{1'b1}}), .out(out_4), .sel(TT));  // open: en
  Multiplexer #(.width(5)) multiplexer_4 (.in0({5{1'b0}}), .in1(multiplexer_5_out), .out(out_5), .sel(TT));  // open: en
  Multiplexer #(.width(5)) multiplexer_5 (
    .in0(5'b00101), .in1(5'b10100), .out(multiplexer_5_out), .sel(AM_FM));  // open: en
  Multiplexer #(.width(5)) multiplexer_6 (.in0({5{1'b0}}), .in1(multiplexer_7_out), .out(out_6), .sel(TT));  // open: en
  Multiplexer #(.width(5)) multiplexer_7 (
    .in0(5'b00001), .in1(5'b10000), .out(multiplexer_7_out), .sel(AM_FM));  // open: en
endmodule

module \上下午文字显示的电路测试电路  (
  input  in_1,
  input  in_2
);

  wire [4:0] \上下午文字显示的电路_1_out_3 , \上下午文字显示的电路_1_out_4 , \上下午文字显示的电路_1_out_5 , \上下午文字显示的电路_1_out_6 ;

  DotMatrix #(.matrixcols(4), .matrixrows(5)) dotmatrix_1 (
    .col0(\上下午文字显示的电路_1_out_3 ), .col1(\上下午文字显示的电路_1_out_4 ), .col2(\上下午文字显示的电路_1_out_5 ),
    .col3(\上下午文字显示的电路_1_out_6 ));
  \上下午文字显示的电路  \u_上下午文字显示的电路_1  (
    .AM_FM(in_1), .TT(in_2), .out_3(\上下午文字显示的电路_1_out_3 ), .out_4(\上下午文字显示的电路_1_out_4 ),
    .out_5(\上下午文字显示的电路_1_out_5 ), .out_6(\上下午文字显示的电路_1_out_6 ));
endmodule

module \电子钟整点报时电路  (
  input  in_1,
  input  in_2,
  input  in_3,
  input  in_4,
  input  in_5,
  input  in_6,
  output out_7
);

  wire and_1_out, clock_1_out;

  Clock clock_1 (.out(clock_1_out));
  and and_1 (and_1_out, in_1, in_2, in_3, in_4, in_5, in_6);
  Multiplexer multiplexer_1 (.in0(1'b0), .in1(clock_1_out), .out(out_7), .sel(and_1_out));  // open: en
endmodule

module \电子钟整点报时电路测试电路  (
  input  in_1,
  input  in_2,
  input  in_3,
  input  in_4,
  input  in_5,
  input  in_6,
  output out_7
);

  \电子钟整点报时电路  \u_电子钟整点报时电路_1  (
    .in_1(in_6), .in_2(in_3), .in_3(in_5), .in_4(in_1), .in_5(in_2), .in_6(in_4), .out_7(out_7));
endmodule

module \秒脉冲产生电路  (
  input  in_1,
  output out_2
);

  wire d_ff_1_q, d_ff_1_qn, d_ff_2_qn;

  D_Flip_Flop d_ff_1 (.clk(in_1), .D(d_ff_1_qn), .Q(d_ff_1_q), .Qn(d_ff_1_qn));  // open: preset, en, reset
  D_Flip_Flop d_ff_2 (.clk(d_ff_1_q), .D(d_ff_2_qn), .Q(out_2), .Qn(d_ff_2_qn));  // open: preset, en, reset
endmodule

module \多功能数字钟  (
  input  CPU,
  input  CPD,
  input  ADJ0,
  input  ADJ1,
  input  CLR,
  input  SET,
  input  CP,
  output out_8,
  output [3:0] out_9,
  output [3:0] out_10,
  output [3:0] out_11,
  output [3:0] out_12,
  output [3:0] out_13,
  output [3:0] out_14,
  output [4:0] out_15,
  output [4:0] out_16,
  output [4:0] out_17,
  output [4:0] out_18
);

  wire multiplexer_1_out, multiplexer_2_out, multiplexer_3_out, multiplexer_4_out, multiplexer_7_out,
       multiplexer_8_out, multiplexer_9_out, multiplexer_10_out, multiplexer_11_out, \n60进制计数器_1_qcc ,
       \n60进制计数器_2_qcc , not_1_out, not_2_out, not_3_out, not_4_out, not_5_out, not_6_out, not_7_out,
       not_8_out, not_9_out, t_ff_1_q, \十二进制计数器或二十四进制的计数器电路_2_nqcc , \秒脉冲产生电路_1_out_2 ;
  wire [3:0] \十二进制计数器或二十四进制的计数器电路_1__0a , \十二进制计数器或二十四进制的计数器电路_1__1a , \十二进制计数器或二十四进制的计数器电路_2__0a ,
       \十二进制计数器或二十四进制的计数器电路_2__1a ;

  not not_1 (not_1_out, ADJ0);
  Multiplexer multiplexer_1 (.in0(not_4_out), .in1(CPU), .out(multiplexer_1_out), .sel(ADJ0));  // open: en
  Multiplexer multiplexer_2 (.in0(\秒脉冲产生电路_1_out_2 ), .in1(1'b0), .out(multiplexer_2_out), .sel(ADJ0));  // open: en
  \秒脉冲产生电路  \u_秒脉冲产生电路_1  (.in_1(CP), .out_2(\秒脉冲产生电路_1_out_2 ));
  Multiplexer multiplexer_3 (.in0(multiplexer_9_out), .in1(1'b0), .out(multiplexer_3_out), .sel(ADJ1));  // open: en
  Multiplexer multiplexer_4 (
    .in0(multiplexer_1_out), .in1(1'b0), .out(multiplexer_4_out), .sel(not_2_out));  // open: en
  not not_2 (not_2_out, ADJ1);
  \_60进制计数器  \u_60进制计数器_1  (
    .CPU(multiplexer_2_out), .ADJ(1'b0), .CLR(CLR), .out_5(out_13[3]), .out_6(out_13[2]), .out_7(out_13[1]),
    .out_8(out_13[0]), .out_9(out_14[3]), .out_10(out_14[2]), .out_11(out_14[1]), .out_12(out_14[0]),
    .Qcc(\n60进制计数器_1_qcc ));  // open: CPD
  \电子钟整点报时电路  \u_电子钟整点报时电路_1  (
    .in_1(out_13[0]), .in_2(out_12[3]), .in_3(out_13[2]), .in_4(out_11[2]), .in_5(out_11[0]),
    .in_6(out_12[0]), .out_7(out_8));
  not not_3 (not_3_out, ADJ0);
  Multiplexer #(.width(4)) multiplexer_5 (
    .in0(\十二进制计数器或二十四进制的计数器电路_2__1a ), .in1(\十二进制计数器或二十四进制的计数器电路_1__1a ), .out(out_9), .sel(SET));  // open: en
  not not_4 (not_4_out, \n60进制计数器_1_qcc );
  Multiplexer #(.width(4)) multiplexer_6 (
    .in0(\十二进制计数器或二十四进制的计数器电路_2__0a ), .in1(\十二进制计数器或二十四进制的计数器电路_1__0a ), .out(out_10), .sel(SET));  // open: en
  not not_5 (not_5_out, not_1_out);
  Multiplexer multiplexer_7 (
    .in0(multiplexer_4_out), .in1(multiplexer_1_out), .out(multiplexer_7_out), .sel(not_3_out));  // open: en
  not not_6 (not_6_out, ADJ1);
  Multiplexer multiplexer_8 (.in0(CPD), .in1(1'b0), .out(multiplexer_8_out), .sel(not_6_out));  // open: en
  \_60进制计数器  \u_60进制计数器_2  (
    .CPU(multiplexer_7_out), .CPD(multiplexer_8_out), .ADJ(not_5_out), .CLR(CLR), .out_5(out_11[3]),
    .out_6(out_11[2]), .out_7(out_11[1]), .out_8(out_11[0]), .out_9(out_12[3]), .out_10(out_12[2]),
    .out_11(out_12[1]), .out_12(out_12[0]), .Qcc(\n60进制计数器_2_qcc ));
  Multiplexer multiplexer_9 (.in0(not_7_out), .in1(CPU), .out(multiplexer_9_out), .sel(ADJ0));  // open: en
  not not_7 (not_7_out, \n60进制计数器_2_qcc );
  not not_8 (not_8_out, not_1_out);
  Multiplexer multiplexer_10 (
    .in0(multiplexer_3_out), .in1(multiplexer_9_out), .out(multiplexer_10_out), .sel(not_3_out));  // open: en
  Multiplexer multiplexer_11 (.in0(CPD), .in1(1'b0), .out(multiplexer_11_out), .sel(ADJ1));  // open: en
  \十二进制计数器或二十四进制的计数器电路  \u_十二进制计数器或二十四进制的计数器电路_1  (
    .CPU(multiplexer_10_out), .CPD(multiplexer_11_out), .Adj(not_8_out), .CLR(CLR), .SET(1'b1),
    ._1d(\十二进制计数器或二十四进制的计数器电路_1__1a [3]), ._1c(\十二进制计数器或二十四进制的计数器电路_1__1a [2]),
    ._1b(\十二进制计数器或二十四进制的计数器电路_1__1a [1]), ._1a(\十二进制计数器或二十四进制的计数器电路_1__1a [0]),
    ._0d(\十二进制计数器或二十四进制的计数器电路_1__0a [3]), ._0c(\十二进制计数器或二十四进制的计数器电路_1__0a [2]),
    ._0b(\十二进制计数器或二十四进制的计数器电路_1__0a [1]), ._0a(\十二进制计数器或二十四进制的计数器电路_1__0a [0]));  // open: nQcc
  \十二进制计数器或二十四进制的计数器电路  \u_十二进制计数器或二十四进制的计数器电路_2  (
    .CPU(multiplexer_10_out), .CPD(multiplexer_11_out), .Adj(not_8_out), .CLR(CLR), .SET(1'b0),
    ._1d(\十二进制计数器或二十四进制的计数器电路_2__1a [3]), ._1c(\十二进制计数器或二十四进制的计数器电路_2__1a [2]),
    ._1b(\十二进制计数器或二十四进制的计数器电路_2__1a [1]), ._1a(\十二进制计数器或二十四进制的计数器电路_2__1a [0]),
    ._0d(\十二进制计数器或二十四进制的计数器电路_2__0a [3]), ._0c(\十二进制计数器或二十四进制的计数器电路_2__0a [2]),
    ._0b(\十二进制计数器或二十四进制的计数器电路_2__0a [1]), ._0a(\十二进制计数器或二十四进制的计数器电路_2__0a [0]),
    .nQcc(\十二进制计数器或二十四进制的计数器电路_2_nqcc ));
  T_Flip_Flop t_ff_1 (.clk(\十二进制计数器或二十四进制的计数器电路_2_nqcc ), .T(1'b1), .Q(t_ff_1_q));  // open: Qn, preset, reset, en
  \上下午文字显示的电路  \u_上下午文字显示的电路_1  (
    .AM_FM(t_ff_1_q), .TT(not_9_out), .out_3(out_15), .out_4(out_16), .out_5(out_17), .out_6(out_18));
  not not_9 (not_9_out, SET);

  // Notes on the sheet:
  //   SEC
  //   MIN
  //   Hour_24
  //   Hour_12
endmodule

module \多功能数字钟测试电路  (
  input  in_1,
  input  in_2,
  input  in_3,
  input  in_4
);

  wire button_1_out, button_2_out, clock_1_out, \多功能数字钟_1_out_8 ;
  wire [3:0] \多功能数字钟_1_out_9 , \多功能数字钟_1_out_10 , \多功能数字钟_1_out_11 , \多功能数字钟_1_out_12 , \多功能数字钟_1_out_13 ,
       \多功能数字钟_1_out_14 ;
  wire [4:0] \多功能数字钟_1_out_15 , \多功能数字钟_1_out_16 , \多功能数字钟_1_out_17 , \多功能数字钟_1_out_18 ;

  DotMatrix #(.matrixcols(4), .matrixrows(5)) dotmatrix_1 (
    .col0(\多功能数字钟_1_out_15 ), .col1(\多功能数字钟_1_out_16 ), .col2(\多功能数字钟_1_out_17 ), .col3(\多功能数字钟_1_out_18 ));
  \多功能数字钟  \u_多功能数字钟_1  (
    .CPU(button_1_out), .CPD(button_2_out), .ADJ0(in_1), .ADJ1(in_2), .CLR(in_4), .SET(in_3),
    .out_15(\多功能数字钟_1_out_15 ), .out_16(\多功能数字钟_1_out_16 ), .out_17(\多功能数字钟_1_out_17 ),
    .out_18(\多功能数字钟_1_out_18 ), .CP(clock_1_out), .out_8(\多功能数字钟_1_out_8 ), .out_9(\多功能数字钟_1_out_9 ),
    .out_10(\多功能数字钟_1_out_10 ), .out_11(\多功能数字钟_1_out_11 ), .out_12(\多功能数字钟_1_out_12 ),
    .out_13(\多功能数字钟_1_out_13 ), .out_14(\多功能数字钟_1_out_14 ));
  Clock clock_1 (.out(clock_1_out));
  Button button_1 (.out(button_1_out));
  Hex_Digit_Display hex_digit_display_1 (.value(\多功能数字钟_1_out_10 ));  // open: dp
  Hex_Digit_Display hex_digit_display_2 (.value(\多功能数字钟_1_out_9 ));  // open: dp
  Hex_Digit_Display hex_digit_display_3 (.value(\多功能数字钟_1_out_11 ));  // open: dp
  Button button_2 (.out(button_2_out));
  Hex_Digit_Display hex_digit_display_4 (.value(\多功能数字钟_1_out_12 ));  // open: dp
  Hex_Digit_Display hex_digit_display_5 (.value(\多功能数字钟_1_out_13 ));  // open: dp
  Hex_Digit_Display hex_digit_display_6 (.value(\多功能数字钟_1_out_14 ));  // open: dp
  LED led_1 (.in(\多功能数字钟_1_out_8 ));
endmodule
