// Logisim project 实验5-校交1801-U201890018-郝凯欣.circ as structural Verilog: 10 circuits, main circuit count60
module count60 (
  input  in_1,
  input  in_2,
  input  in_3,
  input  in_4,
  output out_5,
  output S4,
  output S2,
  output S8,
  output S1,
  output S4_2,
  output S2_2,
  output S8_2,
  output S1_2
);

  wire and_1_out, and_3_out, and_4_out, and_5_out, and_6_out, and_7_out, and_8_out, and_9_out, clock_1_out,
       lab1_1_qa, lab1_1_qb, lab1_1_qc, lab1_1_qd, lab1_2_qa, lab1_2_qb, lab1_2_qc, lab1_2_qd, lab1_3_qa,
       lab1_3_qb, lab1_4_qa, lab1_4_qb, lab1_4_qc, lab1_4_qd, nor_1_out, or_1_out, or_2_out, or_3_out,
       sec_pulse_1_out_2, \先行四位并行加法器_1_c4 , \先行四位并行加法器_1_s0 , \先行四位并行加法器_1_s1 , \先行四位并行加法器_1_s2 ,
       \先行四位并行加法器_1_s3 , \先行四位并行加法器_2_c4 , \先行四位并行加法器_2_s0 , \先行四位并行加法器_2_s1 , \先行四位并行加法器_2_s2 ,
       \先行四位并行加法器_2_s3 , \先行四位并行加法器_3_s0 , \先行四位并行加法器_3_s1 , \先行四位并行加法器_3_s2 , \先行四位并行加法器_3_s3 ,
       \先行四位并行加法器_4_c4 , \先行四位并行加法器_5_s0 , \先行四位并行加法器_5_s1 , \先行四位并行加法器_5_s2 , \先行四位并行加法器_5_s3 ,
       \先行四位并行加法器_6_s0 , \先行四位并行加法器_6_s1 , \先行四位并行加法器_6_s2 , \先行四位并行加法器_6_s3 ;

  Clock clock_1 (.out(clock_1_out));
  or or_1 (or_1_out, lab1_2_qd, lab1_2_qc, lab1_2_qb, lab1_2_qa, lab1_4_qa, lab1_4_qb);
  and and_1 (and_1_out, in_4, or_1_out);
  lab1 lab1_1 (
    .CLR(or_2_out), .Qd(lab1_1_qd), .Qc(lab1_1_qc), .Qb(lab1_1_qb), .Qa(lab1_1_qa), .CPd(1'b0),
    .CPu(sec_pulse_1_out_2), .in_7(in_2), .in_8(lab1_2_qa), .in_5(lab1_2_qb), .in_1(lab1_2_qd),
    .in_2(lab1_2_qc));
  sec_pulse sec_pulse_1 (.out_2(sec_pulse_1_out_2), .in_1(clock_1_out));
  or or_2 (or_2_out, in_1, out_5);
  lab1 lab1_2 (
    .CLR(and_4_out), .Qd(lab1_2_qd), .Qc(lab1_2_qc), .Qb(lab1_2_qb), .Qa(lab1_2_qa), .CPd(and_1_out),
    .CPu(in_3));  // open: in_7, in_8, in_5, in_1, in_2
  and and_2 (out_5, lab1_1_qd, lab1_1_qc, lab1_3_qb, lab1_3_qa);
  and and_3 (and_3_out, lab1_1_qd, lab1_1_qc, lab1_1_qb, lab1_1_qa);
  and and_4 (and_4_out, lab1_2_qd, lab1_2_qc, lab1_4_qb, lab1_4_qa);
  and and_5 (and_5_out, lab1_2_qd, lab1_2_qc, lab1_2_qb, lab1_2_qa);
  nor nor_1 (nor_1_out, lab1_2_qd, lab1_2_qc, lab1_2_qb, lab1_2_qa);
  and and_6 (and_6_out, nor_1_out, and_1_out);
  lab1 lab1_3 (
    .CLR(or_2_out), .Qb(lab1_3_qb), .Qa(lab1_3_qa), .CPd(1'b0), .CPu(and_3_out), .in_7(in_2),
    .in_8(lab1_4_qa), .in_5(lab1_4_qb), .in_1(lab1_4_qd), .in_2(lab1_4_qc));  // open: Qd, Qc
  and and_7 (and_7_out, in_3, and_5_out);
  lab1 lab1_4 (
    .CLR(and_4_out), .Qd(lab1_4_qd), .Qc(lab1_4_qc), .Qb(lab1_4_qb), .Qa(lab1_4_qa), .CPd(and_6_out),
    .CPu(and_7_out));  // open: in_7, in_8, in_5, in_1, in_2
  \先行四位并行加法器  \u_先行四位并行加法器_1  (
    .A0(lab1_1_qa), .A1(lab1_1_qb), .A2(lab1_1_qc), .A3(lab1_1_qd), .B0(1'b0), .B1(lab1_3_qa),
    .B2(lab1_3_qa), .B3(1'b0), .C0(1'b0), .S0(\先行四位并行加法器_1_s0 ), .S1(\先行四位并行加法器_1_s1 ),
    .S2(\先行四位并行加法器_1_s2 ), .S3(\先行四位并行加法器_1_s3 ), .C4(\先行四位并行加法器_1_c4 ));
  \先行四位并行加法器  \u_先行四位并行加法器_2  (
    .A0(\先行四位并行加法器_1_s0 ), .A1(\先行四位并行加法器_1_s1 ), .A2(\先行四位并行加法器_1_s2 ), .A3(\先行四位并行加法器_1_s3 ), .B0(1'b0),
    .B1(lab1_3_qb), .B2(1'b0), .B3(1'b0), .C0(1'b0), .S0(\先行四位并行加法器_2_s0 ), .S1(\先行四位并行加法器_2_s1 ),
    .S2(\先行四位并行加法器_2_s2 ), .S3(\先行四位并行加法器_2_s3 ), .C4(\先行四位并行加法器_2_c4 ));
  and and_8 (and_8_out, \先行四位并行加法器_5_s1 , \先行四位并行加法器_5_s3 );
  and and_9 (and_9_out, \先行四位并行加法器_5_s2 , \先行四位并行加法器_5_s3 );
  \先行四位并行加法器  \u_先行四位并行加法器_3  (
    .A0(lab1_3_qa), .A1(1'b0), .A2(1'b0), .A3(1'b0), .B0(lab1_3_qb), .B1(lab1_3_qb), .B2(1'b0), .B3(1'b0),
    .C0(\先行四位并行加法器_4_c4 ), .S0(\先行四位并行加法器_3_s0 ), .S1(\先行四位并行加法器_3_s1 ), .S2(\先行四位并行加法器_3_s2 ),
    .S3(\先行四位并行加法器_3_s3 ));  // open: C4
  \先行四位并行加法器  \u_先行四位并行加法器_4  (
    .A0(\先行四位并行加法器_5_s0 ), .A1(\先行四位并行加法器_5_s1 ), .A2(\先行四位并行加法器_5_s2 ), .A3(\先行四位并行加法器_5_s3 ), .B0(1'b0),
    .B1(or_3_out), .B2(or_3_out), .B3(1'b0), .C0(1'b0), .S0(S1_2), .S1(S2_2), .S2(S4_2), .S3(S8_2),
    .C4(\先行四位并行加法器_4_c4 ));
  or or_3 (or_3_out, and_8_out, and_9_out);
  \先行四位并行加法器  \u_先行四位并行加法器_5  (
    .A0(\先行四位并行加法器_6_s0 ), .A1(\先行四位并行加法器_6_s1 ), .A2(\先行四位并行加法器_6_s2 ), .A3(\先行四位并行加法器_6_s3 ), .B0(1'b0),
    .B1(\先行四位并行加法器_1_c4 ), .B2(\先行四位并行加法器_1_c4 ), .B3(1'b0), .C0(1'b0), .S0(\先行四位并行加法器_5_s0 ),
    .S1(\先行四位并行加法器_5_s1 ), .S2(\先行四位并行加法器_5_s2 ), .S3(\先行四位并行加法器_5_s3 ));  // open: C4
  \先行四位并行加法器  \u_先行四位并行加法器_6  (
    .A0(\先行四位并行加法器_2_s0 ), .A1(\先行四位并行加法器_2_s1 ), .A2(\先行四位并行加法器_2_s2 ), .A3(\先行四位并行加法器_2_s3 ), .B0(1'b0),
    .B1(\先行四位并行加法器_2_c4 ), .B2(\先行四位并行加法器_2_c4 ), .B3(1'b0), .C0(1'b0), .S0(\先行四位并行加法器_6_s0 ),
    .S1(\先行四位并行加法器_6_s1 ), .S2(\先行四位并行加法器_6_s2 ), .S3(\先行四位并行加法器_6_s3 ));  // open: C4
  \先行四位并行加法器  \u_先行四位并行加法器_7  (
    .A0(\先行四位并行加法器_3_s0 ), .A1(\先行四位并行加法器_3_s1 ), .A2(\先行四位并行加法器_3_s2 ), .A3(\先行四位并行加法器_3_s3 ),
    .B0(\先行四位并行加法器_2_c4 ), .B1(1'b0), .B2(1'b0), .B3(1'b0), .C0(\先行四位并行加法器_1_c4 ), .S0(S1), .S1(S2), .S2(S4),
    .S3(S8));  // open: C4
endmodule

module test (
  input  in_1,
  output out_2
);

  wire button_1_out, button_2_out, button_3_out;
  wire [3:0] count60_1_s1, count60_1_s1_2;

  Button button_1 (.out(button_1_out));
  Button button_2 (.out(button_2_out));
  Hex_Digit_Display hex_digit_display_1 (.value(count60_1_s1));  // open: dp
  Hex_Digit_Display hex_digit_display_2 (.value(count60_1_s1_2));  // open: dp
  count60 count60_1 (
    .in_1(button_3_out), .in_2(in_1), .in_3(button_1_out), .in_4(button_2_out), .out_5(out_2),
    .S8_2(count60_1_s1_2[3]), .S4_2(count60_1_s1_2[2]), .S2_2(count60_1_s1_2[1]), .S1_2(count60_1_s1_2[0]),
    .S8(count60_1_s1[3]), .S4(count60_1_s1[2]), .S2(count60_1_s1[1]), .S1(count60_1_s1[0]));
  Button button_3 (.out(button_3_out));
endmodule

module count12 (
  input  in_1,
  input  in_2,
  input  in_3,
  input  in_4,
  input  in_5,
  output out_6,
  output out_7,
  output out_8,
  output out_9,
  output out_10,
  output out_11,
  output out_12,
  output out_13,
  output out_14
);

  wire and_1_out, and_2_out, not_1_out, not_2_out, not_3_out, not_4_out, not_5_out, or_1_out;

  not not_1 (not_1_out, out_9);
  not not_2 (not_2_out, out_10);
  not not_3 (not_3_out, out_12);
  and and_1 (and_1_out, out_9, not_4_out, out_12);
  not not_4 (not_4_out, out_13);
  count60 count60_1 (
    .in_1(or_1_out), .in_2(in_2), .in_3(in_1), .in_4(in_4), .S8_2(out_10), .S4_2(out_11), .S2_2(out_12),
    .S1_2(out_13), .S8(out_6), .S4(out_7), .S2(out_8), .S1(out_9));  // open: out_5
  or or_1 (or_1_out, out_14, in_5);
  not not_5 (not_5_out, out_13);
  Multiplexer multiplexer_1 (.in0(and_1_out), .in1(and_2_out), .out(out_14), .sel(in_3));  // open: en
  and and_2 (and_2_out, not_2_out, not_5_out, not_1_out, not_3_out, out_11, out_8);
endmodule

module TEST2 (
  input  in_1,
  input  in_2,
  output out_3
);

  wire button_1_out, button_2_out, button_3_out;
  wire [3:0] count12_1_out_9, count12_1_out_13;

  Button button_1 (.out(button_1_out));
  Button button_2 (.out(button_2_out));
  Hex_Digit_Display hex_digit_display_1 (.value(count12_1_out_9));  // open: dp
  Hex_Digit_Display hex_digit_display_2 (.value(count12_1_out_13));  // open: dp
  count12 count12_1 (
    .out_14(out_3), .in_3(in_2), .out_6(count12_1_out_9[3]), .out_7(count12_1_out_9[2]),
    .out_8(count12_1_out_9[1]), .out_9(count12_1_out_9[0]), .out_10(count12_1_out_13[3]),
    .out_11(count12_1_out_13[2]), .out_12(count12_1_out_13[1]), .out_13(count12_1_out_13[0]),
    .in_1(button_1_out), .in_2(in_1), .in_4(button_2_out), .in_5(button_3_out));
  Button button_3 (.out(button_3_out));
endmodule

module NOON (
  input  in_1,
  input  in_2,
  output [4:0] out_3,
  output [4:0] out_4,
  output [4:0] out_5,
  output [4:0] out_6
);

  wire [4:0] multiplexer_1_out, multiplexer_2_out, multiplexer_3_out, multiplexer_4_out;

  Multiplexer #(.width(5)) multiplexer_1 (
    .in0(5'b00001), .in1(5'b10000), .out(multiplexer_1_out), .sel(in_1));  // open: en
  Multiplexer #(.width(5)) multiplexer_2 (
    .in0({5{1'b1}}), .in1({5{1'b1}}), .out(multiplexer_2_out), .sel(in_1));  // open: en
  Multiplexer #(.width(5)) multiplexer_3 (
    .in0(5'b00101), .in1(5'b10100), .out(multiplexer_3_out), .sel(in_1));  // open: en
  Multiplexer #(.width(5)) multiplexer_4 (
    .in0(5'b00001), .in1(5'b10000), .out(multiplexer_4_out), .sel(in_1));  // open: en
  Multiplexer #(.width(5)) multiplexer_5 (
    .in0({5{1'b0}}), .in1(multiplexer_1_out), .out(out_3), .sel(in_2));  // open: en
  Multiplexer #(.width(5)) multiplexer_6 (
    .in0({5{1'b0}}), .in1(multiplexer_2_out), .out(out_4), .sel(in_2));  // open: en
  Multiplexer #(.width(5)) multiplexer_7 (
    .in0({5{1'b0}}), .in1(multiplexer_3_out), .out(out_5), .sel(in_2));  // open: en
  Multiplexer #(.width(5)) multiplexer_8 (
    .in0({5{1'b0}}), .in1(multiplexer_4_out), .out(out_6), .sel(in_2));  // open: en
endmodule

module TEST3 (
  input  in_1,
  input  in_2
);

  wire [4:0] noon_1_out_3, noon_1_out_4, noon_1_out_5, noon_1_out_6;

  DotMatrix #(.matrixcols(4), .matrixrows(5)) dotmatrix_1 (
    .col0(noon_1_out_3), .col1(noon_1_out_4), .col2(noon_1_out_5), .col3(noon_1_out_6));
  NOON noon_1 (
    .in_1(in_1), .in_2(in_2), .out_3(noon_1_out_3), .out_4(noon_1_out_4), .out_5(noon_1_out_5),
    .out_6(noon_1_out_6));
endmodule

module beep (
  input  in_1
);

  wire clock_1_out, multiplexer_1_out;

  Clock clock_1 (.out(clock_1_out));
  LED led_1 (.in(multiplexer_1_out));
  Multiplexer multiplexer_1 (.in0(1'b0), .in1(clock_1_out), .out(multiplexer_1_out), .sel(in_1));  // open: en
endmodule

module sec_pulse (
  input  in_1,
  output out_2
);

  wire lab1_1_qb;

  lab1 lab1_1 (
    .CLR(lab1_1_qb), .Qb(lab1_1_qb), .CPd(1'b0), .CPu(in_1));  // open: Qd, Qc, Qa, in_7, in_8, in_5, in_1, in_2
  T_Flip_Flop t_ff_1 (.clk(lab1_1_qb), .T(1'b1), .Q(out_2));  // open: Qn, preset, reset, en
endmodule

module clock (
  input  CPu,
  input  Adj1,
  input  CPd,
  input  in_4,
  input  Adj0,
  input  in_6,
  output out_7,
  output [4:0] out_8,
  output [4:0] out_9,
  output [4:0] out_10,
  output [4:0] out_11,
  output [3:0] out_12,
  output [3:0] out_13,
  output [3:0] out_14,
  output [3:0] out_15,
  output [3:0] out_16,
  output [3:0] out_17
);

  wire and_1_out, and_2_out, and_3_out, and_4_out, and_5_out, clock_1_out, count12_1_out_14, min_out_5,
       multiplexer_2_out, multiplexer_3_out, multiplexer_4_out, multiplexer_5_out, multiplexer_6_out,
       multiplexer_7_out, not_1_out, not_2_out, not_3_out, sec_out_5, t_ff_1_q, xor_1_out, xor_2_out;

  and and_1 (and_1_out, out_12[2], out_12[0]);
  Clock clock_1 (.out(clock_1_out));
  Multiplexer multiplexer_1 (.in0(1'b0), .in1(clock_1_out), .out(out_7), .sel(and_2_out));  // open: en
  and and_2 (and_2_out, and_1_out, and_4_out);
  count60 sec (
    .in_1(in_6), .out_5(sec_out_5), .S8_2(out_13[3]), .S4_2(out_13[2]), .S2_2(out_13[1]), .S1_2(out_13[0]),
    .S8(out_12[3]), .S4(out_12[2]), .S2(out_12[1]), .S1(out_12[0]));  // open: in_2, in_3, in_4
  Multiplexer multiplexer_2 (.in0(CPu), .in1(1'b0), .out(multiplexer_2_out), .sel(Adj1));  // open: en
  Multiplexer multiplexer_3 (.in0(CPd), .in1(1'b0), .out(multiplexer_3_out), .sel(Adj1));  // open: en
  xor xor_1 (xor_1_out, 1'b1, in_6);
  Multiplexer multiplexer_4 (
    .in0(sec_out_5), .in1(multiplexer_2_out), .out(multiplexer_4_out), .sel(Adj0));  // open: en
  and and_3 (and_3_out, multiplexer_3_out, Adj0);
  Multiplexer multiplexer_5 (.in0(1'b0), .in1(CPu), .out(multiplexer_5_out), .sel(Adj1));  // open: en
  Multiplexer multiplexer_6 (.in0(1'b0), .in1(CPd), .out(multiplexer_6_out), .sel(Adj1));  // open: en
  not not_1 (not_1_out, out_16[2]);
  and and_4 (and_4_out, out_16[3], not_1_out, out_17[2], not_2_out, out_16[0], out_17[0]);
  not not_2 (not_2_out, out_16[1]);
  count60 min (
    .in_1(in_6), .in_2(xor_1_out), .in_3(multiplexer_4_out), .in_4(and_3_out), .out_5(min_out_5),
    .S8_2(out_16[3]), .S4_2(out_16[2]), .S2_2(out_16[1]), .S1_2(out_16[0]), .S8(out_17[3]), .S4(out_17[2]),
    .S2(out_17[1]), .S1(out_17[0]));
  Multiplexer multiplexer_7 (
    .in0(min_out_5), .in1(multiplexer_5_out), .out(multiplexer_7_out), .sel(Adj0));  // open: en
  xor xor_2 (xor_2_out, in_6, 1'b1);
  and and_5 (and_5_out, multiplexer_6_out, Adj0);
  count12 count12_1 (
    .out_14(count12_1_out_14), .in_3(in_4), .out_6(out_14[3]), .out_7(out_14[2]), .out_8(out_14[1]),
    .out_9(out_14[0]), .out_10(out_15[3]), .out_11(out_15[2]), .out_12(out_15[1]), .out_13(out_15[0]),
    .in_1(multiplexer_7_out), .in_2(xor_2_out), .in_4(and_5_out), .in_5(in_6));
  NOON noon_1 (.in_1(t_ff_1_q), .in_2(not_3_out), .out_3(out_8), .out_4(out_9), .out_5(out_10), .out_6(out_11));
  T_Flip_Flop t_ff_1 (.clk(count12_1_out_14), .T(1'b1), .Q(t_ff_1_q));  // open: Qn, preset, reset, en
  not not_3 (not_3_out, in_4);
endmodule

module FINIAL_TEST (
  input  in_1,
  input  in_2,
  input  in_3,
  input  in_4
);

  wire button_1_out, button_2_out, clock_1_out_7;
  wire [3:0] clock_1_out_12, clock_1_out_13, clock_1_out_14, clock_1_out_15, clock_1_out_16, clock_1_out_17;
  wire [4:0] clock_1_out_8, clock_1_out_9, clock_1_out_10, clock_1_out_11;

  DotMatrix #(.matrixcols(4), .matrixrows(5)) dotmatrix_1 (
    .col0(clock_1_out_8), .col1(clock_1_out_9), .col2(clock_1_out_10), .col3(clock_1_out_11));
  Hex_Digit_Display hex_digit_display_1 (.value(clock_1_out_14));  // open: dp
  clock clock_1 (
    .CPu(button_1_out), .CPd(button_2_out), .out_7(clock_1_out_7), .in_4(in_3), .out_12(clock_1_out_12),
    .out_13(clock_1_out_13), .out_17(clock_1_out_17), .out_16(clock_1_out_16), .out_14(clock_1_out_14),
    .out_15(clock_1_out_15), .Adj1(in_2), .Adj0(in_1), .in_6(in_4), .out_8(clock_1_out_8),
    .out_11(clock_1_out_11), .out_10(clock_1_out_10), .out_9(clock_1_out_9));
  Button button_1 (.out(button_1_out));
  Hex_Digit_Display hex_digit_display_2 (.value(clock_1_out_15));  // open: dp
  Hex_Digit_Display hex_digit_display_3 (.value(clock_1_out_17));  // open: dp
  Button button_2 (.out(button_2_out));
  Hex_Digit_Display hex_digit_display_4 (.value(clock_1_out_16));  // open: dp
  Hex_Digit_Display hex_digit_display_5 (.value(clock_1_out_12));  // open: dp
  Hex_Digit_Display hex_digit_display_6 (.value(clock_1_out_13));  // open: dp
  LED led_1 (.in(clock_1_out_7));
endmodule
