// Logisim project 实验6-校交1801-U201816030-车春池.circ as structural Verilog: 7 circuits, main circuit sqrX
module sqrX (
  input  [31:0] a,
  input  [31:0] b,
  input  [31:0] c,
  input  [31:0] d,
  output [31:0] a_prime,
  output [31:0] b_prime,
  output [31:0] c_prime,
  output [31:0] a_prime_2
);

  wire [31:0] multiplier_1_out, multiplier_2_out, multiplier_3_out, multiplier_4_out, multiplier_5_out,
       multiplier_6_out, multiplier_7_out, multiplier_8_out;

  Multiplier #(.width(32)) multiplier_1 (.a(a), .b(a), .out(multiplier_1_out));  // open: cin, cout
  Multiplier #(.width(32)) multiplier_2 (.a(b), .b(c), .out(multiplier_2_out));  // open: cin, cout
  Adder #(.width(32)) adder_1 (.a(multiplier_1_out), .b(multiplier_2_out), .out(a_prime));  // open: cin, cout
  Multiplier #(.width(32)) multiplier_3 (.a(a), .b(b), .out(multiplier_3_out));  // open: cin, cout
  Adder #(.width(32)) adder_2 (.a(multiplier_3_out), .b(multiplier_4_out), .out(b_prime));  // open: cin, cout
  Multiplier #(.width(32)) multiplier_4 (.a(b), .b(d), .out(multiplier_4_out));  // open: cin, cout
  Multiplier #(.width(32)) multiplier_5 (.a(a), .b(c), .out(multiplier_5_out));  // open: cin, cout
  Adder #(.width(32)) adder_3 (.a(multiplier_5_out), .b(multiplier_6_out), .out(c_prime));  // open: cin, cout
  Adder #(.width(32)) adder_4 (.a(multiplier_7_out), .b(multiplier_8_out), .out(a_prime_2));  // open: cin, cout
  Multiplier #(.width(32)) multiplier_6 (.a(c), .b(d), .out(multiplier_6_out));  // open: cin, cout
  Multiplier #(.width(32)) multiplier_7 (.a(c), .b(b), .out(multiplier_7_out));  // open: cin, cout
  Multiplier #(.width(32)) multiplier_8 (.a(d), .b(d), .out(multiplier_8_out));  // open: cin, cout
endmodule

module sqrX_A (
  input  [31:0] a,
  input  [31:0] b,
  input  [31:0] c,
  input  [31:0] d,
  output [31:0] a_prime_prime,
  output [31:0] b_prime_prime,
  output [31:0] c_prime_prime,
  output [31:0] out_8
);

  wire [31:0] adder_2_out, adder_3_out, adder_5_out, adder_6_out, multiplier_1_out, multiplier_2_out,
       multiplier_3_out, multiplier_4_out, multiplier_5_out, multiplier_6_out, multiplier_7_out;

  Multiplier #(.width(32)) multiplier_1 (.a(a), .b(a), .out(multiplier_1_out));  // open: cin, cout
  Adder #(.width(32)) adder_1 (.a(multiplier_2_out), .b(multiplier_5_out), .out(a_prime_prime));  // open: cin, cout
  Multiplier #(.width(32)) multiplier_2 (.a(a), .b(b), .out(multiplier_2_out));  // open: cin, cout
  Adder #(.width(32)) adder_2 (.a(multiplier_1_out), .b(multiplier_4_out), .out(adder_2_out));  // open: cin, cout
  Adder #(.width(32)) adder_3 (.a(multiplier_2_out), .b(multiplier_5_out), .out(adder_3_out));  // open: cin, cout
  Multiplier #(.width(32)) multiplier_3 (.a(a), .b(c), .out(multiplier_3_out));  // open: cin, cout
  Multiplier #(.width(32)) multiplier_4 (.a(b), .b(c), .out(multiplier_4_out));  // open: cin, cout
  Adder #(.width(32)) adder_4 (.a(multiplier_4_out), .b(multiplier_7_out), .out(c_prime_prime));  // open: cin, cout
  Multiplier #(.width(32)) multiplier_5 (.a(b), .b(d), .out(multiplier_5_out));  // open: cin, cout
  Adder #(.width(32)) adder_5 (.a(multiplier_3_out), .b(multiplier_6_out), .out(adder_5_out));  // open: cin, cout
  Multiplier #(.width(32)) multiplier_6 (.a(b), .b(d), .out(multiplier_6_out));  // open: cin, cout
  Adder #(.width(32)) adder_6 (.a(multiplier_4_out), .b(multiplier_7_out), .out(adder_6_out));  // open: cin, cout
  Multiplier #(.width(32)) multiplier_7 (.a(d), .b(d), .out(multiplier_7_out));  // open: cin, cout
  Adder #(.width(32)) adder_7 (.a(adder_2_out), .b(adder_3_out), .out(b_prime_prime));  // open: cin, cout
  Adder #(.width(32)) adder_8 (.a(adder_5_out), .b(adder_6_out), .out(out_8));  // open: cin, cout
endmodule

module \Fibonacci数显示模块  (
  input  [31:0] Fn,
  output [3:0] D0,
  output [3:0] D1,
  output [3:0] D2,
  output [3:0] D3,
  output [3:0] D4,
  output [3:0] D5,
  output [3:0] D6,
  output [3:0] D7,
  output [3:0] D8,
  output [3:0] D9
);

  wire [3:0] divider_5_rem, divider_5_rem_2, divider_5_rem_3, divider_5_rem_4, divider_5_rem_5,
       divider_5_rem_6, divider_5_rem_7, divider_8_out, divider_8_out_2, divider_8_out_3, divider_8_out_4,
       divider_8_out_5, divider_8_out_6, divider_8_out_7, divider_8_rem, divider_8_rem_2, divider_8_rem_3,
       divider_8_rem_4, divider_8_rem_5, divider_8_rem_6, divider_8_rem_7;
  wire [31:0] divider_1_out, divider_2_out, divider_3_out, divider_4_out, divider_5_out, divider_6_out,
       divider_7_out, divider_9_out;
  wire [31:4] divider_1_rem, divider_2_rem, divider_3_rem, divider_4_rem, divider_6_rem, divider_7_rem,
       divider_9_rem;

  Divider #(.width(32)) divider_1 (.a(Fn), .b(32'ha), .out(divider_1_out), .rem({divider_1_rem, D0}));  // open: upper
  Divider #(.width(32)) divider_2 (
    .a(divider_1_out), .b(32'ha), .out(divider_2_out), .rem({divider_2_rem, D1}));  // open: upper
  Divider #(.width(32)) divider_3 (
    .a(divider_9_out), .b(32'ha), .out(divider_3_out), .rem({divider_3_rem, D5}));  // open: upper
  Divider #(.width(32)) divider_4 (
    .a(divider_3_out), .b(32'ha), .out(divider_4_out), .rem({divider_4_rem, D6}));  // open: upper
  Divider #(.width(32)) divider_5 (
    .a(divider_2_out), .b(32'ha), .out(divider_5_out),
    .rem({divider_5_rem_7, divider_5_rem_6, divider_5_rem_5, divider_5_rem_4, divider_5_rem_3, divider_5_rem_2, divider_5_rem, D2}));  // open: upper
  Divider #(.width(32)) divider_6 (
    .a(divider_5_out), .b(32'ha), .out(divider_6_out), .rem({divider_6_rem, D3}));  // open: upper
  Divider #(.width(32)) divider_7 (
    .a(divider_4_out), .b(32'ha), .out(divider_7_out), .rem({divider_7_rem, D7}));  // open: upper
  Divider #(.width(32)) divider_8 (
    .a(divider_7_out), .b(32'ha),
    .out({divider_8_out_7, divider_8_out_6, divider_8_out_5, divider_8_out_4, divider_8_out_3, divider_8_out_2, divider_8_out, D9}),
    .rem({divider_8_rem_7, divider_8_rem_6, divider_8_rem_5, divider_8_rem_4, divider_8_rem_3, divider_8_rem_2, divider_8_rem, D8}));  // open: upper
  Divider #(.width(32)) divider_9 (
    .a(divider_6_out), .b(32'ha), .out(divider_9_out), .rem({divider_9_rem, D4}));  // open: upper
endmodule

module \斐波那契_Fibonacci_数列计算器  (
  input  [5:0] n,
  input  clear,
  input  clk,
  output [3:0] D0,
  output [3:0] D1,
  output [3:0] D2,
  output [3:0] D3,
  output [3:0] D4,
  output [3:0] D5,
  output [3:0] D6,
  output [3:0] D7,
  output [3:0] D8,
  output [3:0] D9
);

  wire controller_1_clear_2, controller_1_clock_2, controller_1_ni_1, controller_1_start;
  wire [31:0] fibo_1_fi;

  Controller controller_1 (
    .clear_2(controller_1_clear_2), .n(n), .clear(clear), .clock(clk), .ni_1(controller_1_ni_1),
    .start(controller_1_start), .clock_2(controller_1_clock_2));
  Fibo fibo_1 (
    .start(controller_1_start), .clr(controller_1_clear_2), .clk(controller_1_clock_2),
    .ni_1(controller_1_ni_1), .Fi(fibo_1_fi));
  \Fibonacci数显示模块  \fibonacci数显示模块_1  (
    .Fn(fibo_1_fi), .D0(D0), .D5(D5), .D1(D1), .D6(D6), .D2(D2), .D7(D7), .D3(D3), .D8(D8), .D4(D4), .D9(D9));
endmodule

module \斐波那契_Fibonacci_数列计算器验证电路  (
  input  [5:0] in_1
);

  wire button_1_out, button_2_out;
  wire [3:0] \斐波那契_fibonacci_数列计算器_1_d0 , \斐波那契_fibonacci_数列计算器_1_d1 , \斐波那契_fibonacci_数列计算器_1_d2 ,
       \斐波那契_fibonacci_数列计算器_1_d3 , \斐波那契_fibonacci_数列计算器_1_d4 , \斐波那契_fibonacci_数列计算器_1_d5 ,
       \斐波那契_fibonacci_数列计算器_1_d6 , \斐波那契_fibonacci_数列计算器_1_d7 , \斐波那契_fibonacci_数列计算器_1_d8 ,
       \斐波那契_fibonacci_数列计算器_1_d9 ;

  Button button_1 (.out(button_1_out));
  Button button_2 (.out(button_2_out));
  Hex_Digit_Display hex_digit_display_1 (.value(\斐波那契_fibonacci_数列计算器_1_d9 ));  // open: dp
  Hex_Digit_Display hex_digit_display_2 (.value(\斐波那契_fibonacci_数列计算器_1_d8 ));  // open: dp
  Hex_Digit_Display hex_digit_display_3 (.value(\斐波那契_fibonacci_数列计算器_1_d7 ));  // open: dp
  \斐波那契_Fibonacci_数列计算器  \u_斐波那契_fibonacci_数列计算器_1  (
    .n(6'b101100), .D0(\斐波那契_fibonacci_数列计算器_1_d0 ), .D1(\斐波那契_fibonacci_数列计算器_1_d1 ),
    .D2(\斐波那契_fibonacci_数列计算器_1_d2 ), .D3(\斐波那契_fibonacci_数列计算器_1_d3 ), .D4(\斐波那契_fibonacci_数列计算器_1_d4 ),
    .D5(\斐波那契_fibonacci_数列计算器_1_d5 ), .D6(\斐波那契_fibonacci_数列计算器_1_d6 ), .D7(\斐波那契_fibonacci_数列计算器_1_d7 ),
    .D8(\斐波那契_fibonacci_数列计算器_1_d8 ), .D9(\斐波那契_fibonacci_数列计算器_1_d9 ), .clear(button_1_out),
    .clk(button_2_out));
  Hex_Digit_Display hex_digit_display_4 (.value(\斐波那契_fibonacci_数列计算器_1_d6 ));  // open: dp
  Hex_Digit_Display hex_digit_display_5 (.value(\斐波那契_fibonacci_数列计算器_1_d5 ));  // open: dp
  Hex_Digit_Display hex_digit_display_6 (.value(\斐波那契_fibonacci_数列计算器_1_d3 ));  // open: dp
  Hex_Digit_Display hex_digit_display_7 (.value(\斐波那契_fibonacci_数列计算器_1_d4 ));  // open: dp
  Hex_Digit_Display hex_digit_display_8 (.value(\斐波那契_fibonacci_数列计算器_1_d1 ));  // open: dp
  Hex_Digit_Display hex_digit_display_9 (.value(\斐波那契_fibonacci_数列计算器_1_d2 ));  // open: dp
  Hex_Digit_Display hex_digit_display_10 (.value(\斐波那契_fibonacci_数列计算器_1_d0 ));  // open: dp
endmodule

module Fibo (
  input  start,
  input  clr,
  input  clk,
  input  ni_1,
  output [31:0] Fi
);

  wire or_1_out;
  wire [31:0] multiplexer_1_out, multiplexer_2_out, multiplexer_3_out, multiplexer_4_out, multiplexer_5_out,
       multiplexer_6_out, multiplexer_7_out, multiplexer_8_out, register_1_q, register_3_q, register_4_q,
       sqrx_1_a_prime, sqrx_1_a_prime_2, sqrx_1_b_prime, sqrx_1_c_prime, sqrx_a_1_a_prime_prime,
       sqrx_a_1_b_prime_prime, sqrx_a_1_c_prime_prime, sqrx_a_1_out_8;

  Multiplexer #(.width(32)) multiplexer_1 (
    .in0({32{1'b0}}), .in1(multiplexer_5_out), .out(multiplexer_1_out), .sel(start));  // open: en
  Register #(.width(32)) register_1 (.D(multiplexer_1_out), .Q(register_1_q), .clk(or_1_out));  // open: en, clr
  or or_1 (or_1_out, clr, clk);
  Multiplexer #(.width(32)) multiplexer_2 (
    .in0(32'h1), .in1(multiplexer_6_out), .out(multiplexer_2_out), .sel(start));  // open: en
  Register #(.width(32)) register_2 (.D(multiplexer_2_out), .Q(Fi), .clk(or_1_out));  // open: en, clr
  Multiplexer #(.width(32)) multiplexer_3 (
    .in0(32'h1), .in1(multiplexer_7_out), .out(multiplexer_3_out), .sel(start));  // open: en
  Register #(.width(32)) register_3 (.D(multiplexer_3_out), .Q(register_3_q), .clk(or_1_out));  // open: en, clr
  Multiplexer #(.width(32)) multiplexer_4 (
    .in0(32'h1), .in1(multiplexer_8_out), .out(multiplexer_4_out), .sel(start));  // open: en
  Register #(.width(32)) register_4 (.D(multiplexer_4_out), .Q(register_4_q), .clk(or_1_out));  // open: en, clr
  sqrX sqrx_1 (
    .a(register_1_q), .b(Fi), .c(register_3_q), .d(register_4_q), .a_prime(sqrx_1_a_prime),
    .b_prime(sqrx_1_b_prime), .c_prime(sqrx_1_c_prime), .a_prime_2(sqrx_1_a_prime_2));
  sqrX_A sqrx_a_1 (
    .a(register_1_q), .b(Fi), .c(register_3_q), .d(register_4_q), .a_prime_prime(sqrx_a_1_a_prime_prime),
    .b_prime_prime(sqrx_a_1_b_prime_prime), .c_prime_prime(sqrx_a_1_c_prime_prime), .out_8(sqrx_a_1_out_8));
  Multiplexer #(.width(32)) multiplexer_5 (
    .in0(sqrx_1_a_prime), .in1(sqrx_a_1_a_prime_prime), .out(multiplexer_5_out), .sel(ni_1));  // open: en
  Multiplexer #(.width(32)) multiplexer_6 (
    .in0(sqrx_1_b_prime), .in1(sqrx_a_1_b_prime_prime), .out(multiplexer_6_out), .sel(ni_1));  // open: en
  Multiplexer #(.width(32)) multiplexer_7 (
    .in0(sqrx_1_c_prime), .in1(sqrx_a_1_c_prime_prime), .out(multiplexer_7_out), .sel(ni_1));  // open: en
  Multiplexer #(.width(32)) multiplexer_8 (
    .in0(sqrx_1_a_prime_2), .in1(sqrx_a_1_out_8), .out(multiplexer_8_out), .sel(ni_1));  // open: en
endmodule

module Controller (
  input  [5:0] n,
  input  clear,
  input  clock,
  output ni_1,
  output start,
  output clock_2,
  output clear_2
);

  wire _1_out, _2_out, _3_out, _4_out, _5_out, _7_out, buffer_1_out, buffer_2_out, buffer_3_out,
       buffer_4_out, buffer_5_out, buffer_6_out, buffer_7_out, buffer_8_out, buffer_9_out, buffer_10_out,
       buffer_12_out, comparator_1_eq, comparator_1_lt, d_ff_1_q;
  wire [7:0] counter_1_q;

  or _2 (_2_out, comparator_1_eq, comparator_1_lt);
  Counter #(.max('h7), .ongoal("stay")) counter_1 (
    .count(1'b1), .Q(counter_1_q), .clk(clock), .clr(clear));  // open: load, D, carry
  and _1 (_1_out, clock, comparator_1_lt);
  or _3 (_3_out, clear, _1_out);
  buf buffer_1 (buffer_1_out, clear);
  buf buffer_2 (buffer_2_out, buffer_1_out);
  Comparator comparator_1 (.a(counter_1_q), .b(8'h5), .eq(comparator_1_eq), .lt(comparator_1_lt));  // open: gt
  buf buffer_3 (buffer_3_out, buffer_4_out);
  buf buffer_4 (buffer_4_out, buffer_2_out);
  and _4 (_4_out, _2_out, clock);
  buf buffer_5 (buffer_5_out, buffer_3_out);
  buf buffer_6 (buffer_6_out, buffer_5_out);
  or _5 (_5_out, ni_1, d_ff_1_q);
  buf buffer_7 (buffer_7_out, buffer_6_out);
  buf buffer_8 (buffer_8_out, buffer_7_out);
  Shift_Register #(.length(6)) shift_register_1 (
    .clk(_3_out), .out(ni_1), .load(clear), .d0(n[0]), .d1(n[1]), .d2(n[2]), .d3(n[3]), .d4(n[4]), .d5(n[5]));  // open: shift, in, clr, q0, q1, q2, q3, q4, q5
  buf buffer_9 (buffer_9_out, buffer_10_out);
  buf buffer_10 (buffer_10_out, buffer_8_out);
  and _6 (clock_2, _4_out, d_ff_1_q);
  buf buffer_11 (clear_2, buffer_12_out);
  buf buffer_12 (buffer_12_out, buffer_9_out);
  or _7 (_7_out, d_ff_1_q, ni_1);
  D_Flip_Flop d_ff_1 (.clk(_3_out), .D(_5_out), .Q(d_ff_1_q), .reset(clear));  // open: Qn, preset, en
  D_Flip_Flop d_ff_2 (.clk(_3_out), .D(_7_out), .Q(start), .reset(clear));  // open: Qn, preset, en
endmodule
